// Digital circuit ACC.dig as structural Verilog
module ACC (
  input  [7:0] i,
  input  s,
  input  e,
  output [7:0] o
);

  wire [7:0] registro_always_e_1_out;

  registro_always_e registro_always_e_1 (.in(i), .s(s), .out(registro_always_e_1_out));
  enabler_high_impedance enabler_high_impedance_1 (.o(o), .i(registro_always_e_1_out), .e(e));
endmodule
