// Digital circuit NOTer.dig as structural Verilog
module NOTer (
  input  [7:0] i,
  input  e,
  output [7:0] o
);

  wire [7:0] enabler_and_1_o, not_nand_1_o;

  enabler_and enabler_and_1 (.o(enabler_and_1_o), .i(i), .e(e));
  not_nand not_nand_1 (.i(enabler_and_1_o[0]), .o(not_nand_1_o[0]));
  not_nand not_nand_2 (.i(enabler_and_1_o[1]), .o(not_nand_1_o[1]));
  not_nand not_nand_3 (.i(enabler_and_1_o[2]), .o(not_nand_1_o[2]));
  not_nand not_nand_4 (.i(enabler_and_1_o[3]), .o(not_nand_1_o[3]));
  not_nand not_nand_5 (.i(enabler_and_1_o[4]), .o(not_nand_1_o[4]));
  not_nand not_nand_6 (.i(enabler_and_1_o[5]), .o(not_nand_1_o[5]));
  not_nand not_nand_7 (.i(enabler_and_1_o[6]), .o(not_nand_1_o[6]));
  not_nand not_nand_8 (.i(enabler_and_1_o[7]), .o(not_nand_1_o[7]));
  enabler_high_impedance enabler_high_impedance_1 (.o(o), .i(not_nand_1_o), .e(e));
endmodule
