// Digital circuit Temporary_register.dig as structural Verilog
module Temporary_register (
  input  [7:0] i,
  input  s,
  output [7:0] o
);

  registro_always_e registro_always_e_1 (.in(i), .s(s), .out(o));
endmodule
