// Digital circuit XORer.dig as structural Verilog
module XORer (
  input  [7:0] i,
  input  e,
  input  [7:0] i2,
  output [7:0] o
);

  wire [7:0] enabler_and_1_o, enabler_and_2_o, xor_nand_2_o;

  enabler_and enabler_and_1 (.o(enabler_and_1_o), .i(i), .e(e));
  enabler_and enabler_and_2 (.o(enabler_and_2_o), .i(i2), .e(e));
  xor_nand xor_nand_1 (.i1(enabler_and_2_o[0]), .i2(enabler_and_1_o[0]), .o(xor_nand_2_o[0]));
  xor_nand xor_nand_2 (.i1(enabler_and_2_o[1]), .i2(enabler_and_1_o[1]), .o(xor_nand_2_o[1]));
  xor_nand xor_nand_3 (.i1(enabler_and_2_o[2]), .i2(enabler_and_1_o[2]), .o(xor_nand_2_o[2]));
  xor_nand xor_nand_4 (.i1(enabler_and_2_o[3]), .i2(enabler_and_1_o[3]), .o(xor_nand_2_o[3]));
  xor_nand xor_nand_5 (.i1(enabler_and_2_o[4]), .i2(enabler_and_1_o[4]), .o(xor_nand_2_o[4]));
  xor_nand xor_nand_6 (.i1(enabler_and_2_o[5]), .i2(enabler_and_1_o[5]), .o(xor_nand_2_o[5]));
  xor_nand xor_nand_7 (.i1(enabler_and_2_o[6]), .i2(enabler_and_1_o[6]), .o(xor_nand_2_o[6]));
  xor_nand xor_nand_8 (.i1(enabler_and_2_o[7]), .i2(enabler_and_1_o[7]), .o(xor_nand_2_o[7]));
  enabler_high_impedance enabler_high_impedance_1 (.o(o), .i(xor_nand_2_o), .e(e));
endmodule
