// Digital circuit decoder_4x16.dig as structural Verilog
module decoder_4x16 (
  input  [3:0] sel,
  output _0000,
  output _0001,
  output _0010,
  output _0011,
  output _0100,
  output _0101,
  output _0110,
  output _0111,
  output _1000,
  output _1001,
  output _1010,
  output _1011,
  output _1100,
  output _1101,
  output _1110,
  output _1111
);

  wire and_nand_1_o, and_nand_2_o, and_nand_3_o, and_nand_4_o, and_nand_5_o, and_nand_6_o, and_nand_7_o,
       and_nand_8_o, and_nand_9_o, and_nand_10_o, and_nand_11_o, and_nand_12_o, and_nand_13_o, and_nand_14_o,
       and_nand_15_o, and_nand_16_o, and_nand_17_o, and_nand_18_o, and_nand_19_o, and_nand_20_o,
       and_nand_21_o, and_nand_22_o, and_nand_23_o, and_nand_24_o, and_nand_25_o, and_nand_26_o,
       and_nand_27_o, and_nand_28_o, and_nand_29_o, and_nand_30_o, and_nand_31_o, and_nand_32_o,
       not_nand_1_o, not_nand_2_o, not_nand_3_o, not_nand_4_o;

  not_nand not_nand_1 (.i(sel[3]), .o(not_nand_1_o));
  not_nand not_nand_2 (.i(sel[1]), .o(not_nand_2_o));
  not_nand not_nand_3 (.i(sel[2]), .o(not_nand_3_o));
  not_nand not_nand_4 (.i(sel[0]), .o(not_nand_4_o));
  and_nand and_nand_1 (.i1(sel[0]), .i2(sel[1]), .o(and_nand_1_o));
  and_nand and_nand_2 (.i1(not_nand_4_o), .i2(sel[1]), .o(and_nand_2_o));
  and_nand and_nand_3 (.i1(sel[0]), .i2(not_nand_2_o), .o(and_nand_3_o));
  and_nand and_nand_4 (.i1(not_nand_4_o), .i2(not_nand_2_o), .o(and_nand_4_o));
  and_nand and_nand_5 (.i1(sel[0]), .i2(sel[1]), .o(and_nand_5_o));
  and_nand and_nand_6 (.i1(not_nand_4_o), .i2(sel[1]), .o(and_nand_6_o));
  and_nand and_nand_7 (.i1(sel[0]), .i2(not_nand_2_o), .o(and_nand_7_o));
  and_nand and_nand_8 (.i1(not_nand_4_o), .i2(not_nand_2_o), .o(and_nand_8_o));
  and_nand and_nand_9 (.i1(sel[0]), .i2(sel[1]), .o(and_nand_9_o));
  and_nand and_nand_10 (.i1(not_nand_4_o), .i2(sel[1]), .o(and_nand_10_o));
  and_nand and_nand_11 (.i1(sel[0]), .i2(not_nand_2_o), .o(and_nand_11_o));
  and_nand and_nand_12 (.i1(not_nand_4_o), .i2(not_nand_2_o), .o(and_nand_12_o));
  and_nand and_nand_13 (.i1(sel[0]), .i2(sel[1]), .o(and_nand_13_o));
  and_nand and_nand_14 (.i1(not_nand_4_o), .i2(sel[1]), .o(and_nand_14_o));
  and_nand and_nand_15 (.i1(sel[0]), .i2(not_nand_2_o), .o(and_nand_15_o));
  and_nand and_nand_16 (.i1(not_nand_4_o), .i2(not_nand_2_o), .o(and_nand_16_o));
  and_nand and_nand_17 (.i1(and_nand_1_o), .i2(sel[2]), .o(and_nand_17_o));
  and_nand and_nand_18 (.i1(and_nand_2_o), .i2(sel[2]), .o(and_nand_18_o));
  and_nand and_nand_19 (.i1(and_nand_3_o), .i2(sel[2]), .o(and_nand_19_o));
  and_nand and_nand_20 (.i1(and_nand_4_o), .i2(sel[2]), .o(and_nand_20_o));
  and_nand and_nand_21 (.i1(and_nand_5_o), .i2(not_nand_3_o), .o(and_nand_21_o));
  and_nand and_nand_22 (.i1(and_nand_6_o), .i2(not_nand_3_o), .o(and_nand_22_o));
  and_nand and_nand_23 (.i1(and_nand_7_o), .i2(not_nand_3_o), .o(and_nand_23_o));
  and_nand and_nand_24 (.i1(and_nand_8_o), .i2(not_nand_3_o), .o(and_nand_24_o));
  and_nand and_nand_25 (.i1(and_nand_9_o), .i2(sel[2]), .o(and_nand_25_o));
  and_nand and_nand_26 (.i1(and_nand_10_o), .i2(sel[2]), .o(and_nand_26_o));
  and_nand and_nand_27 (.i1(and_nand_11_o), .i2(sel[2]), .o(and_nand_27_o));
  and_nand and_nand_28 (.i1(and_nand_12_o), .i2(sel[2]), .o(and_nand_28_o));
  and_nand and_nand_29 (.i1(and_nand_13_o), .i2(not_nand_3_o), .o(and_nand_29_o));
  and_nand and_nand_30 (.i1(and_nand_14_o), .i2(not_nand_3_o), .o(and_nand_30_o));
  and_nand and_nand_31 (.i1(and_nand_15_o), .i2(not_nand_3_o), .o(and_nand_31_o));
  and_nand and_nand_32 (.i1(and_nand_16_o), .i2(not_nand_3_o), .o(and_nand_32_o));
  and_nand and_nand_33 (.i1(and_nand_17_o), .i2(sel[3]), .o(_1111));
  and_nand and_nand_34 (.i1(and_nand_18_o), .i2(sel[3]), .o(_1110));
  and_nand and_nand_35 (.i1(and_nand_19_o), .i2(sel[3]), .o(_1101));
  and_nand and_nand_36 (.i1(and_nand_20_o), .i2(sel[3]), .o(_1100));
  and_nand and_nand_37 (.i1(and_nand_21_o), .i2(sel[3]), .o(_1011));
  and_nand and_nand_38 (.i1(and_nand_22_o), .i2(sel[3]), .o(_1010));
  and_nand and_nand_39 (.i1(and_nand_23_o), .i2(sel[3]), .o(_1001));
  and_nand and_nand_40 (.i1(and_nand_24_o), .i2(sel[3]), .o(_1000));
  and_nand and_nand_41 (.i1(and_nand_25_o), .i2(not_nand_1_o), .o(_0111));
  and_nand and_nand_42 (.i1(and_nand_26_o), .i2(not_nand_1_o), .o(_0110));
  and_nand and_nand_43 (.i1(and_nand_27_o), .i2(not_nand_1_o), .o(_0101));
  and_nand and_nand_44 (.i1(and_nand_28_o), .i2(not_nand_1_o), .o(_0100));
  and_nand and_nand_45 (.i1(and_nand_29_o), .i2(not_nand_1_o), .o(_0011));
  and_nand and_nand_46 (.i1(and_nand_30_o), .i2(not_nand_1_o), .o(_0010));
  and_nand and_nand_47 (.i1(and_nand_31_o), .i2(not_nand_1_o), .o(_0001));
  and_nand and_nand_48 (.i1(and_nand_32_o), .i2(not_nand_1_o), .o(_0000));
endmodule
