// Digital circuit enabler_and.dig as structural Verilog
module enabler_and (
  input  [7:0] i,
  input  e,
  output [7:0] o
);

  and_nand and_nand_1 (.i1(i[0]), .i2(e), .o(o[0]));
  and_nand and_nand_2 (.i1(i[1]), .i2(e), .o(o[1]));
  and_nand and_nand_3 (.i1(i[2]), .i2(e), .o(o[2]));
  and_nand and_nand_4 (.i1(i[3]), .i2(e), .o(o[3]));
  and_nand and_nand_5 (.i1(i[4]), .i2(e), .o(o[4]));
  and_nand and_nand_6 (.i1(i[5]), .i2(e), .o(o[5]));
  and_nand and_nand_7 (.i1(i[6]), .i2(e), .o(o[6]));
  and_nand and_nand_8 (.i1(i[7]), .i2(e), .o(o[7]));
endmodule
