// Digital circuit mem_1bit.dig as structural Verilog
module mem_1bit (
  input  i,
  input  s,
  output o
);

  wire nand_tr_1_o, nand_tr_2_o, nand_tr_4_o;

  nand_tr nand_tr_1 (.i1(i), .i2(s), .o(nand_tr_1_o));
  nand_tr nand_tr_2 (.i1(nand_tr_1_o), .i2(s), .o(nand_tr_2_o));
  nand_tr nand_tr_3 (.i1(nand_tr_1_o), .i2(nand_tr_4_o), .o(o));
  nand_tr nand_tr_4 (.i1(o), .i2(nand_tr_2_o), .o(nand_tr_4_o));
  PullDown pulldown_1 (.out(o));

  // Notes on the sheet:
  //   o: output
  //   i: input data
  //   s: set
endmodule
