// Digital circuit mem_1byte.dig as structural Verilog
module mem_1byte (
  input  i1,
  input  i2,
  input  i3,
  input  i4,
  input  i5,
  input  i6,
  input  i7,
  input  i8,
  input  s,
  input  e,
  output o1,
  output o2,
  output o3,
  output o4,
  output o5,
  output o6,
  output o7,
  output o8
);

  wire mem_1bit_1_o, mem_1bit_2_o, mem_1bit_3_o, mem_1bit_4_o, mem_1bit_5_o, mem_1bit_6_o, mem_1bit_7_o,
       mem_1bit_8_o;

  mem_1bit mem_1bit_1 (.i(i1), .s(s), .o(mem_1bit_1_o));
  mem_1bit mem_1bit_2 (.i(i2), .s(s), .o(mem_1bit_2_o));
  mem_1bit mem_1bit_3 (.i(i3), .s(s), .o(mem_1bit_3_o));
  mem_1bit mem_1bit_4 (.i(i4), .s(s), .o(mem_1bit_4_o));
  mem_1bit mem_1bit_5 (.i(i5), .s(s), .o(mem_1bit_5_o));
  mem_1bit mem_1bit_6 (.i(i6), .s(s), .o(mem_1bit_6_o));
  mem_1bit mem_1bit_7 (.i(i7), .s(s), .o(mem_1bit_7_o));
  mem_1bit mem_1bit_8 (.i(i8), .s(s), .o(mem_1bit_8_o));
  buffer_high_impedance buffer_high_impedance_1 (.i(mem_1bit_1_o), .e(e), .o(o1));
  buffer_high_impedance buffer_high_impedance_2 (.i(mem_1bit_2_o), .e(e), .o(o2));
  buffer_high_impedance buffer_high_impedance_3 (.i(mem_1bit_3_o), .e(e), .o(o3));
  buffer_high_impedance buffer_high_impedance_4 (.i(mem_1bit_4_o), .e(e), .o(o4));
  buffer_high_impedance buffer_high_impedance_5 (.i(mem_1bit_5_o), .e(e), .o(o5));
  buffer_high_impedance buffer_high_impedance_6 (.i(mem_1bit_6_o), .e(e), .o(o6));
  buffer_high_impedance buffer_high_impedance_7 (.i(mem_1bit_7_o), .e(e), .o(o7));
  buffer_high_impedance buffer_high_impedance_8 (.i(mem_1bit_8_o), .e(e), .o(o8));
endmodule
