// Digital circuit or_nand.dig as structural Verilog
module or_nand (
  input  i1,
  input  i2,
  output o
);

  wire not_nand_1_o, not_nand_2_o;

  not_nand not_nand_1 (.i(i1), .o(not_nand_1_o));
  not_nand not_nand_2 (.i(i2), .o(not_nand_2_o));
  nand_tr nand_tr_1 (.i1(not_nand_1_o), .i2(not_nand_2_o), .o(o));
endmodule
