// Digital circuit registro.dig as structural Verilog
module registro (
  input  [7:0] in,
  input  s,
  input  e,
  output [7:0] out
);

  wire [7:0] registro_always_e_1_out;

  registro_always_e registro_always_e_1 (.in(in), .s(s), .out(registro_always_e_1_out));
  enabler_high_impedance enabler_high_impedance_1 (.o(out), .i(registro_always_e_1_out), .e(e));
endmodule
