// Digital circuit shifter_right.dig as structural Verilog
module shifter_right (
  input  [7:0] i,
  input  e,
  input  si,
  output [7:0] o,
  output so
);

  enabler_high_impedance enabler_high_impedance_1 (.o({o[6:0], so}), .i(i), .e(e));
  buffer_high_impedance buffer_high_impedance_1 (.i(si), .e(e), .o(o[7]));

  // Notes on the sheet:
  //   si: shift in
  //   so: shift out
endmodule
