// Digital circuit Register.dig as structural Verilog
module Register (
  input  [7:0] i,
  input  e,
  input  s,
  input  x,
  input  y,
  input  in_6
);

  wire nfet_1_s, nfet_3_s, nfet_5_s, nfet_7_s, nfet_9_s, nfet_11_s, nfet_13_s, nfet_15_s, nfet_17_s,
       nfet_19_s, nfet_21_s, nfet_23_s, nfet_25_s, nfet_27_s, nfet_29_s, nfet_31_s, nfet_33_s, nfet_35_s,
       nfet_37_s, nfet_39_s, nfet_41_s, nfet_43_s, nfet_45_s, nfet_47_s, nfet_49_s, nfet_51_s, nfet_53_s,
       nfet_55_s, nfet_57_s, nfet_59_s, nfet_61_s, nfet_63_s, nfet_65_s, nfet_67_s, nfet_69_s, nfet_71_s,
       nfet_73_s, nfet_75_s, nfet_77_s, nfet_79_s, nfet_81_s, nfet_83_s, nfet_85_s, nfet_87_s, nfet_89_s,
       nfet_91_s, nfet_93_s, nfet_95_s, nfet_97_s, nfet_99_s, nfet_101_s, nfet_103_s, nfet_105_s, nfet_107_s,
       nfet_109_s, nfet_111_s, nfet_113_s, nfet_115_s, nfet_117_s, nfet_119_s, nfet_121_s, nfet_123_s,
       nfet_125_s, nfet_127_s, nfet_129_s, nfet_131_s, nfet_133_s, nfet_135_s, nfet_137_s, nfet_139_s,
       nfet_141_s, nfet_143_s, nfet_145_s, nfet_147_s, nfet_149_s, nfet_151_s, nfet_153_s, nfet_155_s,
       pfet_1_d, pfet_1_s, pfet_2_d, pfet_2_s, pfet_3_d, pfet_3_s, pfet_4_d, pfet_4_s, pfet_5_d, pfet_5_s,
       pfet_6_d, pfet_6_s, pfet_7_d, pfet_7_s, pfet_8_d, pfet_8_s, pfet_17_d, pfet_17_s, pfet_18_d,
       pfet_18_s, pfet_19_d, pfet_19_s, pfet_20_d, pfet_20_s, pfet_21_d, pfet_21_s, pfet_22_d, pfet_22_s,
       pfet_23_d, pfet_23_s, pfet_24_d, pfet_24_s, pfet_33_d, pfet_33_s, pfet_34_d, pfet_34_s, pfet_35_d,
       pfet_35_s, pfet_36_d, pfet_36_s, pfet_37_d, pfet_37_s, pfet_38_d, pfet_38_s, pfet_39_d, pfet_39_s,
       pfet_40_d, pfet_40_s, pfet_49_d, pfet_49_s, pfet_50_d, pfet_50_s, pfet_51_d, pfet_51_s, pfet_52_d,
       pfet_52_s, pfet_53_d, pfet_53_s, pfet_54_d, pfet_54_s, pfet_55_d, pfet_55_s, pfet_56_d, pfet_56_s,
       pfet_65_d, pfet_65_s, pfet_66_d, pfet_66_s, pfet_67_d, pfet_67_s, pfet_71_d, pfet_71_s, pfet_72_d,
       pfet_72_s, pfet_73_d, pfet_73_s, pfet_77_d, pfet_77_s, pfet_78_d, pfet_78_s, pfet_79_d, pfet_79_s,
       pfet_80_d, pfet_80_s, pfet_81_d, pfet_81_s, pfet_82_d, pfet_82_s, pfet_83_d, pfet_83_s, pfet_84_d,
       pfet_84_s, pfet_93_d, pfet_93_s, pfet_94_d, pfet_94_s, pfet_95_d, pfet_95_s, pfet_96_d, pfet_96_s,
       pfet_97_d, pfet_97_s, pfet_98_d, pfet_98_s, pfet_99_d, pfet_99_s, pfet_100_d, pfet_100_s, pfet_109_d,
       pfet_109_s, pfet_110_d, pfet_110_s, pfet_111_d, pfet_111_s, pfet_112_d, pfet_112_s, pfet_125_d,
       pfet_125_s, pfet_126_d, pfet_126_s, pfet_127_d, pfet_127_s, pfet_128_d, pfet_128_s, pfet_129_d,
       pfet_129_s, pfet_130_d, pfet_130_s, pfet_131_d, pfet_131_s, pfet_132_d, pfet_132_s, pfet_141_d,
       pfet_141_s, pfet_142_d, pfet_142_s, pfet_143_d, pfet_143_s, pfet_144_d, pfet_144_s, pfet_145_d,
       pfet_145_s, pfet_146_d, pfet_146_s, pfet_147_d, pfet_147_s, pfet_148_d, pfet_148_s, pfet_157_d,
       pfet_157_s, pfet_158_d, pfet_158_s, pfet_159_d, pfet_159_s, pfet_160_d, pfet_160_s;
  wire [3:0] driver_1_out, driver_1_out_2;

  assign {driver_1_out_2, driver_1_out} = in_6 ? i : 8'bz;  // Driver driver_1
  PFET #(.unidirectional("true")) pfet_1 (.G(driver_1_out_2[0]), .S(pfet_1_s), .D(pfet_1_d));
  PFET #(.unidirectional("true")) pfet_2 (.G(pfet_1_d), .S(pfet_2_s), .D(pfet_2_d));
  PFET #(.unidirectional("true")) pfet_3 (.G(driver_1_out_2[1]), .S(pfet_3_s), .D(pfet_3_d));
  PFET #(.unidirectional("true")) pfet_4 (.G(pfet_3_d), .S(pfet_4_s), .D(pfet_4_d));
  PFET #(.unidirectional("true")) pfet_5 (.G(driver_1_out_2[2]), .S(pfet_5_s), .D(pfet_5_d));
  PFET #(.unidirectional("true")) pfet_6 (.G(pfet_5_d), .S(pfet_6_s), .D(pfet_6_d));
  PFET #(.unidirectional("true")) pfet_7 (.G(driver_1_out_2[3]), .S(pfet_7_s), .D(pfet_7_d));
  PFET #(.unidirectional("true")) pfet_8 (.G(pfet_7_d), .S(pfet_8_s), .D(pfet_8_d));
  PullUp pullup_1 (.out(pfet_1_s));
  PFET #(.unidirectional("true")) pfet_9 (.G(pfet_72_d), .S(pfet_1_s), .D(pfet_1_d));
  NFET #(.unidirectional("true")) nfet_1 (.G(driver_1_out_2[0]), .D(pfet_1_d), .S(nfet_1_s));
  NFET #(.unidirectional("true")) nfet_2 (.G(pfet_72_d), .D(nfet_1_s), .S(1'b0));
  PullUp pullup_2 (.out(pfet_2_s));
  PFET #(.unidirectional("true")) pfet_10 (.G(pfet_72_d), .S(pfet_2_s), .D(pfet_2_d));
  NFET #(.unidirectional("true")) nfet_3 (.G(pfet_1_d), .D(pfet_2_d), .S(nfet_3_s));
  NFET #(.unidirectional("true")) nfet_4 (.G(pfet_72_d), .D(nfet_3_s), .S(1'b0));
  PullUp pullup_3 (.out(pfet_3_s));
  PFET #(.unidirectional("true")) pfet_11 (.G(pfet_72_d), .S(pfet_3_s), .D(pfet_3_d));
  NFET #(.unidirectional("true")) nfet_5 (.G(driver_1_out_2[1]), .D(pfet_3_d), .S(nfet_5_s));
  NFET #(.unidirectional("true")) nfet_6 (.G(pfet_72_d), .D(nfet_5_s), .S(1'b0));
  PullUp pullup_4 (.out(pfet_4_s));
  PFET #(.unidirectional("true")) pfet_12 (.G(pfet_72_d), .S(pfet_4_s), .D(pfet_4_d));
  NFET #(.unidirectional("true")) nfet_7 (.G(pfet_3_d), .D(pfet_4_d), .S(nfet_7_s));
  NFET #(.unidirectional("true")) nfet_8 (.G(pfet_72_d), .D(nfet_7_s), .S(1'b0));
  PullUp pullup_5 (.out(pfet_5_s));
  PFET #(.unidirectional("true")) pfet_13 (.G(pfet_72_d), .S(pfet_5_s), .D(pfet_5_d));
  NFET #(.unidirectional("true")) nfet_9 (.G(driver_1_out_2[2]), .D(pfet_5_d), .S(nfet_9_s));
  NFET #(.unidirectional("true")) nfet_10 (.G(pfet_72_d), .D(nfet_9_s), .S(1'b0));
  PullUp pullup_6 (.out(pfet_6_s));
  PFET #(.unidirectional("true")) pfet_14 (.G(pfet_72_d), .S(pfet_6_s), .D(pfet_6_d));
  NFET #(.unidirectional("true")) nfet_11 (.G(pfet_5_d), .D(pfet_6_d), .S(nfet_11_s));
  NFET #(.unidirectional("true")) nfet_12 (.G(pfet_72_d), .D(nfet_11_s), .S(1'b0));
  PullUp pullup_7 (.out(pfet_7_s));
  PFET #(.unidirectional("true")) pfet_15 (.G(pfet_72_d), .S(pfet_7_s), .D(pfet_7_d));
  NFET #(.unidirectional("true")) nfet_13 (.G(driver_1_out_2[3]), .D(pfet_7_d), .S(nfet_13_s));
  NFET #(.unidirectional("true")) nfet_14 (.G(pfet_72_d), .D(nfet_13_s), .S(1'b0));
  PullUp pullup_8 (.out(pfet_8_s));
  PFET #(.unidirectional("true")) pfet_16 (.G(pfet_72_d), .S(pfet_8_s), .D(pfet_8_d));
  NFET #(.unidirectional("true")) nfet_15 (.G(pfet_7_d), .D(pfet_8_d), .S(nfet_15_s));
  NFET #(.unidirectional("true")) nfet_16 (.G(pfet_72_d), .D(nfet_15_s), .S(1'b0));
  PFET #(.unidirectional("true")) pfet_17 (.G(pfet_1_d), .S(pfet_17_s), .D(pfet_17_d));
  PFET #(.unidirectional("true")) pfet_18 (.G(pfet_17_d), .S(pfet_18_s), .D(pfet_18_d));
  PFET #(.unidirectional("true")) pfet_19 (.G(pfet_3_d), .S(pfet_19_s), .D(pfet_19_d));
  PFET #(.unidirectional("true")) pfet_20 (.G(pfet_19_d), .S(pfet_20_s), .D(pfet_20_d));
  PFET #(.unidirectional("true")) pfet_21 (.G(pfet_5_d), .S(pfet_21_s), .D(pfet_21_d));
  PFET #(.unidirectional("true")) pfet_22 (.G(pfet_21_d), .S(pfet_22_s), .D(pfet_22_d));
  PFET #(.unidirectional("true")) pfet_23 (.G(pfet_7_d), .S(pfet_23_s), .D(pfet_23_d));
  PFET #(.unidirectional("true")) pfet_24 (.G(pfet_23_d), .S(pfet_24_s), .D(pfet_24_d));
  PullUp pullup_9 (.out(pfet_17_s));
  PFET #(.unidirectional("true")) pfet_25 (.G(pfet_18_d), .S(pfet_17_s), .D(pfet_17_d));
  NFET #(.unidirectional("true")) nfet_17 (.G(pfet_1_d), .D(pfet_17_d), .S(nfet_17_s));
  NFET #(.unidirectional("true")) nfet_18 (.G(pfet_18_d), .D(nfet_17_s), .S(1'b0));
  PullUp pullup_10 (.out(pfet_18_s));
  PFET #(.unidirectional("true")) pfet_26 (.G(pfet_2_d), .S(pfet_18_s), .D(pfet_18_d));
  NFET #(.unidirectional("true")) nfet_19 (.G(pfet_17_d), .D(pfet_18_d), .S(nfet_19_s));
  NFET #(.unidirectional("true")) nfet_20 (.G(pfet_2_d), .D(nfet_19_s), .S(1'b0));
  PullUp pullup_11 (.out(pfet_19_s));
  PFET #(.unidirectional("true")) pfet_27 (.G(pfet_20_d), .S(pfet_19_s), .D(pfet_19_d));
  NFET #(.unidirectional("true")) nfet_21 (.G(pfet_3_d), .D(pfet_19_d), .S(nfet_21_s));
  NFET #(.unidirectional("true")) nfet_22 (.G(pfet_20_d), .D(nfet_21_s), .S(1'b0));
  PullUp pullup_12 (.out(pfet_20_s));
  PFET #(.unidirectional("true")) pfet_28 (.G(pfet_4_d), .S(pfet_20_s), .D(pfet_20_d));
  NFET #(.unidirectional("true")) nfet_23 (.G(pfet_19_d), .D(pfet_20_d), .S(nfet_23_s));
  NFET #(.unidirectional("true")) nfet_24 (.G(pfet_4_d), .D(nfet_23_s), .S(1'b0));
  PullUp pullup_13 (.out(pfet_21_s));
  PFET #(.unidirectional("true")) pfet_29 (.G(pfet_22_d), .S(pfet_21_s), .D(pfet_21_d));
  NFET #(.unidirectional("true")) nfet_25 (.G(pfet_5_d), .D(pfet_21_d), .S(nfet_25_s));
  NFET #(.unidirectional("true")) nfet_26 (.G(pfet_22_d), .D(nfet_25_s), .S(1'b0));
  PullUp pullup_14 (.out(pfet_22_s));
  PFET #(.unidirectional("true")) pfet_30 (.G(pfet_6_d), .S(pfet_22_s), .D(pfet_22_d));
  NFET #(.unidirectional("true")) nfet_27 (.G(pfet_21_d), .D(pfet_22_d), .S(nfet_27_s));
  NFET #(.unidirectional("true")) nfet_28 (.G(pfet_6_d), .D(nfet_27_s), .S(1'b0));
  PullUp pullup_15 (.out(pfet_23_s));
  PFET #(.unidirectional("true")) pfet_31 (.G(pfet_24_d), .S(pfet_23_s), .D(pfet_23_d));
  NFET #(.unidirectional("true")) nfet_29 (.G(pfet_7_d), .D(pfet_23_d), .S(nfet_29_s));
  NFET #(.unidirectional("true")) nfet_30 (.G(pfet_24_d), .D(nfet_29_s), .S(1'b0));
  PullUp pullup_16 (.out(pfet_24_s));
  PFET #(.unidirectional("true")) pfet_32 (.G(pfet_8_d), .S(pfet_24_s), .D(pfet_24_d));
  NFET #(.unidirectional("true")) nfet_31 (.G(pfet_23_d), .D(pfet_24_d), .S(nfet_31_s));
  NFET #(.unidirectional("true")) nfet_32 (.G(pfet_8_d), .D(nfet_31_s), .S(1'b0));
  Seven_Seg_Hex seven_seg_hex_1 (.d(driver_1_out_2), .dp(1'b0));
  PullDown pulldown_1 (.out(pfet_17_d));
  PullDown pulldown_2 (.out(pfet_19_d));
  PullDown pulldown_3 (.out(pfet_21_d));
  PullDown pulldown_4 (.out(pfet_23_d));
  Seven_Seg_Hex seven_seg_hex_2 (.d(driver_1_out), .dp(1'b0));
  PFET #(.unidirectional("true")) pfet_33 (.G(driver_1_out[0]), .S(pfet_33_s), .D(pfet_33_d));
  PFET #(.unidirectional("true")) pfet_34 (.G(pfet_33_d), .S(pfet_34_s), .D(pfet_34_d));
  PFET #(.unidirectional("true")) pfet_35 (.G(driver_1_out[1]), .S(pfet_35_s), .D(pfet_35_d));
  PFET #(.unidirectional("true")) pfet_36 (.G(pfet_35_d), .S(pfet_36_s), .D(pfet_36_d));
  PFET #(.unidirectional("true")) pfet_37 (.G(driver_1_out[2]), .S(pfet_37_s), .D(pfet_37_d));
  PFET #(.unidirectional("true")) pfet_38 (.G(pfet_37_d), .S(pfet_38_s), .D(pfet_38_d));
  PFET #(.unidirectional("true")) pfet_39 (.G(driver_1_out[3]), .S(pfet_39_s), .D(pfet_39_d));
  PFET #(.unidirectional("true")) pfet_40 (.G(pfet_39_d), .S(pfet_40_s), .D(pfet_40_d));
  PullUp pullup_17 (.out(pfet_33_s));
  PFET #(.unidirectional("true")) pfet_41 (.G(pfet_72_d), .S(pfet_33_s), .D(pfet_33_d));
  NFET #(.unidirectional("true")) nfet_33 (.G(driver_1_out[0]), .D(pfet_33_d), .S(nfet_33_s));
  NFET #(.unidirectional("true")) nfet_34 (.G(pfet_72_d), .D(nfet_33_s), .S(1'b0));
  PullUp pullup_18 (.out(pfet_34_s));
  PFET #(.unidirectional("true")) pfet_42 (.G(pfet_72_d), .S(pfet_34_s), .D(pfet_34_d));
  NFET #(.unidirectional("true")) nfet_35 (.G(pfet_33_d), .D(pfet_34_d), .S(nfet_35_s));
  NFET #(.unidirectional("true")) nfet_36 (.G(pfet_72_d), .D(nfet_35_s), .S(1'b0));
  PullUp pullup_19 (.out(pfet_35_s));
  PFET #(.unidirectional("true")) pfet_43 (.G(pfet_72_d), .S(pfet_35_s), .D(pfet_35_d));
  NFET #(.unidirectional("true")) nfet_37 (.G(driver_1_out[1]), .D(pfet_35_d), .S(nfet_37_s));
  NFET #(.unidirectional("true")) nfet_38 (.G(pfet_72_d), .D(nfet_37_s), .S(1'b0));
  PullUp pullup_20 (.out(pfet_36_s));
  PFET #(.unidirectional("true")) pfet_44 (.G(pfet_72_d), .S(pfet_36_s), .D(pfet_36_d));
  NFET #(.unidirectional("true")) nfet_39 (.G(pfet_35_d), .D(pfet_36_d), .S(nfet_39_s));
  NFET #(.unidirectional("true")) nfet_40 (.G(pfet_72_d), .D(nfet_39_s), .S(1'b0));
  PullUp pullup_21 (.out(pfet_37_s));
  PFET #(.unidirectional("true")) pfet_45 (.G(pfet_72_d), .S(pfet_37_s), .D(pfet_37_d));
  NFET #(.unidirectional("true")) nfet_41 (.G(driver_1_out[2]), .D(pfet_37_d), .S(nfet_41_s));
  NFET #(.unidirectional("true")) nfet_42 (.G(pfet_72_d), .D(nfet_41_s), .S(1'b0));
  PullUp pullup_22 (.out(pfet_38_s));
  PFET #(.unidirectional("true")) pfet_46 (.G(pfet_72_d), .S(pfet_38_s), .D(pfet_38_d));
  NFET #(.unidirectional("true")) nfet_43 (.G(pfet_37_d), .D(pfet_38_d), .S(nfet_43_s));
  NFET #(.unidirectional("true")) nfet_44 (.G(pfet_72_d), .D(nfet_43_s), .S(1'b0));
  PullUp pullup_23 (.out(pfet_39_s));
  PFET #(.unidirectional("true")) pfet_47 (.G(pfet_72_d), .S(pfet_39_s), .D(pfet_39_d));
  NFET #(.unidirectional("true")) nfet_45 (.G(driver_1_out[3]), .D(pfet_39_d), .S(nfet_45_s));
  NFET #(.unidirectional("true")) nfet_46 (.G(pfet_72_d), .D(nfet_45_s), .S(1'b0));
  PullUp pullup_24 (.out(pfet_40_s));
  PFET #(.unidirectional("true")) pfet_48 (.G(pfet_72_d), .S(pfet_40_s), .D(pfet_40_d));
  NFET #(.unidirectional("true")) nfet_47 (.G(pfet_39_d), .D(pfet_40_d), .S(nfet_47_s));
  NFET #(.unidirectional("true")) nfet_48 (.G(pfet_72_d), .D(nfet_47_s), .S(1'b0));
  PFET #(.unidirectional("true")) pfet_49 (.G(pfet_33_d), .S(pfet_49_s), .D(pfet_49_d));
  PFET #(.unidirectional("true")) pfet_50 (.G(pfet_49_d), .S(pfet_50_s), .D(pfet_50_d));
  PFET #(.unidirectional("true")) pfet_51 (.G(pfet_35_d), .S(pfet_51_s), .D(pfet_51_d));
  PFET #(.unidirectional("true")) pfet_52 (.G(pfet_51_d), .S(pfet_52_s), .D(pfet_52_d));
  PFET #(.unidirectional("true")) pfet_53 (.G(pfet_37_d), .S(pfet_53_s), .D(pfet_53_d));
  PFET #(.unidirectional("true")) pfet_54 (.G(pfet_53_d), .S(pfet_54_s), .D(pfet_54_d));
  PFET #(.unidirectional("true")) pfet_55 (.G(pfet_39_d), .S(pfet_55_s), .D(pfet_55_d));
  PFET #(.unidirectional("true")) pfet_56 (.G(pfet_55_d), .S(pfet_56_s), .D(pfet_56_d));
  PullUp pullup_25 (.out(pfet_49_s));
  PFET #(.unidirectional("true")) pfet_57 (.G(pfet_50_d), .S(pfet_49_s), .D(pfet_49_d));
  NFET #(.unidirectional("true")) nfet_49 (.G(pfet_33_d), .D(pfet_49_d), .S(nfet_49_s));
  NFET #(.unidirectional("true")) nfet_50 (.G(pfet_50_d), .D(nfet_49_s), .S(1'b0));
  PullUp pullup_26 (.out(pfet_50_s));
  PFET #(.unidirectional("true")) pfet_58 (.G(pfet_34_d), .S(pfet_50_s), .D(pfet_50_d));
  NFET #(.unidirectional("true")) nfet_51 (.G(pfet_49_d), .D(pfet_50_d), .S(nfet_51_s));
  NFET #(.unidirectional("true")) nfet_52 (.G(pfet_34_d), .D(nfet_51_s), .S(1'b0));
  PullUp pullup_27 (.out(pfet_51_s));
  PFET #(.unidirectional("true")) pfet_59 (.G(pfet_52_d), .S(pfet_51_s), .D(pfet_51_d));
  NFET #(.unidirectional("true")) nfet_53 (.G(pfet_35_d), .D(pfet_51_d), .S(nfet_53_s));
  NFET #(.unidirectional("true")) nfet_54 (.G(pfet_52_d), .D(nfet_53_s), .S(1'b0));
  PullUp pullup_28 (.out(pfet_52_s));
  PFET #(.unidirectional("true")) pfet_60 (.G(pfet_36_d), .S(pfet_52_s), .D(pfet_52_d));
  NFET #(.unidirectional("true")) nfet_55 (.G(pfet_51_d), .D(pfet_52_d), .S(nfet_55_s));
  NFET #(.unidirectional("true")) nfet_56 (.G(pfet_36_d), .D(nfet_55_s), .S(1'b0));
  PullUp pullup_29 (.out(pfet_53_s));
  PFET #(.unidirectional("true")) pfet_61 (.G(pfet_54_d), .S(pfet_53_s), .D(pfet_53_d));
  NFET #(.unidirectional("true")) nfet_57 (.G(pfet_37_d), .D(pfet_53_d), .S(nfet_57_s));
  NFET #(.unidirectional("true")) nfet_58 (.G(pfet_54_d), .D(nfet_57_s), .S(1'b0));
  PullUp pullup_30 (.out(pfet_54_s));
  PFET #(.unidirectional("true")) pfet_62 (.G(pfet_38_d), .S(pfet_54_s), .D(pfet_54_d));
  NFET #(.unidirectional("true")) nfet_59 (.G(pfet_53_d), .D(pfet_54_d), .S(nfet_59_s));
  NFET #(.unidirectional("true")) nfet_60 (.G(pfet_38_d), .D(nfet_59_s), .S(1'b0));
  PullUp pullup_31 (.out(pfet_55_s));
  PFET #(.unidirectional("true")) pfet_63 (.G(pfet_56_d), .S(pfet_55_s), .D(pfet_55_d));
  NFET #(.unidirectional("true")) nfet_61 (.G(pfet_39_d), .D(pfet_55_d), .S(nfet_61_s));
  NFET #(.unidirectional("true")) nfet_62 (.G(pfet_56_d), .D(nfet_61_s), .S(1'b0));
  PullUp pullup_32 (.out(pfet_56_s));
  PFET #(.unidirectional("true")) pfet_64 (.G(pfet_40_d), .S(pfet_56_s), .D(pfet_56_d));
  NFET #(.unidirectional("true")) nfet_63 (.G(pfet_55_d), .D(pfet_56_d), .S(nfet_63_s));
  NFET #(.unidirectional("true")) nfet_64 (.G(pfet_40_d), .D(nfet_63_s), .S(1'b0));
  PullDown pulldown_5 (.out(pfet_49_d));
  PullDown pulldown_6 (.out(pfet_51_d));
  PullDown pulldown_7 (.out(pfet_53_d));
  PullDown pulldown_8 (.out(pfet_55_d));
  LED led_1 (.in(pfet_23_d));
  LED led_2 (.in(pfet_55_d));
  LED led_3 (.in(pfet_72_d));
  LED led_4 (.in(pfet_21_d));
  LED led_5 (.in(pfet_53_d));
  PFET #(.unidirectional("true")) pfet_65 (.G(e), .S(pfet_65_s), .D(pfet_65_d));
  PFET #(.unidirectional("true")) pfet_66 (.G(s), .S(pfet_66_s), .D(pfet_66_d));
  PFET #(.unidirectional("true")) pfet_67 (.G(x), .S(pfet_67_s), .D(pfet_67_d));
  PullUp pullup_33 (.out(pfet_65_s));
  PFET #(.unidirectional("true")) pfet_68 (.G(pfet_73_d), .S(pfet_65_s), .D(pfet_65_d));
  NFET #(.unidirectional("true")) nfet_65 (.G(e), .D(pfet_65_d), .S(nfet_65_s));
  NFET #(.unidirectional("true")) nfet_66 (.G(pfet_73_d), .D(nfet_65_s), .S(1'b0));
  PullUp pullup_34 (.out(pfet_66_s));
  PFET #(.unidirectional("true")) pfet_69 (.G(pfet_73_d), .S(pfet_66_s), .D(pfet_66_d));
  NFET #(.unidirectional("true")) nfet_67 (.G(s), .D(pfet_66_d), .S(nfet_67_s));
  NFET #(.unidirectional("true")) nfet_68 (.G(pfet_73_d), .D(nfet_67_s), .S(1'b0));
  PullUp pullup_35 (.out(pfet_67_s));
  PFET #(.unidirectional("true")) pfet_70 (.G(y), .S(pfet_67_s), .D(pfet_67_d));
  NFET #(.unidirectional("true")) nfet_69 (.G(x), .D(pfet_67_d), .S(nfet_69_s));
  NFET #(.unidirectional("true")) nfet_70 (.G(y), .D(nfet_69_s), .S(1'b0));
  LED led_6 (.in(pfet_19_d));
  LED led_7 (.in(pfet_51_d));
  PFET #(.unidirectional("true")) pfet_71 (.G(pfet_65_d), .S(pfet_71_s), .D(pfet_71_d));
  PFET #(.unidirectional("true")) pfet_72 (.G(pfet_66_d), .S(pfet_72_s), .D(pfet_72_d));
  PFET #(.unidirectional("true")) pfet_73 (.G(pfet_67_d), .S(pfet_73_s), .D(pfet_73_d));
  LED led_8 (.in(pfet_17_d));
  LED led_9 (.in(pfet_49_d));
  PullUp pullup_36 (.out(pfet_71_s));
  PFET #(.unidirectional("true")) pfet_74 (.G(pfet_65_d), .S(pfet_71_s), .D(pfet_71_d));
  NFET #(.unidirectional("true")) nfet_71 (.G(pfet_65_d), .D(pfet_71_d), .S(nfet_71_s));
  NFET #(.unidirectional("true")) nfet_72 (.G(pfet_65_d), .D(nfet_71_s), .S(1'b0));
  PullUp pullup_37 (.out(pfet_72_s));
  PFET #(.unidirectional("true")) pfet_75 (.G(pfet_66_d), .S(pfet_72_s), .D(pfet_72_d));
  NFET #(.unidirectional("true")) nfet_73 (.G(pfet_66_d), .D(pfet_72_d), .S(nfet_73_s));
  NFET #(.unidirectional("true")) nfet_74 (.G(pfet_66_d), .D(nfet_73_s), .S(1'b0));
  PullUp pullup_38 (.out(pfet_73_s));
  PFET #(.unidirectional("true")) pfet_76 (.G(pfet_67_d), .S(pfet_73_s), .D(pfet_73_d));
  NFET #(.unidirectional("true")) nfet_75 (.G(pfet_67_d), .D(pfet_73_d), .S(nfet_75_s));
  NFET #(.unidirectional("true")) nfet_76 (.G(pfet_67_d), .D(nfet_75_s), .S(1'b0));
  LED led_10 (.in(pfet_71_d));
  PullDown pulldown_9 (.out(pfet_17_d));
  PullDown pulldown_10 (.out(pfet_19_d));
  PullDown pulldown_11 (.out(pfet_21_d));
  PullDown pulldown_12 (.out(pfet_23_d));
  PFET #(.unidirectional("true")) pfet_77 (.G(pfet_17_d), .S(pfet_77_s), .D(pfet_77_d));
  PFET #(.unidirectional("true")) pfet_78 (.G(pfet_71_d), .S(pfet_78_s), .D(pfet_78_d));
  PFET #(.unidirectional("true")) pfet_79 (.G(pfet_19_d), .S(pfet_79_s), .D(pfet_79_d));
  PFET #(.unidirectional("true")) pfet_80 (.G(pfet_71_d), .S(pfet_80_s), .D(pfet_80_d));
  PFET #(.unidirectional("true")) pfet_81 (.G(pfet_21_d), .S(pfet_81_s), .D(pfet_81_d));
  PFET #(.unidirectional("true")) pfet_82 (.G(pfet_71_d), .S(pfet_82_s), .D(pfet_82_d));
  PFET #(.unidirectional("true")) pfet_83 (.G(pfet_23_d), .S(pfet_83_s), .D(pfet_83_d));
  PFET #(.unidirectional("true")) pfet_84 (.G(pfet_71_d), .S(pfet_84_s), .D(pfet_84_d));
  PullUp pullup_39 (.out(pfet_77_s));
  PFET #(.unidirectional("true")) pfet_85 (.G(pfet_71_d), .S(pfet_77_s));  // open: D
  NFET #(.unidirectional("true")) nfet_77 (.G(pfet_17_d), .D(pfet_77_d), .S(nfet_77_s));
  NFET #(.unidirectional("true")) nfet_78 (.G(pfet_71_d), .D(nfet_77_s), .S(1'b0));
  PullUp pullup_40 (.out(pfet_78_s));
  PFET #(.unidirectional("true")) pfet_86 (.G(pfet_71_d), .S(pfet_78_s), .D(pfet_78_d));
  NFET #(.unidirectional("true")) nfet_79 (.G(pfet_71_d), .D(pfet_78_d), .S(nfet_79_s));
  NFET #(.unidirectional("true")) nfet_80 (.G(pfet_71_d), .D(nfet_79_s), .S(1'b0));
  PullUp pullup_41 (.out(pfet_79_s));
  PFET #(.unidirectional("true")) pfet_87 (.G(pfet_71_d), .S(pfet_79_s));  // open: D
  NFET #(.unidirectional("true")) nfet_81 (.G(pfet_19_d), .D(pfet_79_d), .S(nfet_81_s));
  NFET #(.unidirectional("true")) nfet_82 (.G(pfet_71_d), .D(nfet_81_s), .S(1'b0));
  PullUp pullup_42 (.out(pfet_80_s));
  PFET #(.unidirectional("true")) pfet_88 (.G(pfet_71_d), .S(pfet_80_s), .D(pfet_80_d));
  NFET #(.unidirectional("true")) nfet_83 (.G(pfet_71_d), .D(pfet_80_d), .S(nfet_83_s));
  NFET #(.unidirectional("true")) nfet_84 (.G(pfet_71_d), .D(nfet_83_s), .S(1'b0));
  PullUp pullup_43 (.out(pfet_81_s));
  PFET #(.unidirectional("true")) pfet_89 (.G(pfet_71_d), .S(pfet_81_s));  // open: D
  NFET #(.unidirectional("true")) nfet_85 (.G(pfet_21_d), .D(pfet_81_d), .S(nfet_85_s));
  NFET #(.unidirectional("true")) nfet_86 (.G(pfet_71_d), .D(nfet_85_s), .S(1'b0));
  PullUp pullup_44 (.out(pfet_82_s));
  PFET #(.unidirectional("true")) pfet_90 (.G(pfet_71_d), .S(pfet_82_s), .D(pfet_82_d));
  NFET #(.unidirectional("true")) nfet_87 (.G(pfet_71_d), .D(pfet_82_d), .S(nfet_87_s));
  NFET #(.unidirectional("true")) nfet_88 (.G(pfet_71_d), .D(nfet_87_s), .S(1'b0));
  PullUp pullup_45 (.out(pfet_83_s));
  PFET #(.unidirectional("true")) pfet_91 (.G(pfet_71_d), .S(pfet_83_s));  // open: D
  NFET #(.unidirectional("true")) nfet_89 (.G(pfet_23_d), .D(pfet_83_d), .S(nfet_89_s));
  NFET #(.unidirectional("true")) nfet_90 (.G(pfet_71_d), .D(nfet_89_s), .S(1'b0));
  PullUp pullup_46 (.out(pfet_84_s));
  PFET #(.unidirectional("true")) pfet_92 (.G(pfet_71_d), .S(pfet_84_s), .D(pfet_84_d));
  NFET #(.unidirectional("true")) nfet_91 (.G(pfet_71_d), .D(pfet_84_d), .S(nfet_91_s));
  NFET #(.unidirectional("true")) nfet_92 (.G(pfet_71_d), .D(nfet_91_s), .S(1'b0));
  PFET #(.unidirectional("true")) pfet_93 (.G(pfet_17_d), .S(pfet_93_s), .D(pfet_93_d));
  PFET #(.unidirectional("true")) pfet_94 (.G(pfet_78_d), .S(pfet_94_s), .D(pfet_94_d));
  PFET #(.unidirectional("true")) pfet_95 (.G(pfet_19_d), .S(pfet_95_s), .D(pfet_95_d));
  PFET #(.unidirectional("true")) pfet_96 (.G(pfet_80_d), .S(pfet_96_s), .D(pfet_96_d));
  PFET #(.unidirectional("true")) pfet_97 (.G(pfet_21_d), .S(pfet_97_s), .D(pfet_97_d));
  PFET #(.unidirectional("true")) pfet_98 (.G(pfet_82_d), .S(pfet_98_s), .D(pfet_98_d));
  PFET #(.unidirectional("true")) pfet_99 (.G(pfet_23_d), .S(pfet_99_s), .D(pfet_99_d));
  PFET #(.unidirectional("true")) pfet_100 (.G(pfet_84_d), .S(pfet_100_s), .D(pfet_100_d));
  PullUp pullup_47 (.out(pfet_93_s));
  PFET #(.unidirectional("true")) pfet_101 (.G(pfet_17_d), .S(pfet_93_s), .D(pfet_93_d));
  NFET #(.unidirectional("true")) nfet_93 (.G(pfet_17_d), .D(pfet_93_d), .S(nfet_93_s));
  NFET #(.unidirectional("true")) nfet_94 (.G(pfet_17_d), .D(nfet_93_s), .S(1'b0));
  PullUp pullup_48 (.out(pfet_94_s));
  PFET #(.unidirectional("true")) pfet_102 (.G(pfet_78_d), .S(pfet_94_s), .D(pfet_94_d));
  NFET #(.unidirectional("true")) nfet_95 (.G(pfet_78_d), .D(pfet_94_d), .S(nfet_95_s));
  NFET #(.unidirectional("true")) nfet_96 (.G(pfet_78_d), .D(nfet_95_s), .S(1'b0));
  PullUp pullup_49 (.out(pfet_95_s));
  PFET #(.unidirectional("true")) pfet_103 (.G(pfet_19_d), .S(pfet_95_s), .D(pfet_95_d));
  NFET #(.unidirectional("true")) nfet_97 (.G(pfet_19_d), .D(pfet_95_d), .S(nfet_97_s));
  NFET #(.unidirectional("true")) nfet_98 (.G(pfet_19_d), .D(nfet_97_s), .S(1'b0));
  PullUp pullup_50 (.out(pfet_96_s));
  PFET #(.unidirectional("true")) pfet_104 (.G(pfet_80_d), .S(pfet_96_s), .D(pfet_96_d));
  NFET #(.unidirectional("true")) nfet_99 (.G(pfet_80_d), .D(pfet_96_d), .S(nfet_99_s));
  NFET #(.unidirectional("true")) nfet_100 (.G(pfet_80_d), .D(nfet_99_s), .S(1'b0));
  PullUp pullup_51 (.out(pfet_97_s));
  PFET #(.unidirectional("true")) pfet_105 (.G(pfet_21_d), .S(pfet_97_s), .D(pfet_97_d));
  NFET #(.unidirectional("true")) nfet_101 (.G(pfet_21_d), .D(pfet_97_d), .S(nfet_101_s));
  NFET #(.unidirectional("true")) nfet_102 (.G(pfet_21_d), .D(nfet_101_s), .S(1'b0));
  PullUp pullup_52 (.out(pfet_98_s));
  PFET #(.unidirectional("true")) pfet_106 (.G(pfet_82_d), .S(pfet_98_s), .D(pfet_98_d));
  NFET #(.unidirectional("true")) nfet_103 (.G(pfet_82_d), .D(pfet_98_d), .S(nfet_103_s));
  NFET #(.unidirectional("true")) nfet_104 (.G(pfet_82_d), .D(nfet_103_s), .S(1'b0));
  PullUp pullup_53 (.out(pfet_99_s));
  PFET #(.unidirectional("true")) pfet_107 (.G(pfet_23_d), .S(pfet_99_s), .D(pfet_99_d));
  NFET #(.unidirectional("true")) nfet_105 (.G(pfet_23_d), .D(pfet_99_d), .S(nfet_105_s));
  NFET #(.unidirectional("true")) nfet_106 (.G(pfet_23_d), .D(nfet_105_s), .S(1'b0));
  PullUp pullup_54 (.out(pfet_100_s));
  PFET #(.unidirectional("true")) pfet_108 (.G(pfet_84_d), .S(pfet_100_s), .D(pfet_100_d));
  NFET #(.unidirectional("true")) nfet_107 (.G(pfet_84_d), .D(pfet_100_d), .S(nfet_107_s));
  NFET #(.unidirectional("true")) nfet_108 (.G(pfet_84_d), .D(nfet_107_s), .S(1'b0));
  PFET #(.unidirectional("true")) pfet_109 (.G(pfet_93_d), .S(pfet_109_s), .D(pfet_109_d));
  PFET #(.unidirectional("true")) pfet_110 (.G(pfet_95_d), .S(pfet_110_s), .D(pfet_110_d));
  PFET #(.unidirectional("true")) pfet_111 (.G(pfet_97_d), .S(pfet_111_s), .D(pfet_111_d));
  PFET #(.unidirectional("true")) pfet_112 (.G(pfet_99_d), .S(pfet_112_s), .D(pfet_112_d));
  PullUp pullup_55 (.out(pfet_109_s));
  PFET #(.unidirectional("true")) pfet_113 (.G(pfet_94_d), .S(pfet_109_s));  // open: D
  NFET #(.unidirectional("true")) nfet_109 (.G(pfet_93_d), .D(pfet_109_d), .S(nfet_109_s));
  NFET #(.unidirectional("true")) nfet_110 (.G(pfet_94_d), .D(nfet_109_s), .S(1'b0));
  PullUp pullup_56 (.out(pfet_110_s));
  PFET #(.unidirectional("true")) pfet_114 (.G(pfet_96_d), .S(pfet_110_s));  // open: D
  NFET #(.unidirectional("true")) nfet_111 (.G(pfet_95_d), .D(pfet_110_d), .S(nfet_111_s));
  NFET #(.unidirectional("true")) nfet_112 (.G(pfet_96_d), .D(nfet_111_s), .S(1'b0));
  PullUp pullup_57 (.out(pfet_111_s));
  PFET #(.unidirectional("true")) pfet_115 (.G(pfet_98_d), .S(pfet_111_s));  // open: D
  NFET #(.unidirectional("true")) nfet_113 (.G(pfet_97_d), .D(pfet_111_d), .S(nfet_113_s));
  NFET #(.unidirectional("true")) nfet_114 (.G(pfet_98_d), .D(nfet_113_s), .S(1'b0));
  PullUp pullup_58 (.out(pfet_112_s));
  PFET #(.unidirectional("true")) pfet_116 (.G(pfet_100_d), .S(pfet_112_s));  // open: D
  NFET #(.unidirectional("true")) nfet_115 (.G(pfet_99_d), .D(pfet_112_d), .S(nfet_115_s));
  NFET #(.unidirectional("true")) nfet_116 (.G(pfet_100_d), .D(nfet_115_s), .S(1'b0));
  PFET pfet_117 (.G(pfet_77_d), .S(1'b1), .D(driver_1_out[3]));
  PFET pfet_118 (.G(pfet_109_d), .S(driver_1_out[3]), .D(1'b0));
  PFET pfet_119 (.G(pfet_79_d), .S(1'b1), .D(driver_1_out[2]));
  PFET pfet_120 (.G(pfet_110_d), .S(driver_1_out[2]), .D(1'b0));
  PFET pfet_121 (.G(pfet_81_d), .S(1'b1), .D(driver_1_out[1]));
  PFET pfet_122 (.G(pfet_111_d), .S(driver_1_out[1]), .D(1'b0));
  PFET pfet_123 (.G(pfet_83_d), .S(1'b1), .D(driver_1_out[0]));
  PFET pfet_124 (.G(pfet_112_d), .S(driver_1_out[0]), .D(1'b0));
  PullDown pulldown_13 (.out(pfet_49_d));
  PullDown pulldown_14 (.out(pfet_51_d));
  PullDown pulldown_15 (.out(pfet_53_d));
  PullDown pulldown_16 (.out(pfet_55_d));
  PFET #(.unidirectional("true")) pfet_125 (.G(pfet_49_d), .S(pfet_125_s), .D(pfet_125_d));
  PFET #(.unidirectional("true")) pfet_126 (.G(pfet_71_d), .S(pfet_126_s), .D(pfet_126_d));
  PFET #(.unidirectional("true")) pfet_127 (.G(pfet_51_d), .S(pfet_127_s), .D(pfet_127_d));
  PFET #(.unidirectional("true")) pfet_128 (.G(pfet_71_d), .S(pfet_128_s), .D(pfet_128_d));
  PFET #(.unidirectional("true")) pfet_129 (.G(pfet_53_d), .S(pfet_129_s), .D(pfet_129_d));
  PFET #(.unidirectional("true")) pfet_130 (.G(pfet_71_d), .S(pfet_130_s), .D(pfet_130_d));
  PFET #(.unidirectional("true")) pfet_131 (.G(pfet_55_d), .S(pfet_131_s), .D(pfet_131_d));
  PFET #(.unidirectional("true")) pfet_132 (.G(pfet_71_d), .S(pfet_132_s), .D(pfet_132_d));
  PullUp pullup_59 (.out(pfet_125_s));
  PFET #(.unidirectional("true")) pfet_133 (.G(pfet_71_d), .S(pfet_125_s));  // open: D
  NFET #(.unidirectional("true")) nfet_117 (.G(pfet_49_d), .D(pfet_125_d), .S(nfet_117_s));
  NFET #(.unidirectional("true")) nfet_118 (.G(pfet_71_d), .D(nfet_117_s), .S(1'b0));
  PullUp pullup_60 (.out(pfet_126_s));
  PFET #(.unidirectional("true")) pfet_134 (.G(pfet_71_d), .S(pfet_126_s), .D(pfet_126_d));
  NFET #(.unidirectional("true")) nfet_119 (.G(pfet_71_d), .D(pfet_126_d), .S(nfet_119_s));
  NFET #(.unidirectional("true")) nfet_120 (.G(pfet_71_d), .D(nfet_119_s), .S(1'b0));
  PullUp pullup_61 (.out(pfet_127_s));
  PFET #(.unidirectional("true")) pfet_135 (.G(pfet_71_d), .S(pfet_127_s));  // open: D
  NFET #(.unidirectional("true")) nfet_121 (.G(pfet_51_d), .D(pfet_127_d), .S(nfet_121_s));
  NFET #(.unidirectional("true")) nfet_122 (.G(pfet_71_d), .D(nfet_121_s), .S(1'b0));
  PullUp pullup_62 (.out(pfet_128_s));
  PFET #(.unidirectional("true")) pfet_136 (.G(pfet_71_d), .S(pfet_128_s), .D(pfet_128_d));
  NFET #(.unidirectional("true")) nfet_123 (.G(pfet_71_d), .D(pfet_128_d), .S(nfet_123_s));
  NFET #(.unidirectional("true")) nfet_124 (.G(pfet_71_d), .D(nfet_123_s), .S(1'b0));
  PullUp pullup_63 (.out(pfet_129_s));
  PFET #(.unidirectional("true")) pfet_137 (.G(pfet_71_d), .S(pfet_129_s));  // open: D
  NFET #(.unidirectional("true")) nfet_125 (.G(pfet_53_d), .D(pfet_129_d), .S(nfet_125_s));
  NFET #(.unidirectional("true")) nfet_126 (.G(pfet_71_d), .D(nfet_125_s), .S(1'b0));
  PullUp pullup_64 (.out(pfet_130_s));
  PFET #(.unidirectional("true")) pfet_138 (.G(pfet_71_d), .S(pfet_130_s), .D(pfet_130_d));
  NFET #(.unidirectional("true")) nfet_127 (.G(pfet_71_d), .D(pfet_130_d), .S(nfet_127_s));
  NFET #(.unidirectional("true")) nfet_128 (.G(pfet_71_d), .D(nfet_127_s), .S(1'b0));
  PullUp pullup_65 (.out(pfet_131_s));
  PFET #(.unidirectional("true")) pfet_139 (.G(pfet_71_d), .S(pfet_131_s));  // open: D
  NFET #(.unidirectional("true")) nfet_129 (.G(pfet_55_d), .D(pfet_131_d), .S(nfet_129_s));
  NFET #(.unidirectional("true")) nfet_130 (.G(pfet_71_d), .D(nfet_129_s), .S(1'b0));
  PullUp pullup_66 (.out(pfet_132_s));
  PFET #(.unidirectional("true")) pfet_140 (.G(pfet_71_d), .S(pfet_132_s), .D(pfet_132_d));
  NFET #(.unidirectional("true")) nfet_131 (.G(pfet_71_d), .D(pfet_132_d), .S(nfet_131_s));
  NFET #(.unidirectional("true")) nfet_132 (.G(pfet_71_d), .D(nfet_131_s), .S(1'b0));
  PFET #(.unidirectional("true")) pfet_141 (.G(pfet_49_d), .S(pfet_141_s), .D(pfet_141_d));
  PFET #(.unidirectional("true")) pfet_142 (.G(pfet_126_d), .S(pfet_142_s), .D(pfet_142_d));
  PFET #(.unidirectional("true")) pfet_143 (.G(pfet_51_d), .S(pfet_143_s), .D(pfet_143_d));
  PFET #(.unidirectional("true")) pfet_144 (.G(pfet_128_d), .S(pfet_144_s), .D(pfet_144_d));
  PFET #(.unidirectional("true")) pfet_145 (.G(pfet_53_d), .S(pfet_145_s), .D(pfet_145_d));
  PFET #(.unidirectional("true")) pfet_146 (.G(pfet_130_d), .S(pfet_146_s), .D(pfet_146_d));
  PFET #(.unidirectional("true")) pfet_147 (.G(pfet_55_d), .S(pfet_147_s), .D(pfet_147_d));
  PFET #(.unidirectional("true")) pfet_148 (.G(pfet_132_d), .S(pfet_148_s), .D(pfet_148_d));
  PullUp pullup_67 (.out(pfet_141_s));
  PFET #(.unidirectional("true")) pfet_149 (.G(pfet_49_d), .S(pfet_141_s), .D(pfet_141_d));
  NFET #(.unidirectional("true")) nfet_133 (.G(pfet_49_d), .D(pfet_141_d), .S(nfet_133_s));
  NFET #(.unidirectional("true")) nfet_134 (.G(pfet_49_d), .D(nfet_133_s), .S(1'b0));
  PullUp pullup_68 (.out(pfet_142_s));
  PFET #(.unidirectional("true")) pfet_150 (.G(pfet_126_d), .S(pfet_142_s), .D(pfet_142_d));
  NFET #(.unidirectional("true")) nfet_135 (.G(pfet_126_d), .D(pfet_142_d), .S(nfet_135_s));
  NFET #(.unidirectional("true")) nfet_136 (.G(pfet_126_d), .D(nfet_135_s), .S(1'b0));
  PullUp pullup_69 (.out(pfet_143_s));
  PFET #(.unidirectional("true")) pfet_151 (.G(pfet_51_d), .S(pfet_143_s), .D(pfet_143_d));
  NFET #(.unidirectional("true")) nfet_137 (.G(pfet_51_d), .D(pfet_143_d), .S(nfet_137_s));
  NFET #(.unidirectional("true")) nfet_138 (.G(pfet_51_d), .D(nfet_137_s), .S(1'b0));
  PullUp pullup_70 (.out(pfet_144_s));
  PFET #(.unidirectional("true")) pfet_152 (.G(pfet_128_d), .S(pfet_144_s), .D(pfet_144_d));
  NFET #(.unidirectional("true")) nfet_139 (.G(pfet_128_d), .D(pfet_144_d), .S(nfet_139_s));
  NFET #(.unidirectional("true")) nfet_140 (.G(pfet_128_d), .D(nfet_139_s), .S(1'b0));
  PullUp pullup_71 (.out(pfet_145_s));
  PFET #(.unidirectional("true")) pfet_153 (.G(pfet_53_d), .S(pfet_145_s), .D(pfet_145_d));
  NFET #(.unidirectional("true")) nfet_141 (.G(pfet_53_d), .D(pfet_145_d), .S(nfet_141_s));
  NFET #(.unidirectional("true")) nfet_142 (.G(pfet_53_d), .D(nfet_141_s), .S(1'b0));
  PullUp pullup_72 (.out(pfet_146_s));
  PFET #(.unidirectional("true")) pfet_154 (.G(pfet_130_d), .S(pfet_146_s), .D(pfet_146_d));
  NFET #(.unidirectional("true")) nfet_143 (.G(pfet_130_d), .D(pfet_146_d), .S(nfet_143_s));
  NFET #(.unidirectional("true")) nfet_144 (.G(pfet_130_d), .D(nfet_143_s), .S(1'b0));
  PullUp pullup_73 (.out(pfet_147_s));
  PFET #(.unidirectional("true")) pfet_155 (.G(pfet_55_d), .S(pfet_147_s), .D(pfet_147_d));
  NFET #(.unidirectional("true")) nfet_145 (.G(pfet_55_d), .D(pfet_147_d), .S(nfet_145_s));
  NFET #(.unidirectional("true")) nfet_146 (.G(pfet_55_d), .D(nfet_145_s), .S(1'b0));
  PullUp pullup_74 (.out(pfet_148_s));
  PFET #(.unidirectional("true")) pfet_156 (.G(pfet_132_d), .S(pfet_148_s), .D(pfet_148_d));
  NFET #(.unidirectional("true")) nfet_147 (.G(pfet_132_d), .D(pfet_148_d), .S(nfet_147_s));
  NFET #(.unidirectional("true")) nfet_148 (.G(pfet_132_d), .D(nfet_147_s), .S(1'b0));
  PFET #(.unidirectional("true")) pfet_157 (.G(pfet_141_d), .S(pfet_157_s), .D(pfet_157_d));
  PFET #(.unidirectional("true")) pfet_158 (.G(pfet_143_d), .S(pfet_158_s), .D(pfet_158_d));
  PFET #(.unidirectional("true")) pfet_159 (.G(pfet_145_d), .S(pfet_159_s), .D(pfet_159_d));
  PFET #(.unidirectional("true")) pfet_160 (.G(pfet_147_d), .S(pfet_160_s), .D(pfet_160_d));
  PullUp pullup_75 (.out(pfet_157_s));
  PFET #(.unidirectional("true")) pfet_161 (.G(pfet_142_d), .S(pfet_157_s));  // open: D
  NFET #(.unidirectional("true")) nfet_149 (.G(pfet_141_d), .D(pfet_157_d), .S(nfet_149_s));
  NFET #(.unidirectional("true")) nfet_150 (.G(pfet_142_d), .D(nfet_149_s), .S(1'b0));
  PullUp pullup_76 (.out(pfet_158_s));
  PFET #(.unidirectional("true")) pfet_162 (.G(pfet_144_d), .S(pfet_158_s));  // open: D
  NFET #(.unidirectional("true")) nfet_151 (.G(pfet_143_d), .D(pfet_158_d), .S(nfet_151_s));
  NFET #(.unidirectional("true")) nfet_152 (.G(pfet_144_d), .D(nfet_151_s), .S(1'b0));
  PullUp pullup_77 (.out(pfet_159_s));
  PFET #(.unidirectional("true")) pfet_163 (.G(pfet_146_d), .S(pfet_159_s));  // open: D
  NFET #(.unidirectional("true")) nfet_153 (.G(pfet_145_d), .D(pfet_159_d), .S(nfet_153_s));
  NFET #(.unidirectional("true")) nfet_154 (.G(pfet_146_d), .D(nfet_153_s), .S(1'b0));
  PullUp pullup_78 (.out(pfet_160_s));
  PFET #(.unidirectional("true")) pfet_164 (.G(pfet_148_d), .S(pfet_160_s));  // open: D
  NFET #(.unidirectional("true")) nfet_155 (.G(pfet_147_d), .D(pfet_160_d), .S(nfet_155_s));
  NFET #(.unidirectional("true")) nfet_156 (.G(pfet_148_d), .D(nfet_155_s), .S(1'b0));
  PFET pfet_165 (.G(pfet_125_d), .S(1'b1), .D(driver_1_out_2[3]));
  PFET pfet_166 (.G(pfet_157_d), .S(driver_1_out_2[3]), .D(1'b0));
  PFET pfet_167 (.G(pfet_127_d), .S(1'b1), .D(driver_1_out_2[2]));
  PFET pfet_168 (.G(pfet_158_d), .S(driver_1_out_2[2]), .D(1'b0));
  PFET pfet_169 (.G(pfet_129_d), .S(1'b1), .D(driver_1_out_2[1]));
  PFET pfet_170 (.G(pfet_159_d), .S(driver_1_out_2[1]), .D(1'b0));
  PFET pfet_171 (.G(pfet_131_d), .S(1'b1), .D(driver_1_out_2[0]));
  PFET pfet_172 (.G(pfet_160_d), .S(driver_1_out_2[0]), .D(1'b0));

  // Notes on the sheet:
  //   Register
  //   Input/Output
  //   Register enabled
  //   Input
  //   1b mem
  //   Data
  //   Set
  //   NAND
  //   RAM BUS
  //   Output
  //   Enable
  //   AND
  //   X
  //   Y
  //   NOT
  //   Buffer HI 8B
  //   Buffer HI
  //   OR
endmodule
