// Digital circuit and_from_nand.dig as structural Verilog
module and_from_nand (
  input  i1,
  input  i2,
  output o
);

  wire nfet_1_s, nfet_3_s, pfet_1_d, pfet_1_s, pfet_3_s;

  PFET #(.unidirectional("true")) pfet_1 (.G(i1), .S(pfet_1_s), .D(pfet_1_d));
  PullUp pullup_1 (.out(pfet_1_s));
  PFET #(.unidirectional("true")) pfet_2 (.G(i2), .S(pfet_1_s), .D(pfet_1_d));
  NFET #(.unidirectional("true")) nfet_1 (.G(i1), .D(pfet_1_d), .S(nfet_1_s));
  NFET #(.unidirectional("true")) nfet_2 (.G(i2), .D(nfet_1_s), .S(1'b0));
  PFET #(.unidirectional("true")) pfet_3 (.G(pfet_1_d), .S(pfet_3_s), .D(o));
  PFET #(.unidirectional("true")) pfet_4 (.G(pfet_1_d), .S(pfet_3_s), .D(o));
  NFET #(.unidirectional("true")) nfet_3 (.G(pfet_1_d), .D(o), .S(nfet_3_s));
  NFET #(.unidirectional("true")) nfet_4 (.G(pfet_1_d), .D(nfet_3_s), .S(1'b0));
  PullUp pullup_2 (.out(pfet_3_s));

  // Notes on the sheet:
  //   NAND
  //   NOT
endmodule
