// Digital circuit buffer_high_impedance.dig as structural Verilog
module buffer_high_impedance (
  input  i,
  input  e,
  output o
);

  wire nfet_1_s, nfet_3_s, nfet_5_s, nfet_7_s, nfet_9_s, pfet_1_d, pfet_1_s, pfet_2_d, pfet_2_s, pfet_5_d,
       pfet_5_s, pfet_6_d, pfet_6_s, pfet_9_d, pfet_9_s;

  PullDown pulldown_1 (.out(i));
  PFET #(.unidirectional("true")) pfet_1 (.G(i), .S(pfet_1_s), .D(pfet_1_d));
  PFET #(.unidirectional("true")) pfet_2 (.G(e), .S(pfet_2_s), .D(pfet_2_d));
  PFET #(.unidirectional("true")) pfet_3 (.G(e), .S(pfet_1_s), .D(pfet_1_d));
  NFET #(.unidirectional("true")) nfet_1 (.G(i), .D(pfet_1_d), .S(nfet_1_s));
  NFET #(.unidirectional("true")) nfet_2 (.G(e), .D(nfet_1_s), .S(1'b0));
  PFET #(.unidirectional("true")) pfet_4 (.G(e), .S(pfet_2_s), .D(pfet_2_d));
  NFET #(.unidirectional("true")) nfet_3 (.G(e), .D(pfet_2_d), .S(nfet_3_s));
  NFET #(.unidirectional("true")) nfet_4 (.G(e), .D(nfet_3_s), .S(1'b0));
  PullUp pullup_1 (.out(pfet_1_s));
  PullUp pullup_2 (.out(pfet_2_s));
  PFET #(.unidirectional("true")) pfet_5 (.G(i), .S(pfet_5_s), .D(pfet_5_d));
  PFET #(.unidirectional("true")) pfet_6 (.G(pfet_2_d), .S(pfet_6_s), .D(pfet_6_d));
  PullUp pullup_3 (.out(pfet_5_s));
  PFET #(.unidirectional("true")) pfet_7 (.G(i), .S(pfet_5_s), .D(pfet_5_d));
  NFET #(.unidirectional("true")) nfet_5 (.G(i), .D(pfet_5_d), .S(nfet_5_s));
  NFET #(.unidirectional("true")) nfet_6 (.G(i), .D(nfet_5_s), .S(1'b0));
  PullUp pullup_4 (.out(pfet_6_s));
  PFET #(.unidirectional("true")) pfet_8 (.G(pfet_2_d), .S(pfet_6_s), .D(pfet_6_d));
  NFET #(.unidirectional("true")) nfet_7 (.G(pfet_2_d), .D(pfet_6_d), .S(nfet_7_s));
  NFET #(.unidirectional("true")) nfet_8 (.G(pfet_2_d), .D(nfet_7_s), .S(1'b0));
  PFET #(.unidirectional("true")) pfet_9 (.G(pfet_5_d), .S(pfet_9_s), .D(pfet_9_d));
  PFET #(.unidirectional("true")) pfet_10 (.G(pfet_6_d), .S(pfet_9_s), .D(pfet_9_d));
  NFET #(.unidirectional("true")) nfet_9 (.G(pfet_5_d), .D(pfet_9_d), .S(nfet_9_s));
  NFET #(.unidirectional("true")) nfet_10 (.G(pfet_6_d), .D(nfet_9_s), .S(1'b0));
  PFET pfet_11 (.G(pfet_1_d), .S(1'b1), .D(o));
  PullUp pullup_5 (.out(pfet_9_s));
  PFET pfet_12 (.G(pfet_9_d), .S(o), .D(1'b0));

  // Notes on the sheet:
  //   Buffer HI
  //   NAND
  //   NOT
  //   OR
endmodule
