// Digital circuit buffer_high_impedance_8bytes.dig as structural Verilog
module buffer_high_impedance_8bytes (
  input  [7:0] i,
  input  in_3,
  output [7:0] o
);

  wire nfet_1_s, nfet_3_s, nfet_5_s, nfet_7_s, nfet_9_s, nfet_11_s, nfet_13_s, nfet_15_s, nfet_17_s,
       nfet_19_s, nfet_21_s, nfet_23_s, nfet_25_s, nfet_27_s, nfet_29_s, nfet_31_s, nfet_33_s, nfet_35_s,
       nfet_37_s, nfet_39_s, nfet_41_s, nfet_43_s, nfet_45_s, nfet_47_s, nfet_49_s, nfet_51_s, nfet_53_s,
       nfet_55_s, nfet_57_s, nfet_59_s, nfet_61_s, nfet_63_s, nfet_65_s, nfet_67_s, nfet_69_s, nfet_71_s,
       nfet_73_s, nfet_75_s, nfet_77_s, nfet_79_s, pfet_1_d, pfet_1_s, pfet_2_d, pfet_2_s, pfet_3_d,
       pfet_3_s, pfet_4_d, pfet_4_s, pfet_5_d, pfet_5_s, pfet_6_d, pfet_6_s, pfet_7_d, pfet_7_s, pfet_8_d,
       pfet_8_s, pfet_17_d, pfet_17_s, pfet_18_d, pfet_18_s, pfet_19_d, pfet_19_s, pfet_20_d, pfet_20_s,
       pfet_21_d, pfet_21_s, pfet_22_d, pfet_22_s, pfet_23_d, pfet_23_s, pfet_24_d, pfet_24_s, pfet_33_d,
       pfet_33_s, pfet_34_d, pfet_34_s, pfet_35_d, pfet_35_s, pfet_36_d, pfet_36_s, pfet_49_d, pfet_49_s,
       pfet_51_d, pfet_51_s, pfet_53_d, pfet_53_s, pfet_55_d, pfet_55_s, pfet_57_d, pfet_57_s, pfet_59_d,
       pfet_59_s, pfet_61_d, pfet_61_s, pfet_63_d, pfet_63_s, pfet_65_d, pfet_65_s, pfet_66_d, pfet_66_s,
       pfet_67_d, pfet_67_s, pfet_68_d, pfet_68_s, pfet_69_d, pfet_69_s, pfet_70_d, pfet_70_s, pfet_71_d,
       pfet_71_s, pfet_72_d, pfet_72_s, pfet_81_d, pfet_81_s, pfet_83_d, pfet_83_s, pfet_85_d, pfet_85_s,
       pfet_87_d, pfet_87_s;

  PFET #(.unidirectional("true")) pfet_1 (.G(i[4]), .S(pfet_1_s), .D(pfet_1_d));
  PullDown pulldown_1 (.out(i[4]));
  PFET #(.unidirectional("true")) pfet_2 (.G(in_3), .S(pfet_2_s), .D(pfet_2_d));
  PFET #(.unidirectional("true")) pfet_3 (.G(i[5]), .S(pfet_3_s), .D(pfet_3_d));
  PullDown pulldown_2 (.out(i[5]));
  PFET #(.unidirectional("true")) pfet_4 (.G(in_3), .S(pfet_4_s), .D(pfet_4_d));
  PFET #(.unidirectional("true")) pfet_5 (.G(i[6]), .S(pfet_5_s), .D(pfet_5_d));
  PullDown pulldown_3 (.out(i[6]));
  PFET #(.unidirectional("true")) pfet_6 (.G(in_3), .S(pfet_6_s), .D(pfet_6_d));
  PFET #(.unidirectional("true")) pfet_7 (.G(i[7]), .S(pfet_7_s), .D(pfet_7_d));
  PullDown pulldown_4 (.out(i[7]));
  PFET #(.unidirectional("true")) pfet_8 (.G(in_3), .S(pfet_8_s), .D(pfet_8_d));
  PullUp pullup_1 (.out(pfet_1_s));
  PFET #(.unidirectional("true")) pfet_9 (.G(in_3), .S(pfet_1_s));  // open: D
  NFET #(.unidirectional("true")) nfet_1 (.G(i[4]), .D(pfet_1_d), .S(nfet_1_s));
  NFET #(.unidirectional("true")) nfet_2 (.G(in_3), .D(nfet_1_s), .S(1'b0));
  PullUp pullup_2 (.out(pfet_2_s));
  PFET #(.unidirectional("true")) pfet_10 (.G(in_3), .S(pfet_2_s), .D(pfet_2_d));
  NFET #(.unidirectional("true")) nfet_3 (.G(in_3), .D(pfet_2_d), .S(nfet_3_s));
  NFET #(.unidirectional("true")) nfet_4 (.G(in_3), .D(nfet_3_s), .S(1'b0));
  PullUp pullup_3 (.out(pfet_3_s));
  PFET #(.unidirectional("true")) pfet_11 (.G(in_3), .S(pfet_3_s));  // open: D
  NFET #(.unidirectional("true")) nfet_5 (.G(i[5]), .D(pfet_3_d), .S(nfet_5_s));
  NFET #(.unidirectional("true")) nfet_6 (.G(in_3), .D(nfet_5_s), .S(1'b0));
  PullUp pullup_4 (.out(pfet_4_s));
  PFET #(.unidirectional("true")) pfet_12 (.G(in_3), .S(pfet_4_s), .D(pfet_4_d));
  NFET #(.unidirectional("true")) nfet_7 (.G(in_3), .D(pfet_4_d), .S(nfet_7_s));
  NFET #(.unidirectional("true")) nfet_8 (.G(in_3), .D(nfet_7_s), .S(1'b0));
  PullUp pullup_5 (.out(pfet_5_s));
  PFET #(.unidirectional("true")) pfet_13 (.G(in_3), .S(pfet_5_s));  // open: D
  NFET #(.unidirectional("true")) nfet_9 (.G(i[6]), .D(pfet_5_d), .S(nfet_9_s));
  NFET #(.unidirectional("true")) nfet_10 (.G(in_3), .D(nfet_9_s), .S(1'b0));
  PullUp pullup_6 (.out(pfet_6_s));
  PFET #(.unidirectional("true")) pfet_14 (.G(in_3), .S(pfet_6_s), .D(pfet_6_d));
  NFET #(.unidirectional("true")) nfet_11 (.G(in_3), .D(pfet_6_d), .S(nfet_11_s));
  NFET #(.unidirectional("true")) nfet_12 (.G(in_3), .D(nfet_11_s), .S(1'b0));
  PullUp pullup_7 (.out(pfet_7_s));
  PFET #(.unidirectional("true")) pfet_15 (.G(in_3), .S(pfet_7_s));  // open: D
  NFET #(.unidirectional("true")) nfet_13 (.G(i[7]), .D(pfet_7_d), .S(nfet_13_s));
  NFET #(.unidirectional("true")) nfet_14 (.G(in_3), .D(nfet_13_s), .S(1'b0));
  PullUp pullup_8 (.out(pfet_8_s));
  PFET #(.unidirectional("true")) pfet_16 (.G(in_3), .S(pfet_8_s), .D(pfet_8_d));
  NFET #(.unidirectional("true")) nfet_15 (.G(in_3), .D(pfet_8_d), .S(nfet_15_s));
  NFET #(.unidirectional("true")) nfet_16 (.G(in_3), .D(nfet_15_s), .S(1'b0));
  PFET #(.unidirectional("true")) pfet_17 (.G(i[4]), .S(pfet_17_s), .D(pfet_17_d));
  PFET #(.unidirectional("true")) pfet_18 (.G(pfet_2_d), .S(pfet_18_s), .D(pfet_18_d));
  PFET #(.unidirectional("true")) pfet_19 (.G(i[5]), .S(pfet_19_s), .D(pfet_19_d));
  PFET #(.unidirectional("true")) pfet_20 (.G(pfet_4_d), .S(pfet_20_s), .D(pfet_20_d));
  PFET #(.unidirectional("true")) pfet_21 (.G(i[6]), .S(pfet_21_s), .D(pfet_21_d));
  PFET #(.unidirectional("true")) pfet_22 (.G(pfet_6_d), .S(pfet_22_s), .D(pfet_22_d));
  PFET #(.unidirectional("true")) pfet_23 (.G(i[7]), .S(pfet_23_s), .D(pfet_23_d));
  PFET #(.unidirectional("true")) pfet_24 (.G(pfet_8_d), .S(pfet_24_s), .D(pfet_24_d));
  PullUp pullup_9 (.out(pfet_17_s));
  PFET #(.unidirectional("true")) pfet_25 (.G(i[4]), .S(pfet_17_s), .D(pfet_17_d));
  NFET #(.unidirectional("true")) nfet_17 (.G(i[4]), .D(pfet_17_d), .S(nfet_17_s));
  NFET #(.unidirectional("true")) nfet_18 (.G(i[4]), .D(nfet_17_s), .S(1'b0));
  PullUp pullup_10 (.out(pfet_18_s));
  PFET #(.unidirectional("true")) pfet_26 (.G(pfet_2_d), .S(pfet_18_s), .D(pfet_18_d));
  NFET #(.unidirectional("true")) nfet_19 (.G(pfet_2_d), .D(pfet_18_d), .S(nfet_19_s));
  NFET #(.unidirectional("true")) nfet_20 (.G(pfet_2_d), .D(nfet_19_s), .S(1'b0));
  PullUp pullup_11 (.out(pfet_19_s));
  PFET #(.unidirectional("true")) pfet_27 (.G(i[5]), .S(pfet_19_s), .D(pfet_19_d));
  NFET #(.unidirectional("true")) nfet_21 (.G(i[5]), .D(pfet_19_d), .S(nfet_21_s));
  NFET #(.unidirectional("true")) nfet_22 (.G(i[5]), .D(nfet_21_s), .S(1'b0));
  PullUp pullup_12 (.out(pfet_20_s));
  PFET #(.unidirectional("true")) pfet_28 (.G(pfet_4_d), .S(pfet_20_s), .D(pfet_20_d));
  NFET #(.unidirectional("true")) nfet_23 (.G(pfet_4_d), .D(pfet_20_d), .S(nfet_23_s));
  NFET #(.unidirectional("true")) nfet_24 (.G(pfet_4_d), .D(nfet_23_s), .S(1'b0));
  PullUp pullup_13 (.out(pfet_21_s));
  PFET #(.unidirectional("true")) pfet_29 (.G(i[6]), .S(pfet_21_s), .D(pfet_21_d));
  NFET #(.unidirectional("true")) nfet_25 (.G(i[6]), .D(pfet_21_d), .S(nfet_25_s));
  NFET #(.unidirectional("true")) nfet_26 (.G(i[6]), .D(nfet_25_s), .S(1'b0));
  PullUp pullup_14 (.out(pfet_22_s));
  PFET #(.unidirectional("true")) pfet_30 (.G(pfet_6_d), .S(pfet_22_s), .D(pfet_22_d));
  NFET #(.unidirectional("true")) nfet_27 (.G(pfet_6_d), .D(pfet_22_d), .S(nfet_27_s));
  NFET #(.unidirectional("true")) nfet_28 (.G(pfet_6_d), .D(nfet_27_s), .S(1'b0));
  PullUp pullup_15 (.out(pfet_23_s));
  PFET #(.unidirectional("true")) pfet_31 (.G(i[7]), .S(pfet_23_s), .D(pfet_23_d));
  NFET #(.unidirectional("true")) nfet_29 (.G(i[7]), .D(pfet_23_d), .S(nfet_29_s));
  NFET #(.unidirectional("true")) nfet_30 (.G(i[7]), .D(nfet_29_s), .S(1'b0));
  PullUp pullup_16 (.out(pfet_24_s));
  PFET #(.unidirectional("true")) pfet_32 (.G(pfet_8_d), .S(pfet_24_s), .D(pfet_24_d));
  NFET #(.unidirectional("true")) nfet_31 (.G(pfet_8_d), .D(pfet_24_d), .S(nfet_31_s));
  NFET #(.unidirectional("true")) nfet_32 (.G(pfet_8_d), .D(nfet_31_s), .S(1'b0));
  PFET #(.unidirectional("true")) pfet_33 (.G(pfet_17_d), .S(pfet_33_s), .D(pfet_33_d));
  PFET #(.unidirectional("true")) pfet_34 (.G(pfet_19_d), .S(pfet_34_s), .D(pfet_34_d));
  PFET #(.unidirectional("true")) pfet_35 (.G(pfet_21_d), .S(pfet_35_s), .D(pfet_35_d));
  PFET #(.unidirectional("true")) pfet_36 (.G(pfet_23_d), .S(pfet_36_s), .D(pfet_36_d));
  PullUp pullup_17 (.out(pfet_33_s));
  PFET #(.unidirectional("true")) pfet_37 (.G(pfet_18_d), .S(pfet_33_s));  // open: D
  NFET #(.unidirectional("true")) nfet_33 (.G(pfet_17_d), .D(pfet_33_d), .S(nfet_33_s));
  NFET #(.unidirectional("true")) nfet_34 (.G(pfet_18_d), .D(nfet_33_s), .S(1'b0));
  PullUp pullup_18 (.out(pfet_34_s));
  PFET #(.unidirectional("true")) pfet_38 (.G(pfet_20_d), .S(pfet_34_s));  // open: D
  NFET #(.unidirectional("true")) nfet_35 (.G(pfet_19_d), .D(pfet_34_d), .S(nfet_35_s));
  NFET #(.unidirectional("true")) nfet_36 (.G(pfet_20_d), .D(nfet_35_s), .S(1'b0));
  PullUp pullup_19 (.out(pfet_35_s));
  PFET #(.unidirectional("true")) pfet_39 (.G(pfet_22_d), .S(pfet_35_s));  // open: D
  NFET #(.unidirectional("true")) nfet_37 (.G(pfet_21_d), .D(pfet_35_d), .S(nfet_37_s));
  NFET #(.unidirectional("true")) nfet_38 (.G(pfet_22_d), .D(nfet_37_s), .S(1'b0));
  PullUp pullup_20 (.out(pfet_36_s));
  PFET #(.unidirectional("true")) pfet_40 (.G(pfet_24_d), .S(pfet_36_s));  // open: D
  NFET #(.unidirectional("true")) nfet_39 (.G(pfet_23_d), .D(pfet_36_d), .S(nfet_39_s));
  NFET #(.unidirectional("true")) nfet_40 (.G(pfet_24_d), .D(nfet_39_s), .S(1'b0));
  PFET pfet_41 (.G(pfet_1_d), .S(1'b1), .D(o[4]));
  PFET pfet_42 (.G(pfet_33_d), .S(o[4]), .D(1'b0));
  PFET pfet_43 (.G(pfet_3_d), .S(1'b1), .D(o[5]));
  PFET pfet_44 (.G(pfet_34_d), .S(o[5]), .D(1'b0));
  PFET pfet_45 (.G(pfet_5_d), .S(1'b1), .D(o[6]));
  PFET pfet_46 (.G(pfet_35_d), .S(o[6]), .D(1'b0));
  PFET pfet_47 (.G(pfet_7_d), .S(1'b1), .D(o[7]));
  PFET pfet_48 (.G(pfet_36_d), .S(o[7]), .D(1'b0));
  PullDown pulldown_5 (.out(i[0]));
  PullDown pulldown_6 (.out(i[1]));
  PullDown pulldown_7 (.out(i[2]));
  PullDown pulldown_8 (.out(i[3]));
  PFET #(.unidirectional("true")) pfet_49 (.G(i[0]), .S(pfet_49_s), .D(pfet_49_d));
  PFET #(.unidirectional("true")) pfet_50 (.G(in_3), .S(pfet_49_s));  // open: D
  NFET #(.unidirectional("true")) nfet_41 (.G(i[0]), .D(pfet_49_d), .S(nfet_41_s));
  NFET #(.unidirectional("true")) nfet_42 (.G(in_3), .D(nfet_41_s), .S(1'b0));
  PFET #(.unidirectional("true")) pfet_51 (.G(in_3), .S(pfet_51_s), .D(pfet_51_d));
  PFET #(.unidirectional("true")) pfet_52 (.G(in_3), .S(pfet_51_s), .D(pfet_51_d));
  NFET #(.unidirectional("true")) nfet_43 (.G(in_3), .D(pfet_51_d), .S(nfet_43_s));
  NFET #(.unidirectional("true")) nfet_44 (.G(in_3), .D(nfet_43_s), .S(1'b0));
  PFET #(.unidirectional("true")) pfet_53 (.G(i[1]), .S(pfet_53_s), .D(pfet_53_d));
  PFET #(.unidirectional("true")) pfet_54 (.G(in_3), .S(pfet_53_s));  // open: D
  NFET #(.unidirectional("true")) nfet_45 (.G(i[1]), .D(pfet_53_d), .S(nfet_45_s));
  NFET #(.unidirectional("true")) nfet_46 (.G(in_3), .D(nfet_45_s), .S(1'b0));
  PFET #(.unidirectional("true")) pfet_55 (.G(in_3), .S(pfet_55_s), .D(pfet_55_d));
  PFET #(.unidirectional("true")) pfet_56 (.G(in_3), .S(pfet_55_s), .D(pfet_55_d));
  NFET #(.unidirectional("true")) nfet_47 (.G(in_3), .D(pfet_55_d), .S(nfet_47_s));
  NFET #(.unidirectional("true")) nfet_48 (.G(in_3), .D(nfet_47_s), .S(1'b0));
  PFET #(.unidirectional("true")) pfet_57 (.G(i[2]), .S(pfet_57_s), .D(pfet_57_d));
  PFET #(.unidirectional("true")) pfet_58 (.G(in_3), .S(pfet_57_s));  // open: D
  NFET #(.unidirectional("true")) nfet_49 (.G(i[2]), .D(pfet_57_d), .S(nfet_49_s));
  NFET #(.unidirectional("true")) nfet_50 (.G(in_3), .D(nfet_49_s), .S(1'b0));
  PFET #(.unidirectional("true")) pfet_59 (.G(in_3), .S(pfet_59_s), .D(pfet_59_d));
  PFET #(.unidirectional("true")) pfet_60 (.G(in_3), .S(pfet_59_s), .D(pfet_59_d));
  NFET #(.unidirectional("true")) nfet_51 (.G(in_3), .D(pfet_59_d), .S(nfet_51_s));
  NFET #(.unidirectional("true")) nfet_52 (.G(in_3), .D(nfet_51_s), .S(1'b0));
  PFET #(.unidirectional("true")) pfet_61 (.G(i[3]), .S(pfet_61_s), .D(pfet_61_d));
  PFET #(.unidirectional("true")) pfet_62 (.G(in_3), .S(pfet_61_s));  // open: D
  NFET #(.unidirectional("true")) nfet_53 (.G(i[3]), .D(pfet_61_d), .S(nfet_53_s));
  NFET #(.unidirectional("true")) nfet_54 (.G(in_3), .D(nfet_53_s), .S(1'b0));
  PFET #(.unidirectional("true")) pfet_63 (.G(in_3), .S(pfet_63_s), .D(pfet_63_d));
  PFET #(.unidirectional("true")) pfet_64 (.G(in_3), .S(pfet_63_s), .D(pfet_63_d));
  NFET #(.unidirectional("true")) nfet_55 (.G(in_3), .D(pfet_63_d), .S(nfet_55_s));
  NFET #(.unidirectional("true")) nfet_56 (.G(in_3), .D(nfet_55_s), .S(1'b0));
  PullUp pullup_21 (.out(pfet_49_s));
  PullUp pullup_22 (.out(pfet_51_s));
  PullUp pullup_23 (.out(pfet_53_s));
  PullUp pullup_24 (.out(pfet_55_s));
  PullUp pullup_25 (.out(pfet_57_s));
  PullUp pullup_26 (.out(pfet_59_s));
  PullUp pullup_27 (.out(pfet_61_s));
  PullUp pullup_28 (.out(pfet_63_s));
  PFET #(.unidirectional("true")) pfet_65 (.G(i[0]), .S(pfet_65_s), .D(pfet_65_d));
  PFET #(.unidirectional("true")) pfet_66 (.G(pfet_51_d), .S(pfet_66_s), .D(pfet_66_d));
  PFET #(.unidirectional("true")) pfet_67 (.G(i[1]), .S(pfet_67_s), .D(pfet_67_d));
  PFET #(.unidirectional("true")) pfet_68 (.G(pfet_55_d), .S(pfet_68_s), .D(pfet_68_d));
  PFET #(.unidirectional("true")) pfet_69 (.G(i[2]), .S(pfet_69_s), .D(pfet_69_d));
  PFET #(.unidirectional("true")) pfet_70 (.G(pfet_59_d), .S(pfet_70_s), .D(pfet_70_d));
  PFET #(.unidirectional("true")) pfet_71 (.G(i[3]), .S(pfet_71_s), .D(pfet_71_d));
  PFET #(.unidirectional("true")) pfet_72 (.G(pfet_63_d), .S(pfet_72_s), .D(pfet_72_d));
  PullUp pullup_29 (.out(pfet_65_s));
  PFET #(.unidirectional("true")) pfet_73 (.G(i[0]), .S(pfet_65_s), .D(pfet_65_d));
  NFET #(.unidirectional("true")) nfet_57 (.G(i[0]), .D(pfet_65_d), .S(nfet_57_s));
  NFET #(.unidirectional("true")) nfet_58 (.G(i[0]), .D(nfet_57_s), .S(1'b0));
  PullUp pullup_30 (.out(pfet_66_s));
  PFET #(.unidirectional("true")) pfet_74 (.G(pfet_51_d), .S(pfet_66_s), .D(pfet_66_d));
  NFET #(.unidirectional("true")) nfet_59 (.G(pfet_51_d), .D(pfet_66_d), .S(nfet_59_s));
  NFET #(.unidirectional("true")) nfet_60 (.G(pfet_51_d), .D(nfet_59_s), .S(1'b0));
  PullUp pullup_31 (.out(pfet_67_s));
  PFET #(.unidirectional("true")) pfet_75 (.G(i[1]), .S(pfet_67_s), .D(pfet_67_d));
  NFET #(.unidirectional("true")) nfet_61 (.G(i[1]), .D(pfet_67_d), .S(nfet_61_s));
  NFET #(.unidirectional("true")) nfet_62 (.G(i[1]), .D(nfet_61_s), .S(1'b0));
  PullUp pullup_32 (.out(pfet_68_s));
  PFET #(.unidirectional("true")) pfet_76 (.G(pfet_55_d), .S(pfet_68_s), .D(pfet_68_d));
  NFET #(.unidirectional("true")) nfet_63 (.G(pfet_55_d), .D(pfet_68_d), .S(nfet_63_s));
  NFET #(.unidirectional("true")) nfet_64 (.G(pfet_55_d), .D(nfet_63_s), .S(1'b0));
  PullUp pullup_33 (.out(pfet_69_s));
  PFET #(.unidirectional("true")) pfet_77 (.G(i[2]), .S(pfet_69_s), .D(pfet_69_d));
  NFET #(.unidirectional("true")) nfet_65 (.G(i[2]), .D(pfet_69_d), .S(nfet_65_s));
  NFET #(.unidirectional("true")) nfet_66 (.G(i[2]), .D(nfet_65_s), .S(1'b0));
  PullUp pullup_34 (.out(pfet_70_s));
  PFET #(.unidirectional("true")) pfet_78 (.G(pfet_59_d), .S(pfet_70_s), .D(pfet_70_d));
  NFET #(.unidirectional("true")) nfet_67 (.G(pfet_59_d), .D(pfet_70_d), .S(nfet_67_s));
  NFET #(.unidirectional("true")) nfet_68 (.G(pfet_59_d), .D(nfet_67_s), .S(1'b0));
  PullUp pullup_35 (.out(pfet_71_s));
  PFET #(.unidirectional("true")) pfet_79 (.G(i[3]), .S(pfet_71_s), .D(pfet_71_d));
  NFET #(.unidirectional("true")) nfet_69 (.G(i[3]), .D(pfet_71_d), .S(nfet_69_s));
  NFET #(.unidirectional("true")) nfet_70 (.G(i[3]), .D(nfet_69_s), .S(1'b0));
  PullUp pullup_36 (.out(pfet_72_s));
  PFET #(.unidirectional("true")) pfet_80 (.G(pfet_63_d), .S(pfet_72_s), .D(pfet_72_d));
  NFET #(.unidirectional("true")) nfet_71 (.G(pfet_63_d), .D(pfet_72_d), .S(nfet_71_s));
  NFET #(.unidirectional("true")) nfet_72 (.G(pfet_63_d), .D(nfet_71_s), .S(1'b0));
  PullDown pulldown_9 ();  // open: out
  PFET #(.unidirectional("true")) pfet_81 (.G(pfet_65_d), .S(pfet_81_s), .D(pfet_81_d));
  PFET #(.unidirectional("true")) pfet_82 (.G(pfet_66_d), .S(pfet_81_s));  // open: D
  NFET #(.unidirectional("true")) nfet_73 (.G(pfet_65_d), .D(pfet_81_d), .S(nfet_73_s));
  NFET #(.unidirectional("true")) nfet_74 (.G(pfet_66_d), .D(nfet_73_s), .S(1'b0));
  PFET #(.unidirectional("true")) pfet_83 (.G(pfet_67_d), .S(pfet_83_s), .D(pfet_83_d));
  PFET #(.unidirectional("true")) pfet_84 (.G(pfet_68_d), .S(pfet_83_s));  // open: D
  NFET #(.unidirectional("true")) nfet_75 (.G(pfet_67_d), .D(pfet_83_d), .S(nfet_75_s));
  NFET #(.unidirectional("true")) nfet_76 (.G(pfet_68_d), .D(nfet_75_s), .S(1'b0));
  PFET #(.unidirectional("true")) pfet_85 (.G(pfet_69_d), .S(pfet_85_s), .D(pfet_85_d));
  PFET #(.unidirectional("true")) pfet_86 (.G(pfet_70_d), .S(pfet_85_s));  // open: D
  NFET #(.unidirectional("true")) nfet_77 (.G(pfet_69_d), .D(pfet_85_d), .S(nfet_77_s));
  NFET #(.unidirectional("true")) nfet_78 (.G(pfet_70_d), .D(nfet_77_s), .S(1'b0));
  PFET #(.unidirectional("true")) pfet_87 (.G(pfet_71_d), .S(pfet_87_s), .D(pfet_87_d));
  PFET #(.unidirectional("true")) pfet_88 (.G(pfet_72_d), .S(pfet_87_s));  // open: D
  NFET #(.unidirectional("true")) nfet_79 (.G(pfet_71_d), .D(pfet_87_d), .S(nfet_79_s));
  NFET #(.unidirectional("true")) nfet_80 (.G(pfet_72_d), .D(nfet_79_s), .S(1'b0));
  PFET pfet_89 (.G(pfet_49_d), .S(1'b1), .D(o[0]));
  PullUp pullup_37 (.out(pfet_81_s));
  PFET pfet_90 (.G(pfet_81_d), .S(o[0]), .D(1'b0));
  PFET pfet_91 (.G(pfet_53_d), .S(1'b1), .D(o[1]));
  PullUp pullup_38 (.out(pfet_83_s));
  PFET pfet_92 (.G(pfet_83_d), .S(o[1]), .D(1'b0));
  PFET pfet_93 (.G(pfet_57_d), .S(1'b1), .D(o[2]));
  PullUp pullup_39 (.out(pfet_85_s));
  PFET pfet_94 (.G(pfet_85_d), .S(o[2]), .D(1'b0));
  PFET pfet_95 (.G(pfet_61_d), .S(1'b1), .D(o[3]));
  PullUp pullup_40 (.out(pfet_87_s));
  PFET pfet_96 (.G(pfet_87_d), .S(o[3]), .D(1'b0));
  Seven_Seg_Hex seven_seg_hex_1 (.d(o[7:4]), .dp(1'b0));
  Seven_Seg_Hex seven_seg_hex_2 (.d(o[3:0]), .dp(1'b0));

  // Notes on the sheet:
  //   Buffer HI 8B
  //   Input
  //   Set
  //   Buffer HI
  //   NAND
  //   NOT
  //   OR
  //   Output
endmodule
