// Digital circuit byte_visor.dig as structural Verilog
module byte_visor (
);

  wire [3:0] undriven, undriven_2;

  Seven_Seg_Hex seven_seg_hex_1 (.d(undriven), .dp(1'b0));
  Seven_Seg_Hex seven_seg_hex_2 (.d(undriven_2), .dp(1'b0));
endmodule
