// Digital circuit decoder_4x16.dig as structural Verilog
module decoder_4x16 (
  input  [3:0] sel,
  output _0000,
  output _0001,
  output _0010,
  output _0011,
  output _0100,
  output _0101,
  output _0110,
  output _0111,
  output _1000,
  output _1001,
  output _1011,
  output _1010,
  output _1100,
  output _1110,
  output _1111,
  output _1101
);

  wire nfet_1_s, nfet_3_s, nfet_5_s, nfet_7_s, nfet_9_s, nfet_11_s, nfet_13_s, nfet_15_s, nfet_17_s,
       nfet_19_s, nfet_21_s, nfet_23_s, nfet_25_s, nfet_27_s, nfet_29_s, nfet_31_s, nfet_33_s, nfet_35_s,
       nfet_37_s, nfet_39_s, nfet_41_s, nfet_43_s, nfet_45_s, nfet_47_s, nfet_49_s, nfet_51_s, nfet_53_s,
       nfet_55_s, nfet_57_s, nfet_59_s, nfet_61_s, nfet_63_s, nfet_65_s, nfet_67_s, nfet_69_s, nfet_71_s,
       nfet_73_s, nfet_75_s, nfet_77_s, nfet_79_s, nfet_81_s, nfet_83_s, nfet_85_s, nfet_87_s, nfet_89_s,
       nfet_91_s, nfet_93_s, nfet_95_s, nfet_97_s, nfet_99_s, nfet_101_s, nfet_103_s, nfet_105_s, nfet_107_s,
       nfet_109_s, nfet_111_s, nfet_113_s, nfet_115_s, nfet_117_s, nfet_119_s, nfet_121_s, nfet_123_s,
       nfet_125_s, nfet_127_s, nfet_129_s, nfet_131_s, nfet_133_s, nfet_135_s, nfet_137_s, nfet_139_s,
       nfet_141_s, nfet_143_s, nfet_145_s, nfet_147_s, nfet_149_s, nfet_151_s, nfet_153_s, nfet_155_s,
       nfet_157_s, nfet_159_s, nfet_161_s, nfet_163_s, nfet_165_s, nfet_167_s, nfet_169_s, nfet_171_s,
       nfet_173_s, nfet_175_s, nfet_177_s, nfet_179_s, nfet_181_s, nfet_183_s, nfet_185_s, nfet_187_s,
       nfet_189_s, nfet_191_s, nfet_193_s, nfet_195_s, nfet_197_s, nfet_199_s, pfet_1_d, pfet_1_s, pfet_3_d,
       pfet_3_s, pfet_5_d, pfet_5_s, pfet_7_d, pfet_7_s, pfet_9_d, pfet_9_s, pfet_10_d, pfet_10_s, pfet_11_d,
       pfet_11_s, pfet_12_d, pfet_12_s, pfet_13_d, pfet_13_s, pfet_14_d, pfet_14_s, pfet_15_d, pfet_15_s,
       pfet_16_d, pfet_16_s, pfet_17_d, pfet_17_s, pfet_18_d, pfet_18_s, pfet_19_d, pfet_19_s, pfet_20_d,
       pfet_20_s, pfet_21_d, pfet_21_s, pfet_22_d, pfet_22_s, pfet_23_d, pfet_23_s, pfet_24_d, pfet_24_s,
       pfet_41_d, pfet_41_s, pfet_43_d, pfet_43_s, pfet_45_d, pfet_45_s, pfet_46_d, pfet_46_s, pfet_47_d,
       pfet_47_s, pfet_48_d, pfet_48_s, pfet_49_d, pfet_49_s, pfet_50_d, pfet_50_s, pfet_51_d, pfet_51_s,
       pfet_52_d, pfet_52_s, pfet_53_d, pfet_53_s, pfet_54_d, pfet_54_s, pfet_55_d, pfet_55_s, pfet_56_d,
       pfet_56_s, pfet_57_d, pfet_57_s, pfet_58_d, pfet_58_s, pfet_73_d, pfet_73_s, pfet_74_d, pfet_74_s,
       pfet_75_d, pfet_75_s, pfet_76_d, pfet_76_s, pfet_77_d, pfet_77_s, pfet_78_d, pfet_78_s, pfet_79_d,
       pfet_79_s, pfet_80_d, pfet_80_s, pfet_81_d, pfet_81_s, pfet_82_d, pfet_82_s, pfet_83_d, pfet_83_s,
       pfet_84_d, pfet_84_s, pfet_85_d, pfet_85_s, pfet_86_d, pfet_86_s, pfet_87_d, pfet_87_s, pfet_88_d,
       pfet_88_s, pfet_105_d, pfet_105_s, pfet_106_d, pfet_106_s, pfet_107_d, pfet_107_s, pfet_108_d,
       pfet_108_s, pfet_109_d, pfet_109_s, pfet_110_d, pfet_110_s, pfet_111_d, pfet_111_s, pfet_112_d,
       pfet_112_s, pfet_113_d, pfet_113_s, pfet_114_d, pfet_114_s, pfet_115_d, pfet_115_s, pfet_116_d,
       pfet_116_s, pfet_117_d, pfet_117_s, pfet_118_d, pfet_118_s, pfet_119_d, pfet_119_s, pfet_120_d,
       pfet_120_s, pfet_137_d, pfet_137_s, pfet_138_d, pfet_138_s, pfet_141_d, pfet_141_s, pfet_143_d,
       pfet_143_s, pfet_145_d, pfet_145_s, pfet_147_d, pfet_147_s, pfet_149_d, pfet_149_s, pfet_151_d,
       pfet_151_s, pfet_153_d, pfet_153_s, pfet_155_d, pfet_155_s, pfet_157_d, pfet_157_s, pfet_159_d,
       pfet_159_s, pfet_161_d, pfet_161_s, pfet_163_d, pfet_163_s, pfet_165_d, pfet_165_s, pfet_167_d,
       pfet_167_s, pfet_169_s, pfet_170_s, pfet_171_s, pfet_172_s, pfet_173_s, pfet_174_s, pfet_175_s,
       pfet_176_s, pfet_177_s, pfet_178_s, pfet_179_s, pfet_180_s, pfet_181_s, pfet_182_s, pfet_183_s,
       pfet_184_s;

  PFET #(.unidirectional("true")) pfet_1 (.G(sel[3]), .S(pfet_1_s), .D(pfet_1_d));
  PullUp pullup_1 (.out(pfet_1_s));
  PFET #(.unidirectional("true")) pfet_2 (.G(sel[3]), .S(pfet_1_s), .D(pfet_1_d));
  NFET #(.unidirectional("true")) nfet_1 (.G(sel[3]), .D(pfet_1_d), .S(nfet_1_s));
  NFET #(.unidirectional("true")) nfet_2 (.G(sel[3]), .D(nfet_1_s), .S(1'b0));
  PFET #(.unidirectional("true")) pfet_3 (.G(sel[2]), .S(pfet_3_s), .D(pfet_3_d));
  PullUp pullup_2 (.out(pfet_3_s));
  PFET #(.unidirectional("true")) pfet_4 (.G(sel[2]), .S(pfet_3_s), .D(pfet_3_d));
  NFET #(.unidirectional("true")) nfet_3 (.G(sel[2]), .D(pfet_3_d), .S(nfet_3_s));
  NFET #(.unidirectional("true")) nfet_4 (.G(sel[2]), .D(nfet_3_s), .S(1'b0));
  PFET #(.unidirectional("true")) pfet_5 (.G(sel[1]), .S(pfet_5_s), .D(pfet_5_d));
  PFET #(.unidirectional("true")) pfet_6 (.G(sel[1]), .S(pfet_5_s), .D(pfet_5_d));
  NFET #(.unidirectional("true")) nfet_5 (.G(sel[1]), .D(pfet_5_d), .S(nfet_5_s));
  NFET #(.unidirectional("true")) nfet_6 (.G(sel[1]), .D(nfet_5_s), .S(1'b0));
  PullUp pullup_3 (.out(pfet_5_s));
  PFET #(.unidirectional("true")) pfet_7 (.G(sel[0]), .S(pfet_7_s), .D(pfet_7_d));
  PullUp pullup_4 (.out(pfet_7_s));
  PFET #(.unidirectional("true")) pfet_8 (.G(sel[0]), .S(pfet_7_s), .D(pfet_7_d));
  NFET #(.unidirectional("true")) nfet_7 (.G(sel[0]), .D(pfet_7_d), .S(nfet_7_s));
  NFET #(.unidirectional("true")) nfet_8 (.G(sel[0]), .D(nfet_7_s), .S(1'b0));
  PFET #(.unidirectional("true")) pfet_9 (.G(sel[0]), .S(pfet_9_s), .D(pfet_9_d));
  PFET #(.unidirectional("true")) pfet_10 (.G(pfet_7_d), .S(pfet_10_s), .D(pfet_10_d));
  PFET #(.unidirectional("true")) pfet_11 (.G(sel[0]), .S(pfet_11_s), .D(pfet_11_d));
  PFET #(.unidirectional("true")) pfet_12 (.G(pfet_7_d), .S(pfet_12_s), .D(pfet_12_d));
  PFET #(.unidirectional("true")) pfet_13 (.G(sel[0]), .S(pfet_13_s), .D(pfet_13_d));
  PFET #(.unidirectional("true")) pfet_14 (.G(pfet_7_d), .S(pfet_14_s), .D(pfet_14_d));
  PFET #(.unidirectional("true")) pfet_15 (.G(sel[0]), .S(pfet_15_s), .D(pfet_15_d));
  PFET #(.unidirectional("true")) pfet_16 (.G(pfet_7_d), .S(pfet_16_s), .D(pfet_16_d));
  PFET #(.unidirectional("true")) pfet_17 (.G(sel[0]), .S(pfet_17_s), .D(pfet_17_d));
  PFET #(.unidirectional("true")) pfet_18 (.G(pfet_7_d), .S(pfet_18_s), .D(pfet_18_d));
  PFET #(.unidirectional("true")) pfet_19 (.G(sel[0]), .S(pfet_19_s), .D(pfet_19_d));
  PFET #(.unidirectional("true")) pfet_20 (.G(pfet_7_d), .S(pfet_20_s), .D(pfet_20_d));
  PFET #(.unidirectional("true")) pfet_21 (.G(sel[0]), .S(pfet_21_s), .D(pfet_21_d));
  PFET #(.unidirectional("true")) pfet_22 (.G(pfet_7_d), .S(pfet_22_s), .D(pfet_22_d));
  PFET #(.unidirectional("true")) pfet_23 (.G(sel[0]), .S(pfet_23_s), .D(pfet_23_d));
  PFET #(.unidirectional("true")) pfet_24 (.G(pfet_7_d), .S(pfet_24_s), .D(pfet_24_d));
  PullUp pullup_5 (.out(pfet_9_s));
  PFET #(.unidirectional("true")) pfet_25 (.G(sel[1]), .S(pfet_9_s), .D(pfet_9_d));
  NFET #(.unidirectional("true")) nfet_9 (.G(sel[0]), .D(pfet_9_d), .S(nfet_9_s));
  NFET #(.unidirectional("true")) nfet_10 (.G(sel[1]), .D(nfet_9_s), .S(1'b0));
  PullUp pullup_6 (.out(pfet_10_s));
  PFET #(.unidirectional("true")) pfet_26 (.G(sel[1]), .S(pfet_10_s), .D(pfet_10_d));
  NFET #(.unidirectional("true")) nfet_11 (.G(pfet_7_d), .D(pfet_10_d), .S(nfet_11_s));
  NFET #(.unidirectional("true")) nfet_12 (.G(sel[1]), .D(nfet_11_s), .S(1'b0));
  PullUp pullup_7 (.out(pfet_11_s));
  PFET #(.unidirectional("true")) pfet_27 (.G(pfet_5_d), .S(pfet_11_s), .D(pfet_11_d));
  NFET #(.unidirectional("true")) nfet_13 (.G(sel[0]), .D(pfet_11_d), .S(nfet_13_s));
  NFET #(.unidirectional("true")) nfet_14 (.G(pfet_5_d), .D(nfet_13_s), .S(1'b0));
  PullUp pullup_8 (.out(pfet_12_s));
  PFET #(.unidirectional("true")) pfet_28 (.G(pfet_5_d), .S(pfet_12_s), .D(pfet_12_d));
  NFET #(.unidirectional("true")) nfet_15 (.G(pfet_7_d), .D(pfet_12_d), .S(nfet_15_s));
  NFET #(.unidirectional("true")) nfet_16 (.G(pfet_5_d), .D(nfet_15_s), .S(1'b0));
  PullUp pullup_9 (.out(pfet_13_s));
  PFET #(.unidirectional("true")) pfet_29 (.G(sel[1]), .S(pfet_13_s), .D(pfet_13_d));
  NFET #(.unidirectional("true")) nfet_17 (.G(sel[0]), .D(pfet_13_d), .S(nfet_17_s));
  NFET #(.unidirectional("true")) nfet_18 (.G(sel[1]), .D(nfet_17_s), .S(1'b0));
  PullUp pullup_10 (.out(pfet_14_s));
  PFET #(.unidirectional("true")) pfet_30 (.G(sel[1]), .S(pfet_14_s), .D(pfet_14_d));
  NFET #(.unidirectional("true")) nfet_19 (.G(pfet_7_d), .D(pfet_14_d), .S(nfet_19_s));
  NFET #(.unidirectional("true")) nfet_20 (.G(sel[1]), .D(nfet_19_s), .S(1'b0));
  PullUp pullup_11 (.out(pfet_15_s));
  PFET #(.unidirectional("true")) pfet_31 (.G(pfet_5_d), .S(pfet_15_s), .D(pfet_15_d));
  NFET #(.unidirectional("true")) nfet_21 (.G(sel[0]), .D(pfet_15_d), .S(nfet_21_s));
  NFET #(.unidirectional("true")) nfet_22 (.G(pfet_5_d), .D(nfet_21_s), .S(1'b0));
  PullUp pullup_12 (.out(pfet_16_s));
  PFET #(.unidirectional("true")) pfet_32 (.G(pfet_5_d), .S(pfet_16_s), .D(pfet_16_d));
  NFET #(.unidirectional("true")) nfet_23 (.G(pfet_7_d), .D(pfet_16_d), .S(nfet_23_s));
  NFET #(.unidirectional("true")) nfet_24 (.G(pfet_5_d), .D(nfet_23_s), .S(1'b0));
  PullUp pullup_13 (.out(pfet_17_s));
  PFET #(.unidirectional("true")) pfet_33 (.G(sel[1]), .S(pfet_17_s), .D(pfet_17_d));
  NFET #(.unidirectional("true")) nfet_25 (.G(sel[0]), .D(pfet_17_d), .S(nfet_25_s));
  NFET #(.unidirectional("true")) nfet_26 (.G(sel[1]), .D(nfet_25_s), .S(1'b0));
  PullUp pullup_14 (.out(pfet_18_s));
  PFET #(.unidirectional("true")) pfet_34 (.G(sel[1]), .S(pfet_18_s), .D(pfet_18_d));
  NFET #(.unidirectional("true")) nfet_27 (.G(pfet_7_d), .D(pfet_18_d), .S(nfet_27_s));
  NFET #(.unidirectional("true")) nfet_28 (.G(sel[1]), .D(nfet_27_s), .S(1'b0));
  PullUp pullup_15 (.out(pfet_19_s));
  PFET #(.unidirectional("true")) pfet_35 (.G(pfet_5_d), .S(pfet_19_s), .D(pfet_19_d));
  NFET #(.unidirectional("true")) nfet_29 (.G(sel[0]), .D(pfet_19_d), .S(nfet_29_s));
  NFET #(.unidirectional("true")) nfet_30 (.G(pfet_5_d), .D(nfet_29_s), .S(1'b0));
  PullUp pullup_16 (.out(pfet_20_s));
  PFET #(.unidirectional("true")) pfet_36 (.G(pfet_5_d), .S(pfet_20_s), .D(pfet_20_d));
  NFET #(.unidirectional("true")) nfet_31 (.G(pfet_7_d), .D(pfet_20_d), .S(nfet_31_s));
  NFET #(.unidirectional("true")) nfet_32 (.G(pfet_5_d), .D(nfet_31_s), .S(1'b0));
  PullUp pullup_17 (.out(pfet_21_s));
  PFET #(.unidirectional("true")) pfet_37 (.G(sel[1]), .S(pfet_21_s), .D(pfet_21_d));
  NFET #(.unidirectional("true")) nfet_33 (.G(sel[0]), .D(pfet_21_d), .S(nfet_33_s));
  NFET #(.unidirectional("true")) nfet_34 (.G(sel[1]), .D(nfet_33_s), .S(1'b0));
  PullUp pullup_18 (.out(pfet_22_s));
  PFET #(.unidirectional("true")) pfet_38 (.G(sel[1]), .S(pfet_22_s), .D(pfet_22_d));
  NFET #(.unidirectional("true")) nfet_35 (.G(pfet_7_d), .D(pfet_22_d), .S(nfet_35_s));
  NFET #(.unidirectional("true")) nfet_36 (.G(sel[1]), .D(nfet_35_s), .S(1'b0));
  PullUp pullup_19 (.out(pfet_23_s));
  PFET #(.unidirectional("true")) pfet_39 (.G(pfet_5_d), .S(pfet_23_s), .D(pfet_23_d));
  NFET #(.unidirectional("true")) nfet_37 (.G(sel[0]), .D(pfet_23_d), .S(nfet_37_s));
  NFET #(.unidirectional("true")) nfet_38 (.G(pfet_5_d), .D(nfet_37_s), .S(1'b0));
  PullUp pullup_20 (.out(pfet_24_s));
  PFET #(.unidirectional("true")) pfet_40 (.G(pfet_5_d), .S(pfet_24_s), .D(pfet_24_d));
  NFET #(.unidirectional("true")) nfet_39 (.G(pfet_7_d), .D(pfet_24_d), .S(nfet_39_s));
  NFET #(.unidirectional("true")) nfet_40 (.G(pfet_5_d), .D(nfet_39_s), .S(1'b0));
  PFET #(.unidirectional("true")) pfet_41 (.G(pfet_9_d), .S(pfet_41_s), .D(pfet_41_d));
  PFET #(.unidirectional("true")) pfet_42 (.G(pfet_9_d), .S(pfet_41_s), .D(pfet_41_d));
  NFET #(.unidirectional("true")) nfet_41 (.G(pfet_9_d), .D(pfet_41_d), .S(nfet_41_s));
  NFET #(.unidirectional("true")) nfet_42 (.G(pfet_9_d), .D(nfet_41_s), .S(1'b0));
  PFET #(.unidirectional("true")) pfet_43 (.G(pfet_10_d), .S(pfet_43_s), .D(pfet_43_d));
  PFET #(.unidirectional("true")) pfet_44 (.G(pfet_10_d), .S(pfet_43_s), .D(pfet_43_d));
  NFET #(.unidirectional("true")) nfet_43 (.G(pfet_10_d), .D(pfet_43_d), .S(nfet_43_s));
  NFET #(.unidirectional("true")) nfet_44 (.G(pfet_10_d), .D(nfet_43_s), .S(1'b0));
  PFET #(.unidirectional("true")) pfet_45 (.G(pfet_11_d), .S(pfet_45_s), .D(pfet_45_d));
  PFET #(.unidirectional("true")) pfet_46 (.G(pfet_12_d), .S(pfet_46_s), .D(pfet_46_d));
  PFET #(.unidirectional("true")) pfet_47 (.G(pfet_13_d), .S(pfet_47_s), .D(pfet_47_d));
  PFET #(.unidirectional("true")) pfet_48 (.G(pfet_14_d), .S(pfet_48_s), .D(pfet_48_d));
  PFET #(.unidirectional("true")) pfet_49 (.G(pfet_15_d), .S(pfet_49_s), .D(pfet_49_d));
  PFET #(.unidirectional("true")) pfet_50 (.G(pfet_16_d), .S(pfet_50_s), .D(pfet_50_d));
  PFET #(.unidirectional("true")) pfet_51 (.G(pfet_17_d), .S(pfet_51_s), .D(pfet_51_d));
  PFET #(.unidirectional("true")) pfet_52 (.G(pfet_18_d), .S(pfet_52_s), .D(pfet_52_d));
  PFET #(.unidirectional("true")) pfet_53 (.G(pfet_19_d), .S(pfet_53_s), .D(pfet_53_d));
  PFET #(.unidirectional("true")) pfet_54 (.G(pfet_20_d), .S(pfet_54_s), .D(pfet_54_d));
  PFET #(.unidirectional("true")) pfet_55 (.G(pfet_21_d), .S(pfet_55_s), .D(pfet_55_d));
  PFET #(.unidirectional("true")) pfet_56 (.G(pfet_22_d), .S(pfet_56_s), .D(pfet_56_d));
  PFET #(.unidirectional("true")) pfet_57 (.G(pfet_23_d), .S(pfet_57_s), .D(pfet_57_d));
  PFET #(.unidirectional("true")) pfet_58 (.G(pfet_24_d), .S(pfet_58_s), .D(pfet_58_d));
  PullUp pullup_21 (.out(pfet_41_s));
  PullUp pullup_22 (.out(pfet_43_s));
  PullUp pullup_23 (.out(pfet_45_s));
  PFET #(.unidirectional("true")) pfet_59 (.G(pfet_11_d), .S(pfet_45_s), .D(pfet_45_d));
  NFET #(.unidirectional("true")) nfet_45 (.G(pfet_11_d), .D(pfet_45_d), .S(nfet_45_s));
  NFET #(.unidirectional("true")) nfet_46 (.G(pfet_11_d), .D(nfet_45_s), .S(1'b0));
  PullUp pullup_24 (.out(pfet_46_s));
  PFET #(.unidirectional("true")) pfet_60 (.G(pfet_12_d), .S(pfet_46_s), .D(pfet_46_d));
  NFET #(.unidirectional("true")) nfet_47 (.G(pfet_12_d), .D(pfet_46_d), .S(nfet_47_s));
  NFET #(.unidirectional("true")) nfet_48 (.G(pfet_12_d), .D(nfet_47_s), .S(1'b0));
  PullUp pullup_25 (.out(pfet_47_s));
  PFET #(.unidirectional("true")) pfet_61 (.G(pfet_13_d), .S(pfet_47_s), .D(pfet_47_d));
  NFET #(.unidirectional("true")) nfet_49 (.G(pfet_13_d), .D(pfet_47_d), .S(nfet_49_s));
  NFET #(.unidirectional("true")) nfet_50 (.G(pfet_13_d), .D(nfet_49_s), .S(1'b0));
  PullUp pullup_26 (.out(pfet_48_s));
  PFET #(.unidirectional("true")) pfet_62 (.G(pfet_14_d), .S(pfet_48_s), .D(pfet_48_d));
  NFET #(.unidirectional("true")) nfet_51 (.G(pfet_14_d), .D(pfet_48_d), .S(nfet_51_s));
  NFET #(.unidirectional("true")) nfet_52 (.G(pfet_14_d), .D(nfet_51_s), .S(1'b0));
  PullUp pullup_27 (.out(pfet_49_s));
  PFET #(.unidirectional("true")) pfet_63 (.G(pfet_15_d), .S(pfet_49_s), .D(pfet_49_d));
  NFET #(.unidirectional("true")) nfet_53 (.G(pfet_15_d), .D(pfet_49_d), .S(nfet_53_s));
  NFET #(.unidirectional("true")) nfet_54 (.G(pfet_15_d), .D(nfet_53_s), .S(1'b0));
  PullUp pullup_28 (.out(pfet_50_s));
  PFET #(.unidirectional("true")) pfet_64 (.G(pfet_16_d), .S(pfet_50_s), .D(pfet_50_d));
  NFET #(.unidirectional("true")) nfet_55 (.G(pfet_16_d), .D(pfet_50_d), .S(nfet_55_s));
  NFET #(.unidirectional("true")) nfet_56 (.G(pfet_16_d), .D(nfet_55_s), .S(1'b0));
  PullUp pullup_29 (.out(pfet_51_s));
  PFET #(.unidirectional("true")) pfet_65 (.G(pfet_17_d), .S(pfet_51_s), .D(pfet_51_d));
  NFET #(.unidirectional("true")) nfet_57 (.G(pfet_17_d), .D(pfet_51_d), .S(nfet_57_s));
  NFET #(.unidirectional("true")) nfet_58 (.G(pfet_17_d), .D(nfet_57_s), .S(1'b0));
  PullUp pullup_30 (.out(pfet_52_s));
  PFET #(.unidirectional("true")) pfet_66 (.G(pfet_18_d), .S(pfet_52_s), .D(pfet_52_d));
  NFET #(.unidirectional("true")) nfet_59 (.G(pfet_18_d), .D(pfet_52_d), .S(nfet_59_s));
  NFET #(.unidirectional("true")) nfet_60 (.G(pfet_18_d), .D(nfet_59_s), .S(1'b0));
  PullUp pullup_31 (.out(pfet_53_s));
  PFET #(.unidirectional("true")) pfet_67 (.G(pfet_19_d), .S(pfet_53_s), .D(pfet_53_d));
  NFET #(.unidirectional("true")) nfet_61 (.G(pfet_19_d), .D(pfet_53_d), .S(nfet_61_s));
  NFET #(.unidirectional("true")) nfet_62 (.G(pfet_19_d), .D(nfet_61_s), .S(1'b0));
  PullUp pullup_32 (.out(pfet_54_s));
  PFET #(.unidirectional("true")) pfet_68 (.G(pfet_20_d), .S(pfet_54_s), .D(pfet_54_d));
  NFET #(.unidirectional("true")) nfet_63 (.G(pfet_20_d), .D(pfet_54_d), .S(nfet_63_s));
  NFET #(.unidirectional("true")) nfet_64 (.G(pfet_20_d), .D(nfet_63_s), .S(1'b0));
  PullUp pullup_33 (.out(pfet_55_s));
  PFET #(.unidirectional("true")) pfet_69 (.G(pfet_21_d), .S(pfet_55_s), .D(pfet_55_d));
  NFET #(.unidirectional("true")) nfet_65 (.G(pfet_21_d), .D(pfet_55_d), .S(nfet_65_s));
  NFET #(.unidirectional("true")) nfet_66 (.G(pfet_21_d), .D(nfet_65_s), .S(1'b0));
  PullUp pullup_34 (.out(pfet_56_s));
  PFET #(.unidirectional("true")) pfet_70 (.G(pfet_22_d), .S(pfet_56_s), .D(pfet_56_d));
  NFET #(.unidirectional("true")) nfet_67 (.G(pfet_22_d), .D(pfet_56_d), .S(nfet_67_s));
  NFET #(.unidirectional("true")) nfet_68 (.G(pfet_22_d), .D(nfet_67_s), .S(1'b0));
  PullUp pullup_35 (.out(pfet_57_s));
  PFET #(.unidirectional("true")) pfet_71 (.G(pfet_23_d), .S(pfet_57_s), .D(pfet_57_d));
  NFET #(.unidirectional("true")) nfet_69 (.G(pfet_23_d), .D(pfet_57_d), .S(nfet_69_s));
  NFET #(.unidirectional("true")) nfet_70 (.G(pfet_23_d), .D(nfet_69_s), .S(1'b0));
  PullUp pullup_36 (.out(pfet_58_s));
  PFET #(.unidirectional("true")) pfet_72 (.G(pfet_24_d), .S(pfet_58_s), .D(pfet_58_d));
  NFET #(.unidirectional("true")) nfet_71 (.G(pfet_24_d), .D(pfet_58_d), .S(nfet_71_s));
  NFET #(.unidirectional("true")) nfet_72 (.G(pfet_24_d), .D(nfet_71_s), .S(1'b0));
  PFET #(.unidirectional("true")) pfet_73 (.G(pfet_41_d), .S(pfet_73_s), .D(pfet_73_d));
  PFET #(.unidirectional("true")) pfet_74 (.G(pfet_43_d), .S(pfet_74_s), .D(pfet_74_d));
  PFET #(.unidirectional("true")) pfet_75 (.G(pfet_45_d), .S(pfet_75_s), .D(pfet_75_d));
  PFET #(.unidirectional("true")) pfet_76 (.G(pfet_46_d), .S(pfet_76_s), .D(pfet_76_d));
  PFET #(.unidirectional("true")) pfet_77 (.G(pfet_47_d), .S(pfet_77_s), .D(pfet_77_d));
  PFET #(.unidirectional("true")) pfet_78 (.G(pfet_48_d), .S(pfet_78_s), .D(pfet_78_d));
  PFET #(.unidirectional("true")) pfet_79 (.G(pfet_49_d), .S(pfet_79_s), .D(pfet_79_d));
  PFET #(.unidirectional("true")) pfet_80 (.G(pfet_50_d), .S(pfet_80_s), .D(pfet_80_d));
  PFET #(.unidirectional("true")) pfet_81 (.G(pfet_51_d), .S(pfet_81_s), .D(pfet_81_d));
  PFET #(.unidirectional("true")) pfet_82 (.G(pfet_52_d), .S(pfet_82_s), .D(pfet_82_d));
  PFET #(.unidirectional("true")) pfet_83 (.G(pfet_53_d), .S(pfet_83_s), .D(pfet_83_d));
  PFET #(.unidirectional("true")) pfet_84 (.G(pfet_54_d), .S(pfet_84_s), .D(pfet_84_d));
  PFET #(.unidirectional("true")) pfet_85 (.G(pfet_55_d), .S(pfet_85_s), .D(pfet_85_d));
  PFET #(.unidirectional("true")) pfet_86 (.G(pfet_56_d), .S(pfet_86_s), .D(pfet_86_d));
  PFET #(.unidirectional("true")) pfet_87 (.G(pfet_57_d), .S(pfet_87_s), .D(pfet_87_d));
  PFET #(.unidirectional("true")) pfet_88 (.G(pfet_58_d), .S(pfet_88_s), .D(pfet_88_d));
  PullUp pullup_37 (.out(pfet_73_s));
  PFET #(.unidirectional("true")) pfet_89 (.G(sel[2]), .S(pfet_73_s), .D(pfet_73_d));
  NFET #(.unidirectional("true")) nfet_73 (.G(pfet_41_d), .D(pfet_73_d), .S(nfet_73_s));
  NFET #(.unidirectional("true")) nfet_74 (.G(sel[2]), .D(nfet_73_s), .S(1'b0));
  PullUp pullup_38 (.out(pfet_74_s));
  PFET #(.unidirectional("true")) pfet_90 (.G(sel[2]), .S(pfet_74_s), .D(pfet_74_d));
  NFET #(.unidirectional("true")) nfet_75 (.G(pfet_43_d), .D(pfet_74_d), .S(nfet_75_s));
  NFET #(.unidirectional("true")) nfet_76 (.G(sel[2]), .D(nfet_75_s), .S(1'b0));
  PullUp pullup_39 (.out(pfet_75_s));
  PFET #(.unidirectional("true")) pfet_91 (.G(sel[2]), .S(pfet_75_s), .D(pfet_75_d));
  NFET #(.unidirectional("true")) nfet_77 (.G(pfet_45_d), .D(pfet_75_d), .S(nfet_77_s));
  NFET #(.unidirectional("true")) nfet_78 (.G(sel[2]), .D(nfet_77_s), .S(1'b0));
  PullUp pullup_40 (.out(pfet_76_s));
  PFET #(.unidirectional("true")) pfet_92 (.G(sel[2]), .S(pfet_76_s), .D(pfet_76_d));
  NFET #(.unidirectional("true")) nfet_79 (.G(pfet_46_d), .D(pfet_76_d), .S(nfet_79_s));
  NFET #(.unidirectional("true")) nfet_80 (.G(sel[2]), .D(nfet_79_s), .S(1'b0));
  PullUp pullup_41 (.out(pfet_77_s));
  PFET #(.unidirectional("true")) pfet_93 (.G(pfet_3_d), .S(pfet_77_s), .D(pfet_77_d));
  NFET #(.unidirectional("true")) nfet_81 (.G(pfet_47_d), .D(pfet_77_d), .S(nfet_81_s));
  NFET #(.unidirectional("true")) nfet_82 (.G(pfet_3_d), .D(nfet_81_s), .S(1'b0));
  PullUp pullup_42 (.out(pfet_78_s));
  PFET #(.unidirectional("true")) pfet_94 (.G(pfet_3_d), .S(pfet_78_s), .D(pfet_78_d));
  NFET #(.unidirectional("true")) nfet_83 (.G(pfet_48_d), .D(pfet_78_d), .S(nfet_83_s));
  NFET #(.unidirectional("true")) nfet_84 (.G(pfet_3_d), .D(nfet_83_s), .S(1'b0));
  PullUp pullup_43 (.out(pfet_79_s));
  PFET #(.unidirectional("true")) pfet_95 (.G(pfet_3_d), .S(pfet_79_s), .D(pfet_79_d));
  NFET #(.unidirectional("true")) nfet_85 (.G(pfet_49_d), .D(pfet_79_d), .S(nfet_85_s));
  NFET #(.unidirectional("true")) nfet_86 (.G(pfet_3_d), .D(nfet_85_s), .S(1'b0));
  PullUp pullup_44 (.out(pfet_80_s));
  PFET #(.unidirectional("true")) pfet_96 (.G(pfet_3_d), .S(pfet_80_s), .D(pfet_80_d));
  NFET #(.unidirectional("true")) nfet_87 (.G(pfet_50_d), .D(pfet_80_d), .S(nfet_87_s));
  NFET #(.unidirectional("true")) nfet_88 (.G(pfet_3_d), .D(nfet_87_s), .S(1'b0));
  PullUp pullup_45 (.out(pfet_81_s));
  PFET #(.unidirectional("true")) pfet_97 (.G(sel[2]), .S(pfet_81_s), .D(pfet_81_d));
  NFET #(.unidirectional("true")) nfet_89 (.G(pfet_51_d), .D(pfet_81_d), .S(nfet_89_s));
  NFET #(.unidirectional("true")) nfet_90 (.G(sel[2]), .D(nfet_89_s), .S(1'b0));
  PullUp pullup_46 (.out(pfet_82_s));
  PFET #(.unidirectional("true")) pfet_98 (.G(sel[2]), .S(pfet_82_s), .D(pfet_82_d));
  NFET #(.unidirectional("true")) nfet_91 (.G(pfet_52_d), .D(pfet_82_d), .S(nfet_91_s));
  NFET #(.unidirectional("true")) nfet_92 (.G(sel[2]), .D(nfet_91_s), .S(1'b0));
  PullUp pullup_47 (.out(pfet_83_s));
  PFET #(.unidirectional("true")) pfet_99 (.G(sel[2]), .S(pfet_83_s), .D(pfet_83_d));
  NFET #(.unidirectional("true")) nfet_93 (.G(pfet_53_d), .D(pfet_83_d), .S(nfet_93_s));
  NFET #(.unidirectional("true")) nfet_94 (.G(sel[2]), .D(nfet_93_s), .S(1'b0));
  PullUp pullup_48 (.out(pfet_84_s));
  PFET #(.unidirectional("true")) pfet_100 (.G(sel[2]), .S(pfet_84_s), .D(pfet_84_d));
  NFET #(.unidirectional("true")) nfet_95 (.G(pfet_54_d), .D(pfet_84_d), .S(nfet_95_s));
  NFET #(.unidirectional("true")) nfet_96 (.G(sel[2]), .D(nfet_95_s), .S(1'b0));
  PullUp pullup_49 (.out(pfet_85_s));
  PFET #(.unidirectional("true")) pfet_101 (.G(pfet_3_d), .S(pfet_85_s), .D(pfet_85_d));
  NFET #(.unidirectional("true")) nfet_97 (.G(pfet_55_d), .D(pfet_85_d), .S(nfet_97_s));
  NFET #(.unidirectional("true")) nfet_98 (.G(pfet_3_d), .D(nfet_97_s), .S(1'b0));
  PullUp pullup_50 (.out(pfet_86_s));
  PFET #(.unidirectional("true")) pfet_102 (.G(pfet_3_d), .S(pfet_86_s), .D(pfet_86_d));
  NFET #(.unidirectional("true")) nfet_99 (.G(pfet_56_d), .D(pfet_86_d), .S(nfet_99_s));
  NFET #(.unidirectional("true")) nfet_100 (.G(pfet_3_d), .D(nfet_99_s), .S(1'b0));
  PullUp pullup_51 (.out(pfet_87_s));
  PFET #(.unidirectional("true")) pfet_103 (.G(pfet_3_d), .S(pfet_87_s), .D(pfet_87_d));
  NFET #(.unidirectional("true")) nfet_101 (.G(pfet_57_d), .D(pfet_87_d), .S(nfet_101_s));
  NFET #(.unidirectional("true")) nfet_102 (.G(pfet_3_d), .D(nfet_101_s), .S(1'b0));
  PullUp pullup_52 (.out(pfet_88_s));
  PFET #(.unidirectional("true")) pfet_104 (.G(pfet_3_d), .S(pfet_88_s), .D(pfet_88_d));
  NFET #(.unidirectional("true")) nfet_103 (.G(pfet_58_d), .D(pfet_88_d), .S(nfet_103_s));
  NFET #(.unidirectional("true")) nfet_104 (.G(pfet_3_d), .D(nfet_103_s), .S(1'b0));
  PFET #(.unidirectional("true")) pfet_105 (.G(pfet_73_d), .S(pfet_105_s), .D(pfet_105_d));
  PFET #(.unidirectional("true")) pfet_106 (.G(pfet_74_d), .S(pfet_106_s), .D(pfet_106_d));
  PFET #(.unidirectional("true")) pfet_107 (.G(pfet_75_d), .S(pfet_107_s), .D(pfet_107_d));
  PFET #(.unidirectional("true")) pfet_108 (.G(pfet_76_d), .S(pfet_108_s), .D(pfet_108_d));
  PFET #(.unidirectional("true")) pfet_109 (.G(pfet_77_d), .S(pfet_109_s), .D(pfet_109_d));
  PFET #(.unidirectional("true")) pfet_110 (.G(pfet_78_d), .S(pfet_110_s), .D(pfet_110_d));
  PFET #(.unidirectional("true")) pfet_111 (.G(pfet_79_d), .S(pfet_111_s), .D(pfet_111_d));
  PFET #(.unidirectional("true")) pfet_112 (.G(pfet_80_d), .S(pfet_112_s), .D(pfet_112_d));
  PFET #(.unidirectional("true")) pfet_113 (.G(pfet_81_d), .S(pfet_113_s), .D(pfet_113_d));
  PFET #(.unidirectional("true")) pfet_114 (.G(pfet_82_d), .S(pfet_114_s), .D(pfet_114_d));
  PFET #(.unidirectional("true")) pfet_115 (.G(pfet_83_d), .S(pfet_115_s), .D(pfet_115_d));
  PFET #(.unidirectional("true")) pfet_116 (.G(pfet_84_d), .S(pfet_116_s), .D(pfet_116_d));
  PFET #(.unidirectional("true")) pfet_117 (.G(pfet_85_d), .S(pfet_117_s), .D(pfet_117_d));
  PFET #(.unidirectional("true")) pfet_118 (.G(pfet_86_d), .S(pfet_118_s), .D(pfet_118_d));
  PFET #(.unidirectional("true")) pfet_119 (.G(pfet_87_d), .S(pfet_119_s), .D(pfet_119_d));
  PFET #(.unidirectional("true")) pfet_120 (.G(pfet_88_d), .S(pfet_120_s), .D(pfet_120_d));
  PullUp pullup_53 (.out(pfet_105_s));
  PFET #(.unidirectional("true")) pfet_121 (.G(pfet_73_d), .S(pfet_105_s), .D(pfet_105_d));
  NFET #(.unidirectional("true")) nfet_105 (.G(pfet_73_d), .D(pfet_105_d), .S(nfet_105_s));
  NFET #(.unidirectional("true")) nfet_106 (.G(pfet_73_d), .D(nfet_105_s), .S(1'b0));
  PullUp pullup_54 (.out(pfet_106_s));
  PFET #(.unidirectional("true")) pfet_122 (.G(pfet_74_d), .S(pfet_106_s), .D(pfet_106_d));
  NFET #(.unidirectional("true")) nfet_107 (.G(pfet_74_d), .D(pfet_106_d), .S(nfet_107_s));
  NFET #(.unidirectional("true")) nfet_108 (.G(pfet_74_d), .D(nfet_107_s), .S(1'b0));
  PullUp pullup_55 (.out(pfet_107_s));
  PFET #(.unidirectional("true")) pfet_123 (.G(pfet_75_d), .S(pfet_107_s), .D(pfet_107_d));
  NFET #(.unidirectional("true")) nfet_109 (.G(pfet_75_d), .D(pfet_107_d), .S(nfet_109_s));
  NFET #(.unidirectional("true")) nfet_110 (.G(pfet_75_d), .D(nfet_109_s), .S(1'b0));
  PullUp pullup_56 (.out(pfet_108_s));
  PFET #(.unidirectional("true")) pfet_124 (.G(pfet_76_d), .S(pfet_108_s), .D(pfet_108_d));
  NFET #(.unidirectional("true")) nfet_111 (.G(pfet_76_d), .D(pfet_108_d), .S(nfet_111_s));
  NFET #(.unidirectional("true")) nfet_112 (.G(pfet_76_d), .D(nfet_111_s), .S(1'b0));
  PullUp pullup_57 (.out(pfet_109_s));
  PFET #(.unidirectional("true")) pfet_125 (.G(pfet_77_d), .S(pfet_109_s), .D(pfet_109_d));
  NFET #(.unidirectional("true")) nfet_113 (.G(pfet_77_d), .D(pfet_109_d), .S(nfet_113_s));
  NFET #(.unidirectional("true")) nfet_114 (.G(pfet_77_d), .D(nfet_113_s), .S(1'b0));
  PullUp pullup_58 (.out(pfet_110_s));
  PFET #(.unidirectional("true")) pfet_126 (.G(pfet_78_d), .S(pfet_110_s), .D(pfet_110_d));
  NFET #(.unidirectional("true")) nfet_115 (.G(pfet_78_d), .D(pfet_110_d), .S(nfet_115_s));
  NFET #(.unidirectional("true")) nfet_116 (.G(pfet_78_d), .D(nfet_115_s), .S(1'b0));
  PullUp pullup_59 (.out(pfet_111_s));
  PFET #(.unidirectional("true")) pfet_127 (.G(pfet_79_d), .S(pfet_111_s), .D(pfet_111_d));
  NFET #(.unidirectional("true")) nfet_117 (.G(pfet_79_d), .D(pfet_111_d), .S(nfet_117_s));
  NFET #(.unidirectional("true")) nfet_118 (.G(pfet_79_d), .D(nfet_117_s), .S(1'b0));
  PullUp pullup_60 (.out(pfet_112_s));
  PFET #(.unidirectional("true")) pfet_128 (.G(pfet_80_d), .S(pfet_112_s), .D(pfet_112_d));
  NFET #(.unidirectional("true")) nfet_119 (.G(pfet_80_d), .D(pfet_112_d), .S(nfet_119_s));
  NFET #(.unidirectional("true")) nfet_120 (.G(pfet_80_d), .D(nfet_119_s), .S(1'b0));
  PullUp pullup_61 (.out(pfet_113_s));
  PFET #(.unidirectional("true")) pfet_129 (.G(pfet_81_d), .S(pfet_113_s), .D(pfet_113_d));
  NFET #(.unidirectional("true")) nfet_121 (.G(pfet_81_d), .D(pfet_113_d), .S(nfet_121_s));
  NFET #(.unidirectional("true")) nfet_122 (.G(pfet_81_d), .D(nfet_121_s), .S(1'b0));
  PullUp pullup_62 (.out(pfet_114_s));
  PFET #(.unidirectional("true")) pfet_130 (.G(pfet_82_d), .S(pfet_114_s), .D(pfet_114_d));
  NFET #(.unidirectional("true")) nfet_123 (.G(pfet_82_d), .D(pfet_114_d), .S(nfet_123_s));
  NFET #(.unidirectional("true")) nfet_124 (.G(pfet_82_d), .D(nfet_123_s), .S(1'b0));
  PullUp pullup_63 (.out(pfet_115_s));
  PFET #(.unidirectional("true")) pfet_131 (.G(pfet_83_d), .S(pfet_115_s), .D(pfet_115_d));
  NFET #(.unidirectional("true")) nfet_125 (.G(pfet_83_d), .D(pfet_115_d), .S(nfet_125_s));
  NFET #(.unidirectional("true")) nfet_126 (.G(pfet_83_d), .D(nfet_125_s), .S(1'b0));
  PullUp pullup_64 (.out(pfet_116_s));
  PFET #(.unidirectional("true")) pfet_132 (.G(pfet_84_d), .S(pfet_116_s), .D(pfet_116_d));
  NFET #(.unidirectional("true")) nfet_127 (.G(pfet_84_d), .D(pfet_116_d), .S(nfet_127_s));
  NFET #(.unidirectional("true")) nfet_128 (.G(pfet_84_d), .D(nfet_127_s), .S(1'b0));
  PullUp pullup_65 (.out(pfet_117_s));
  PFET #(.unidirectional("true")) pfet_133 (.G(pfet_85_d), .S(pfet_117_s), .D(pfet_117_d));
  NFET #(.unidirectional("true")) nfet_129 (.G(pfet_85_d), .D(pfet_117_d), .S(nfet_129_s));
  NFET #(.unidirectional("true")) nfet_130 (.G(pfet_85_d), .D(nfet_129_s), .S(1'b0));
  PullUp pullup_66 (.out(pfet_118_s));
  PFET #(.unidirectional("true")) pfet_134 (.G(pfet_86_d), .S(pfet_118_s), .D(pfet_118_d));
  NFET #(.unidirectional("true")) nfet_131 (.G(pfet_86_d), .D(pfet_118_d), .S(nfet_131_s));
  NFET #(.unidirectional("true")) nfet_132 (.G(pfet_86_d), .D(nfet_131_s), .S(1'b0));
  PullUp pullup_67 (.out(pfet_119_s));
  PFET #(.unidirectional("true")) pfet_135 (.G(pfet_87_d), .S(pfet_119_s), .D(pfet_119_d));
  NFET #(.unidirectional("true")) nfet_133 (.G(pfet_87_d), .D(pfet_119_d), .S(nfet_133_s));
  NFET #(.unidirectional("true")) nfet_134 (.G(pfet_87_d), .D(nfet_133_s), .S(1'b0));
  PullUp pullup_68 (.out(pfet_120_s));
  PFET #(.unidirectional("true")) pfet_136 (.G(pfet_88_d), .S(pfet_120_s), .D(pfet_120_d));
  NFET #(.unidirectional("true")) nfet_135 (.G(pfet_88_d), .D(pfet_120_d), .S(nfet_135_s));
  NFET #(.unidirectional("true")) nfet_136 (.G(pfet_88_d), .D(nfet_135_s), .S(1'b0));
  PFET #(.unidirectional("true")) pfet_137 (.G(pfet_105_d), .S(pfet_137_s), .D(pfet_137_d));
  PFET #(.unidirectional("true")) pfet_138 (.G(pfet_106_d), .S(pfet_138_s), .D(pfet_138_d));
  PullUp pullup_69 (.out(pfet_137_s));
  PFET #(.unidirectional("true")) pfet_139 (.G(sel[3]), .S(pfet_137_s), .D(pfet_137_d));
  NFET #(.unidirectional("true")) nfet_137 (.G(pfet_105_d), .D(pfet_137_d), .S(nfet_137_s));
  NFET #(.unidirectional("true")) nfet_138 (.G(sel[3]), .D(nfet_137_s), .S(1'b0));
  PullUp pullup_70 (.out(pfet_138_s));
  PFET #(.unidirectional("true")) pfet_140 (.G(sel[3]), .S(pfet_138_s), .D(pfet_138_d));
  NFET #(.unidirectional("true")) nfet_139 (.G(pfet_106_d), .D(pfet_138_d), .S(nfet_139_s));
  NFET #(.unidirectional("true")) nfet_140 (.G(sel[3]), .D(nfet_139_s), .S(1'b0));
  PFET #(.unidirectional("true")) pfet_141 (.G(pfet_107_d), .S(pfet_141_s), .D(pfet_141_d));
  PFET #(.unidirectional("true")) pfet_142 (.G(sel[3]), .S(pfet_141_s), .D(pfet_141_d));
  NFET #(.unidirectional("true")) nfet_141 (.G(pfet_107_d), .D(pfet_141_d), .S(nfet_141_s));
  NFET #(.unidirectional("true")) nfet_142 (.G(sel[3]), .D(nfet_141_s), .S(1'b0));
  PFET #(.unidirectional("true")) pfet_143 (.G(pfet_108_d), .S(pfet_143_s), .D(pfet_143_d));
  PFET #(.unidirectional("true")) pfet_144 (.G(sel[3]), .S(pfet_143_s), .D(pfet_143_d));
  NFET #(.unidirectional("true")) nfet_143 (.G(pfet_108_d), .D(pfet_143_d), .S(nfet_143_s));
  NFET #(.unidirectional("true")) nfet_144 (.G(sel[3]), .D(nfet_143_s), .S(1'b0));
  PFET #(.unidirectional("true")) pfet_145 (.G(pfet_109_d), .S(pfet_145_s), .D(pfet_145_d));
  PFET #(.unidirectional("true")) pfet_146 (.G(sel[3]), .S(pfet_145_s), .D(pfet_145_d));
  NFET #(.unidirectional("true")) nfet_145 (.G(pfet_109_d), .D(pfet_145_d), .S(nfet_145_s));
  NFET #(.unidirectional("true")) nfet_146 (.G(sel[3]), .D(nfet_145_s), .S(1'b0));
  PFET #(.unidirectional("true")) pfet_147 (.G(pfet_110_d), .S(pfet_147_s), .D(pfet_147_d));
  PFET #(.unidirectional("true")) pfet_148 (.G(sel[3]), .S(pfet_147_s), .D(pfet_147_d));
  NFET #(.unidirectional("true")) nfet_147 (.G(pfet_110_d), .D(pfet_147_d), .S(nfet_147_s));
  NFET #(.unidirectional("true")) nfet_148 (.G(sel[3]), .D(nfet_147_s), .S(1'b0));
  PFET #(.unidirectional("true")) pfet_149 (.G(pfet_111_d), .S(pfet_149_s), .D(pfet_149_d));
  PFET #(.unidirectional("true")) pfet_150 (.G(sel[3]), .S(pfet_149_s), .D(pfet_149_d));
  NFET #(.unidirectional("true")) nfet_149 (.G(pfet_111_d), .D(pfet_149_d), .S(nfet_149_s));
  NFET #(.unidirectional("true")) nfet_150 (.G(sel[3]), .D(nfet_149_s), .S(1'b0));
  PFET #(.unidirectional("true")) pfet_151 (.G(pfet_112_d), .S(pfet_151_s), .D(pfet_151_d));
  PFET #(.unidirectional("true")) pfet_152 (.G(sel[3]), .S(pfet_151_s), .D(pfet_151_d));
  NFET #(.unidirectional("true")) nfet_151 (.G(pfet_112_d), .D(pfet_151_d), .S(nfet_151_s));
  NFET #(.unidirectional("true")) nfet_152 (.G(sel[3]), .D(nfet_151_s), .S(1'b0));
  PFET #(.unidirectional("true")) pfet_153 (.G(pfet_113_d), .S(pfet_153_s), .D(pfet_153_d));
  PFET #(.unidirectional("true")) pfet_154 (.G(pfet_1_d), .S(pfet_153_s), .D(pfet_153_d));
  NFET #(.unidirectional("true")) nfet_153 (.G(pfet_113_d), .D(pfet_153_d), .S(nfet_153_s));
  NFET #(.unidirectional("true")) nfet_154 (.G(pfet_1_d), .D(nfet_153_s), .S(1'b0));
  PFET #(.unidirectional("true")) pfet_155 (.G(pfet_114_d), .S(pfet_155_s), .D(pfet_155_d));
  PFET #(.unidirectional("true")) pfet_156 (.G(pfet_1_d), .S(pfet_155_s), .D(pfet_155_d));
  NFET #(.unidirectional("true")) nfet_155 (.G(pfet_114_d), .D(pfet_155_d), .S(nfet_155_s));
  NFET #(.unidirectional("true")) nfet_156 (.G(pfet_1_d), .D(nfet_155_s), .S(1'b0));
  PFET #(.unidirectional("true")) pfet_157 (.G(pfet_115_d), .S(pfet_157_s), .D(pfet_157_d));
  PFET #(.unidirectional("true")) pfet_158 (.G(pfet_1_d), .S(pfet_157_s), .D(pfet_157_d));
  NFET #(.unidirectional("true")) nfet_157 (.G(pfet_115_d), .D(pfet_157_d), .S(nfet_157_s));
  NFET #(.unidirectional("true")) nfet_158 (.G(pfet_1_d), .D(nfet_157_s), .S(1'b0));
  PFET #(.unidirectional("true")) pfet_159 (.G(pfet_116_d), .S(pfet_159_s), .D(pfet_159_d));
  PFET #(.unidirectional("true")) pfet_160 (.G(pfet_1_d), .S(pfet_159_s), .D(pfet_159_d));
  NFET #(.unidirectional("true")) nfet_159 (.G(pfet_116_d), .D(pfet_159_d), .S(nfet_159_s));
  NFET #(.unidirectional("true")) nfet_160 (.G(pfet_1_d), .D(nfet_159_s), .S(1'b0));
  PFET #(.unidirectional("true")) pfet_161 (.G(pfet_117_d), .S(pfet_161_s), .D(pfet_161_d));
  PFET #(.unidirectional("true")) pfet_162 (.G(pfet_1_d), .S(pfet_161_s), .D(pfet_161_d));
  NFET #(.unidirectional("true")) nfet_161 (.G(pfet_117_d), .D(pfet_161_d), .S(nfet_161_s));
  NFET #(.unidirectional("true")) nfet_162 (.G(pfet_1_d), .D(nfet_161_s), .S(1'b0));
  PFET #(.unidirectional("true")) pfet_163 (.G(pfet_118_d), .S(pfet_163_s), .D(pfet_163_d));
  PFET #(.unidirectional("true")) pfet_164 (.G(pfet_1_d), .S(pfet_163_s), .D(pfet_163_d));
  NFET #(.unidirectional("true")) nfet_163 (.G(pfet_118_d), .D(pfet_163_d), .S(nfet_163_s));
  NFET #(.unidirectional("true")) nfet_164 (.G(pfet_1_d), .D(nfet_163_s), .S(1'b0));
  PFET #(.unidirectional("true")) pfet_165 (.G(pfet_119_d), .S(pfet_165_s), .D(pfet_165_d));
  PFET #(.unidirectional("true")) pfet_166 (.G(pfet_1_d), .S(pfet_165_s), .D(pfet_165_d));
  NFET #(.unidirectional("true")) nfet_165 (.G(pfet_119_d), .D(pfet_165_d), .S(nfet_165_s));
  NFET #(.unidirectional("true")) nfet_166 (.G(pfet_1_d), .D(nfet_165_s), .S(1'b0));
  PFET #(.unidirectional("true")) pfet_167 (.G(pfet_120_d), .S(pfet_167_s), .D(pfet_167_d));
  PFET #(.unidirectional("true")) pfet_168 (.G(pfet_1_d), .S(pfet_167_s), .D(pfet_167_d));
  NFET #(.unidirectional("true")) nfet_167 (.G(pfet_120_d), .D(pfet_167_d), .S(nfet_167_s));
  NFET #(.unidirectional("true")) nfet_168 (.G(pfet_1_d), .D(nfet_167_s), .S(1'b0));
  PFET #(.unidirectional("true")) pfet_169 (.G(pfet_137_d), .S(pfet_169_s), .D(_1111));
  PFET #(.unidirectional("true")) pfet_170 (.G(pfet_138_d), .S(pfet_170_s), .D(_1110));
  PullUp pullup_71 (.out(pfet_141_s));
  PFET #(.unidirectional("true")) pfet_171 (.G(pfet_141_d), .S(pfet_171_s), .D(_1101));
  PullUp pullup_72 (.out(pfet_143_s));
  PFET #(.unidirectional("true")) pfet_172 (.G(pfet_143_d), .S(pfet_172_s), .D(_1100));
  PullUp pullup_73 (.out(pfet_145_s));
  PFET #(.unidirectional("true")) pfet_173 (.G(pfet_145_d), .S(pfet_173_s), .D(_1011));
  PullUp pullup_74 (.out(pfet_147_s));
  PFET #(.unidirectional("true")) pfet_174 (.G(pfet_147_d), .S(pfet_174_s), .D(_1010));
  PullUp pullup_75 (.out(pfet_149_s));
  PFET #(.unidirectional("true")) pfet_175 (.G(pfet_149_d), .S(pfet_175_s), .D(_1001));
  PullUp pullup_76 (.out(pfet_151_s));
  PFET #(.unidirectional("true")) pfet_176 (.G(pfet_151_d), .S(pfet_176_s), .D(_1000));
  PullUp pullup_77 (.out(pfet_153_s));
  PFET #(.unidirectional("true")) pfet_177 (.G(pfet_153_d), .S(pfet_177_s), .D(_0111));
  PullUp pullup_78 (.out(pfet_155_s));
  PFET #(.unidirectional("true")) pfet_178 (.G(pfet_155_d), .S(pfet_178_s), .D(_0110));
  PullUp pullup_79 (.out(pfet_157_s));
  PFET #(.unidirectional("true")) pfet_179 (.G(pfet_157_d), .S(pfet_179_s), .D(_0101));
  PullUp pullup_80 (.out(pfet_159_s));
  PFET #(.unidirectional("true")) pfet_180 (.G(pfet_159_d), .S(pfet_180_s), .D(_0100));
  PullUp pullup_81 (.out(pfet_161_s));
  PFET #(.unidirectional("true")) pfet_181 (.G(pfet_161_d), .S(pfet_181_s), .D(_0011));
  PullUp pullup_82 (.out(pfet_163_s));
  PFET #(.unidirectional("true")) pfet_182 (.G(pfet_163_d), .S(pfet_182_s), .D(_0010));
  PullUp pullup_83 (.out(pfet_165_s));
  PFET #(.unidirectional("true")) pfet_183 (.G(pfet_165_d), .S(pfet_183_s), .D(_0001));
  PullUp pullup_84 (.out(pfet_167_s));
  PFET #(.unidirectional("true")) pfet_184 (.G(pfet_167_d), .S(pfet_184_s), .D(_0000));
  PullUp pullup_85 (.out(pfet_169_s));
  PFET #(.unidirectional("true")) pfet_185 (.G(pfet_137_d), .S(pfet_169_s), .D(_1111));
  NFET #(.unidirectional("true")) nfet_169 (.G(pfet_137_d), .D(_1111), .S(nfet_169_s));
  NFET #(.unidirectional("true")) nfet_170 (.G(pfet_137_d), .D(nfet_169_s), .S(1'b0));
  PullUp pullup_86 (.out(pfet_170_s));
  PFET #(.unidirectional("true")) pfet_186 (.G(pfet_138_d), .S(pfet_170_s), .D(_1110));
  NFET #(.unidirectional("true")) nfet_171 (.G(pfet_138_d), .D(_1110), .S(nfet_171_s));
  NFET #(.unidirectional("true")) nfet_172 (.G(pfet_138_d), .D(nfet_171_s), .S(1'b0));
  PullUp pullup_87 (.out(pfet_171_s));
  PFET #(.unidirectional("true")) pfet_187 (.G(pfet_141_d), .S(pfet_171_s), .D(_1101));
  NFET #(.unidirectional("true")) nfet_173 (.G(pfet_141_d), .D(_1101), .S(nfet_173_s));
  NFET #(.unidirectional("true")) nfet_174 (.G(pfet_141_d), .D(nfet_173_s), .S(1'b0));
  PullUp pullup_88 (.out(pfet_172_s));
  PFET #(.unidirectional("true")) pfet_188 (.G(pfet_143_d), .S(pfet_172_s), .D(_1100));
  NFET #(.unidirectional("true")) nfet_175 (.G(pfet_143_d), .D(_1100), .S(nfet_175_s));
  NFET #(.unidirectional("true")) nfet_176 (.G(pfet_143_d), .D(nfet_175_s), .S(1'b0));
  PullUp pullup_89 (.out(pfet_173_s));
  PFET #(.unidirectional("true")) pfet_189 (.G(pfet_145_d), .S(pfet_173_s), .D(_1011));
  NFET #(.unidirectional("true")) nfet_177 (.G(pfet_145_d), .D(_1011), .S(nfet_177_s));
  NFET #(.unidirectional("true")) nfet_178 (.G(pfet_145_d), .D(nfet_177_s), .S(1'b0));
  PullUp pullup_90 (.out(pfet_174_s));
  PFET #(.unidirectional("true")) pfet_190 (.G(pfet_147_d), .S(pfet_174_s), .D(_1010));
  NFET #(.unidirectional("true")) nfet_179 (.G(pfet_147_d), .D(_1010), .S(nfet_179_s));
  NFET #(.unidirectional("true")) nfet_180 (.G(pfet_147_d), .D(nfet_179_s), .S(1'b0));
  PullUp pullup_91 (.out(pfet_175_s));
  PFET #(.unidirectional("true")) pfet_191 (.G(pfet_149_d), .S(pfet_175_s), .D(_1001));
  NFET #(.unidirectional("true")) nfet_181 (.G(pfet_149_d), .D(_1001), .S(nfet_181_s));
  NFET #(.unidirectional("true")) nfet_182 (.G(pfet_149_d), .D(nfet_181_s), .S(1'b0));
  PullUp pullup_92 (.out(pfet_176_s));
  PFET #(.unidirectional("true")) pfet_192 (.G(pfet_151_d), .S(pfet_176_s), .D(_1000));
  NFET #(.unidirectional("true")) nfet_183 (.G(pfet_151_d), .D(_1000), .S(nfet_183_s));
  NFET #(.unidirectional("true")) nfet_184 (.G(pfet_151_d), .D(nfet_183_s), .S(1'b0));
  PullUp pullup_93 (.out(pfet_177_s));
  PFET #(.unidirectional("true")) pfet_193 (.G(pfet_153_d), .S(pfet_177_s), .D(_0111));
  NFET #(.unidirectional("true")) nfet_185 (.G(pfet_153_d), .D(_0111), .S(nfet_185_s));
  NFET #(.unidirectional("true")) nfet_186 (.G(pfet_153_d), .D(nfet_185_s), .S(1'b0));
  PullUp pullup_94 (.out(pfet_178_s));
  PFET #(.unidirectional("true")) pfet_194 (.G(pfet_155_d), .S(pfet_178_s), .D(_0110));
  NFET #(.unidirectional("true")) nfet_187 (.G(pfet_155_d), .D(_0110), .S(nfet_187_s));
  NFET #(.unidirectional("true")) nfet_188 (.G(pfet_155_d), .D(nfet_187_s), .S(1'b0));
  PullUp pullup_95 (.out(pfet_179_s));
  PFET #(.unidirectional("true")) pfet_195 (.G(pfet_157_d), .S(pfet_179_s), .D(_0101));
  NFET #(.unidirectional("true")) nfet_189 (.G(pfet_157_d), .D(_0101), .S(nfet_189_s));
  NFET #(.unidirectional("true")) nfet_190 (.G(pfet_157_d), .D(nfet_189_s), .S(1'b0));
  PullUp pullup_96 (.out(pfet_180_s));
  PFET #(.unidirectional("true")) pfet_196 (.G(pfet_159_d), .S(pfet_180_s), .D(_0100));
  NFET #(.unidirectional("true")) nfet_191 (.G(pfet_159_d), .D(_0100), .S(nfet_191_s));
  NFET #(.unidirectional("true")) nfet_192 (.G(pfet_159_d), .D(nfet_191_s), .S(1'b0));
  PullUp pullup_97 (.out(pfet_181_s));
  PFET #(.unidirectional("true")) pfet_197 (.G(pfet_161_d), .S(pfet_181_s), .D(_0011));
  NFET #(.unidirectional("true")) nfet_193 (.G(pfet_161_d), .D(_0011), .S(nfet_193_s));
  NFET #(.unidirectional("true")) nfet_194 (.G(pfet_161_d), .D(nfet_193_s), .S(1'b0));
  PullUp pullup_98 (.out(pfet_182_s));
  PFET #(.unidirectional("true")) pfet_198 (.G(pfet_163_d), .S(pfet_182_s), .D(_0010));
  NFET #(.unidirectional("true")) nfet_195 (.G(pfet_163_d), .D(_0010), .S(nfet_195_s));
  NFET #(.unidirectional("true")) nfet_196 (.G(pfet_163_d), .D(nfet_195_s), .S(1'b0));
  PullUp pullup_99 (.out(pfet_183_s));
  PFET #(.unidirectional("true")) pfet_199 (.G(pfet_165_d), .S(pfet_183_s), .D(_0001));
  NFET #(.unidirectional("true")) nfet_197 (.G(pfet_165_d), .D(_0001), .S(nfet_197_s));
  NFET #(.unidirectional("true")) nfet_198 (.G(pfet_165_d), .D(nfet_197_s), .S(1'b0));
  PullUp pullup_100 (.out(pfet_184_s));
  PFET #(.unidirectional("true")) pfet_200 (.G(pfet_167_d), .S(pfet_184_s), .D(_0000));
  NFET #(.unidirectional("true")) nfet_199 (.G(pfet_167_d), .D(_0000), .S(nfet_199_s));
  NFET #(.unidirectional("true")) nfet_200 (.G(pfet_167_d), .D(nfet_199_s), .S(1'b0));

  // Notes on the sheet:
  //   NOT
  //   AND
  //   NAND
endmodule
