// Digital circuit mem_1bit.dig as structural Verilog
module mem_1bit (
  input  i,
  input  s,
  output o
);

  wire nfet_1_s, nfet_3_s, nfet_5_s, nfet_7_s, pfet_1_d, pfet_1_s, pfet_2_d, pfet_2_s, pfet_5_s, pfet_6_d,
       pfet_6_s;

  PFET #(.unidirectional("true")) pfet_1 (.G(i), .S(pfet_1_s), .D(pfet_1_d));
  PFET #(.unidirectional("true")) pfet_2 (.G(pfet_1_d), .S(pfet_2_s), .D(pfet_2_d));
  PullUp pullup_1 (.out(pfet_1_s));
  PFET #(.unidirectional("true")) pfet_3 (.G(s), .S(pfet_1_s), .D(pfet_1_d));
  NFET #(.unidirectional("true")) nfet_1 (.G(i), .D(pfet_1_d), .S(nfet_1_s));
  NFET #(.unidirectional("true")) nfet_2 (.G(s), .D(nfet_1_s), .S(1'b0));
  PullUp pullup_2 (.out(pfet_2_s));
  PFET #(.unidirectional("true")) pfet_4 (.G(s), .S(pfet_2_s), .D(pfet_2_d));
  NFET #(.unidirectional("true")) nfet_3 (.G(pfet_1_d), .D(pfet_2_d), .S(nfet_3_s));
  NFET #(.unidirectional("true")) nfet_4 (.G(s), .D(nfet_3_s), .S(1'b0));
  PFET #(.unidirectional("true")) pfet_5 (.G(pfet_1_d), .S(pfet_5_s), .D(o));
  PFET #(.unidirectional("true")) pfet_6 (.G(o), .S(pfet_6_s), .D(pfet_6_d));
  PullUp pullup_3 (.out(pfet_5_s));
  PFET #(.unidirectional("true")) pfet_7 (.G(pfet_6_d), .S(pfet_5_s), .D(o));
  NFET #(.unidirectional("true")) nfet_5 (.G(pfet_1_d), .D(o), .S(nfet_5_s));
  NFET #(.unidirectional("true")) nfet_6 (.G(pfet_6_d), .D(nfet_5_s), .S(1'b0));
  PullUp pullup_4 (.out(pfet_6_s));
  PFET #(.unidirectional("true")) pfet_8 (.G(pfet_2_d), .S(pfet_6_s), .D(pfet_6_d));
  NFET #(.unidirectional("true")) nfet_7 (.G(o), .D(pfet_6_d), .S(nfet_7_s));
  NFET #(.unidirectional("true")) nfet_8 (.G(pfet_2_d), .D(nfet_7_s), .S(1'b0));
  PullDown pulldown_1 (.out(o));

  // Notes on the sheet:
  //   o: output
  //   i: input data
  //   s: set
  //   1b mem
  //   Data
  //   Set
  //   NAND
  //   Output
endmodule
