// Digital circuit not_from_nand.dig as structural Verilog
module not_from_nand (
  input  i1,
  output o
);

  wire nfet_1_s, pfet_1_s;

  PFET #(.unidirectional("true")) pfet_1 (.G(i1), .S(pfet_1_s), .D(o));
  NFET #(.unidirectional("true")) nfet_1 (.G(i1), .D(o), .S(nfet_1_s));
  NFET #(.unidirectional("true")) nfet_2 (.G(i1), .D(nfet_1_s), .S(1'b0));
  PullUp pullup_1 (.out(pfet_1_s));
  PFET #(.unidirectional("true")) pfet_2 (.G(i1), .S(pfet_1_s), .D(o));

  // Notes on the sheet:
  //   NOT
endmodule
