// Digital circuit or_from_nand.dig as structural Verilog
module or_from_nand (
  input  i1,
  input  i2,
  output o
);

  wire nfet_1_s, nfet_3_s, nfet_5_s, pfet_1_d, pfet_1_s, pfet_2_d, pfet_2_s, pfet_5_s;

  PFET #(.unidirectional("true")) pfet_1 (.G(i1), .S(pfet_1_s), .D(pfet_1_d));
  PFET #(.unidirectional("true")) pfet_2 (.G(i2), .S(pfet_2_s), .D(pfet_2_d));
  NFET #(.unidirectional("true")) nfet_1 (.G(i1), .D(pfet_1_d), .S(nfet_1_s));
  NFET #(.unidirectional("true")) nfet_2 (.G(i1), .D(nfet_1_s), .S(1'b0));
  NFET #(.unidirectional("true")) nfet_3 (.G(i2), .D(pfet_2_d), .S(nfet_3_s));
  NFET #(.unidirectional("true")) nfet_4 (.G(i2), .D(nfet_3_s), .S(1'b0));
  PullUp pullup_1 (.out(pfet_1_s));
  PFET #(.unidirectional("true")) pfet_3 (.G(i1), .S(pfet_1_s), .D(pfet_1_d));
  PullUp pullup_2 (.out(pfet_2_s));
  PFET #(.unidirectional("true")) pfet_4 (.G(i2), .S(pfet_2_s), .D(pfet_2_d));
  PFET #(.unidirectional("true")) pfet_5 (.G(pfet_1_d), .S(pfet_5_s), .D(o));
  NFET #(.unidirectional("true")) nfet_5 (.G(pfet_1_d), .D(o), .S(nfet_5_s));
  NFET #(.unidirectional("true")) nfet_6 (.G(pfet_2_d), .D(nfet_5_s), .S(1'b0));
  PullUp pullup_3 (.out(pfet_5_s));
  PFET #(.unidirectional("true")) pfet_6 (.G(pfet_2_d), .S(pfet_5_s), .D(o));

  // Notes on the sheet:
  //   OR
  //   NOT
  //   NAND
endmodule
