// Digital circuit register_always_enabled.dig as structural Verilog
module register_always_enabled (
  input  in_1,
  input  [7:0] i,
  output [7:0] o
);

  wire nfet_1_s, nfet_3_s, nfet_5_s, nfet_7_s, nfet_9_s, nfet_11_s, nfet_13_s, nfet_15_s, nfet_17_s,
       nfet_19_s, nfet_21_s, nfet_23_s, nfet_25_s, nfet_27_s, nfet_29_s, nfet_31_s, nfet_33_s, nfet_35_s,
       nfet_37_s, nfet_39_s, nfet_41_s, nfet_43_s, nfet_45_s, nfet_47_s, nfet_49_s, nfet_51_s, nfet_53_s,
       nfet_55_s, nfet_57_s, nfet_59_s, nfet_61_s, nfet_63_s, pfet_1_d, pfet_1_s, pfet_2_d, pfet_2_s,
       pfet_3_d, pfet_3_s, pfet_4_d, pfet_4_s, pfet_5_d, pfet_5_s, pfet_6_d, pfet_6_s, pfet_7_d, pfet_7_s,
       pfet_8_d, pfet_8_s, pfet_17_s, pfet_18_d, pfet_18_s, pfet_19_s, pfet_20_d, pfet_20_s, pfet_21_s,
       pfet_22_d, pfet_22_s, pfet_23_s, pfet_24_d, pfet_24_s, pfet_33_d, pfet_33_s, pfet_34_d, pfet_34_s,
       pfet_35_d, pfet_35_s, pfet_36_d, pfet_36_s, pfet_37_d, pfet_37_s, pfet_38_d, pfet_38_s, pfet_39_d,
       pfet_39_s, pfet_40_d, pfet_40_s, pfet_49_s, pfet_51_d, pfet_51_s, pfet_53_s, pfet_55_d, pfet_55_s,
       pfet_57_s, pfet_59_d, pfet_59_s, pfet_61_s, pfet_63_d, pfet_63_s;

  PFET #(.unidirectional("true")) pfet_1 (.G(i[4]), .S(pfet_1_s), .D(pfet_1_d));
  PFET #(.unidirectional("true")) pfet_2 (.G(pfet_1_d), .S(pfet_2_s), .D(pfet_2_d));
  PFET #(.unidirectional("true")) pfet_3 (.G(i[5]), .S(pfet_3_s), .D(pfet_3_d));
  PFET #(.unidirectional("true")) pfet_4 (.G(pfet_3_d), .S(pfet_4_s), .D(pfet_4_d));
  PFET #(.unidirectional("true")) pfet_5 (.G(i[6]), .S(pfet_5_s), .D(pfet_5_d));
  PFET #(.unidirectional("true")) pfet_6 (.G(pfet_5_d), .S(pfet_6_s), .D(pfet_6_d));
  PFET #(.unidirectional("true")) pfet_7 (.G(i[7]), .S(pfet_7_s), .D(pfet_7_d));
  PFET #(.unidirectional("true")) pfet_8 (.G(pfet_7_d), .S(pfet_8_s), .D(pfet_8_d));
  PullUp pullup_1 (.out(pfet_1_s));
  PFET #(.unidirectional("true")) pfet_9 (.G(in_1), .S(pfet_1_s), .D(pfet_1_d));
  NFET #(.unidirectional("true")) nfet_1 (.G(i[4]), .D(pfet_1_d), .S(nfet_1_s));
  NFET #(.unidirectional("true")) nfet_2 (.G(in_1), .D(nfet_1_s), .S(1'b0));
  PullUp pullup_2 (.out(pfet_2_s));
  PFET #(.unidirectional("true")) pfet_10 (.G(in_1), .S(pfet_2_s), .D(pfet_2_d));
  NFET #(.unidirectional("true")) nfet_3 (.G(pfet_1_d), .D(pfet_2_d), .S(nfet_3_s));
  NFET #(.unidirectional("true")) nfet_4 (.G(in_1), .D(nfet_3_s), .S(1'b0));
  PullUp pullup_3 (.out(pfet_3_s));
  PFET #(.unidirectional("true")) pfet_11 (.G(in_1), .S(pfet_3_s), .D(pfet_3_d));
  NFET #(.unidirectional("true")) nfet_5 (.G(i[5]), .D(pfet_3_d), .S(nfet_5_s));
  NFET #(.unidirectional("true")) nfet_6 (.G(in_1), .D(nfet_5_s), .S(1'b0));
  PullUp pullup_4 (.out(pfet_4_s));
  PFET #(.unidirectional("true")) pfet_12 (.G(in_1), .S(pfet_4_s), .D(pfet_4_d));
  NFET #(.unidirectional("true")) nfet_7 (.G(pfet_3_d), .D(pfet_4_d), .S(nfet_7_s));
  NFET #(.unidirectional("true")) nfet_8 (.G(in_1), .D(nfet_7_s), .S(1'b0));
  PullUp pullup_5 (.out(pfet_5_s));
  PFET #(.unidirectional("true")) pfet_13 (.G(in_1), .S(pfet_5_s), .D(pfet_5_d));
  NFET #(.unidirectional("true")) nfet_9 (.G(i[6]), .D(pfet_5_d), .S(nfet_9_s));
  NFET #(.unidirectional("true")) nfet_10 (.G(in_1), .D(nfet_9_s), .S(1'b0));
  PullUp pullup_6 (.out(pfet_6_s));
  PFET #(.unidirectional("true")) pfet_14 (.G(in_1), .S(pfet_6_s), .D(pfet_6_d));
  NFET #(.unidirectional("true")) nfet_11 (.G(pfet_5_d), .D(pfet_6_d), .S(nfet_11_s));
  NFET #(.unidirectional("true")) nfet_12 (.G(in_1), .D(nfet_11_s), .S(1'b0));
  PullUp pullup_7 (.out(pfet_7_s));
  PFET #(.unidirectional("true")) pfet_15 (.G(in_1), .S(pfet_7_s), .D(pfet_7_d));
  NFET #(.unidirectional("true")) nfet_13 (.G(i[7]), .D(pfet_7_d), .S(nfet_13_s));
  NFET #(.unidirectional("true")) nfet_14 (.G(in_1), .D(nfet_13_s), .S(1'b0));
  PullUp pullup_8 (.out(pfet_8_s));
  PFET #(.unidirectional("true")) pfet_16 (.G(in_1), .S(pfet_8_s), .D(pfet_8_d));
  NFET #(.unidirectional("true")) nfet_15 (.G(pfet_7_d), .D(pfet_8_d), .S(nfet_15_s));
  NFET #(.unidirectional("true")) nfet_16 (.G(in_1), .D(nfet_15_s), .S(1'b0));
  PFET #(.unidirectional("true")) pfet_17 (.G(pfet_1_d), .S(pfet_17_s), .D(o[4]));
  PFET #(.unidirectional("true")) pfet_18 (.G(o[4]), .S(pfet_18_s), .D(pfet_18_d));
  PFET #(.unidirectional("true")) pfet_19 (.G(pfet_3_d), .S(pfet_19_s), .D(o[5]));
  PFET #(.unidirectional("true")) pfet_20 (.G(o[5]), .S(pfet_20_s), .D(pfet_20_d));
  PFET #(.unidirectional("true")) pfet_21 (.G(pfet_5_d), .S(pfet_21_s), .D(o[6]));
  PFET #(.unidirectional("true")) pfet_22 (.G(o[6]), .S(pfet_22_s), .D(pfet_22_d));
  PFET #(.unidirectional("true")) pfet_23 (.G(pfet_7_d), .S(pfet_23_s), .D(o[7]));
  PFET #(.unidirectional("true")) pfet_24 (.G(o[7]), .S(pfet_24_s), .D(pfet_24_d));
  PullUp pullup_9 (.out(pfet_17_s));
  PFET #(.unidirectional("true")) pfet_25 (.G(pfet_18_d), .S(pfet_17_s), .D(o[4]));
  NFET #(.unidirectional("true")) nfet_17 (.G(pfet_1_d), .D(o[4]), .S(nfet_17_s));
  NFET #(.unidirectional("true")) nfet_18 (.G(pfet_18_d), .D(nfet_17_s), .S(1'b0));
  PullUp pullup_10 (.out(pfet_18_s));
  PFET #(.unidirectional("true")) pfet_26 (.G(pfet_2_d), .S(pfet_18_s), .D(pfet_18_d));
  NFET #(.unidirectional("true")) nfet_19 (.G(o[4]), .D(pfet_18_d), .S(nfet_19_s));
  NFET #(.unidirectional("true")) nfet_20 (.G(pfet_2_d), .D(nfet_19_s), .S(1'b0));
  PullUp pullup_11 (.out(pfet_19_s));
  PFET #(.unidirectional("true")) pfet_27 (.G(pfet_20_d), .S(pfet_19_s), .D(o[5]));
  NFET #(.unidirectional("true")) nfet_21 (.G(pfet_3_d), .D(o[5]), .S(nfet_21_s));
  NFET #(.unidirectional("true")) nfet_22 (.G(pfet_20_d), .D(nfet_21_s), .S(1'b0));
  PullUp pullup_12 (.out(pfet_20_s));
  PFET #(.unidirectional("true")) pfet_28 (.G(pfet_4_d), .S(pfet_20_s), .D(pfet_20_d));
  NFET #(.unidirectional("true")) nfet_23 (.G(o[5]), .D(pfet_20_d), .S(nfet_23_s));
  NFET #(.unidirectional("true")) nfet_24 (.G(pfet_4_d), .D(nfet_23_s), .S(1'b0));
  PullUp pullup_13 (.out(pfet_21_s));
  PFET #(.unidirectional("true")) pfet_29 (.G(pfet_22_d), .S(pfet_21_s), .D(o[6]));
  NFET #(.unidirectional("true")) nfet_25 (.G(pfet_5_d), .D(o[6]), .S(nfet_25_s));
  NFET #(.unidirectional("true")) nfet_26 (.G(pfet_22_d), .D(nfet_25_s), .S(1'b0));
  PullUp pullup_14 (.out(pfet_22_s));
  PFET #(.unidirectional("true")) pfet_30 (.G(pfet_6_d), .S(pfet_22_s), .D(pfet_22_d));
  NFET #(.unidirectional("true")) nfet_27 (.G(o[6]), .D(pfet_22_d), .S(nfet_27_s));
  NFET #(.unidirectional("true")) nfet_28 (.G(pfet_6_d), .D(nfet_27_s), .S(1'b0));
  PullUp pullup_15 (.out(pfet_23_s));
  PFET #(.unidirectional("true")) pfet_31 (.G(pfet_24_d), .S(pfet_23_s), .D(o[7]));
  NFET #(.unidirectional("true")) nfet_29 (.G(pfet_7_d), .D(o[7]), .S(nfet_29_s));
  NFET #(.unidirectional("true")) nfet_30 (.G(pfet_24_d), .D(nfet_29_s), .S(1'b0));
  PullUp pullup_16 (.out(pfet_24_s));
  PFET #(.unidirectional("true")) pfet_32 (.G(pfet_8_d), .S(pfet_24_s), .D(pfet_24_d));
  NFET #(.unidirectional("true")) nfet_31 (.G(o[7]), .D(pfet_24_d), .S(nfet_31_s));
  NFET #(.unidirectional("true")) nfet_32 (.G(pfet_8_d), .D(nfet_31_s), .S(1'b0));
  PullDown pulldown_1 (.out(o[4]));
  PullDown pulldown_2 (.out(o[5]));
  PullDown pulldown_3 (.out(o[6]));
  PullDown pulldown_4 (.out(o[7]));
  PFET #(.unidirectional("true")) pfet_33 (.G(i[0]), .S(pfet_33_s), .D(pfet_33_d));
  PFET #(.unidirectional("true")) pfet_34 (.G(pfet_33_d), .S(pfet_34_s), .D(pfet_34_d));
  PFET #(.unidirectional("true")) pfet_35 (.G(i[1]), .S(pfet_35_s), .D(pfet_35_d));
  PFET #(.unidirectional("true")) pfet_36 (.G(pfet_35_d), .S(pfet_36_s), .D(pfet_36_d));
  PFET #(.unidirectional("true")) pfet_37 (.G(i[2]), .S(pfet_37_s), .D(pfet_37_d));
  PFET #(.unidirectional("true")) pfet_38 (.G(pfet_37_d), .S(pfet_38_s), .D(pfet_38_d));
  PFET #(.unidirectional("true")) pfet_39 (.G(i[3]), .S(pfet_39_s), .D(pfet_39_d));
  PFET #(.unidirectional("true")) pfet_40 (.G(pfet_39_d), .S(pfet_40_s), .D(pfet_40_d));
  PullUp pullup_17 (.out(pfet_33_s));
  PFET #(.unidirectional("true")) pfet_41 (.G(in_1), .S(pfet_33_s), .D(pfet_33_d));
  NFET #(.unidirectional("true")) nfet_33 (.G(i[0]), .D(pfet_33_d), .S(nfet_33_s));
  NFET #(.unidirectional("true")) nfet_34 (.G(in_1), .D(nfet_33_s), .S(1'b0));
  PullUp pullup_18 (.out(pfet_34_s));
  PFET #(.unidirectional("true")) pfet_42 (.G(in_1), .S(pfet_34_s), .D(pfet_34_d));
  NFET #(.unidirectional("true")) nfet_35 (.G(pfet_33_d), .D(pfet_34_d), .S(nfet_35_s));
  NFET #(.unidirectional("true")) nfet_36 (.G(in_1), .D(nfet_35_s), .S(1'b0));
  PullUp pullup_19 (.out(pfet_35_s));
  PFET #(.unidirectional("true")) pfet_43 (.G(in_1), .S(pfet_35_s), .D(pfet_35_d));
  NFET #(.unidirectional("true")) nfet_37 (.G(i[1]), .D(pfet_35_d), .S(nfet_37_s));
  NFET #(.unidirectional("true")) nfet_38 (.G(in_1), .D(nfet_37_s), .S(1'b0));
  PullUp pullup_20 (.out(pfet_36_s));
  PFET #(.unidirectional("true")) pfet_44 (.G(in_1), .S(pfet_36_s), .D(pfet_36_d));
  NFET #(.unidirectional("true")) nfet_39 (.G(pfet_35_d), .D(pfet_36_d), .S(nfet_39_s));
  NFET #(.unidirectional("true")) nfet_40 (.G(in_1), .D(nfet_39_s), .S(1'b0));
  PullUp pullup_21 (.out(pfet_37_s));
  PFET #(.unidirectional("true")) pfet_45 (.G(in_1), .S(pfet_37_s), .D(pfet_37_d));
  NFET #(.unidirectional("true")) nfet_41 (.G(i[2]), .D(pfet_37_d), .S(nfet_41_s));
  NFET #(.unidirectional("true")) nfet_42 (.G(in_1), .D(nfet_41_s), .S(1'b0));
  PullUp pullup_22 (.out(pfet_38_s));
  PFET #(.unidirectional("true")) pfet_46 (.G(in_1), .S(pfet_38_s), .D(pfet_38_d));
  NFET #(.unidirectional("true")) nfet_43 (.G(pfet_37_d), .D(pfet_38_d), .S(nfet_43_s));
  NFET #(.unidirectional("true")) nfet_44 (.G(in_1), .D(nfet_43_s), .S(1'b0));
  PullUp pullup_23 (.out(pfet_39_s));
  PFET #(.unidirectional("true")) pfet_47 (.G(in_1), .S(pfet_39_s), .D(pfet_39_d));
  NFET #(.unidirectional("true")) nfet_45 (.G(i[3]), .D(pfet_39_d), .S(nfet_45_s));
  NFET #(.unidirectional("true")) nfet_46 (.G(in_1), .D(nfet_45_s), .S(1'b0));
  PullUp pullup_24 (.out(pfet_40_s));
  PFET #(.unidirectional("true")) pfet_48 (.G(in_1), .S(pfet_40_s), .D(pfet_40_d));
  NFET #(.unidirectional("true")) nfet_47 (.G(pfet_39_d), .D(pfet_40_d), .S(nfet_47_s));
  NFET #(.unidirectional("true")) nfet_48 (.G(in_1), .D(nfet_47_s), .S(1'b0));
  PFET #(.unidirectional("true")) pfet_49 (.G(pfet_33_d), .S(pfet_49_s), .D(o[0]));
  PFET #(.unidirectional("true")) pfet_50 (.G(pfet_51_d), .S(pfet_49_s), .D(o[0]));
  NFET #(.unidirectional("true")) nfet_49 (.G(pfet_33_d), .D(o[0]), .S(nfet_49_s));
  NFET #(.unidirectional("true")) nfet_50 (.G(pfet_51_d), .D(nfet_49_s), .S(1'b0));
  PFET #(.unidirectional("true")) pfet_51 (.G(o[0]), .S(pfet_51_s), .D(pfet_51_d));
  PFET #(.unidirectional("true")) pfet_52 (.G(pfet_34_d), .S(pfet_51_s), .D(pfet_51_d));
  NFET #(.unidirectional("true")) nfet_51 (.G(o[0]), .D(pfet_51_d), .S(nfet_51_s));
  NFET #(.unidirectional("true")) nfet_52 (.G(pfet_34_d), .D(nfet_51_s), .S(1'b0));
  PFET #(.unidirectional("true")) pfet_53 (.G(pfet_35_d), .S(pfet_53_s), .D(o[1]));
  PFET #(.unidirectional("true")) pfet_54 (.G(pfet_55_d), .S(pfet_53_s), .D(o[1]));
  NFET #(.unidirectional("true")) nfet_53 (.G(pfet_35_d), .D(o[1]), .S(nfet_53_s));
  NFET #(.unidirectional("true")) nfet_54 (.G(pfet_55_d), .D(nfet_53_s), .S(1'b0));
  PFET #(.unidirectional("true")) pfet_55 (.G(o[1]), .S(pfet_55_s), .D(pfet_55_d));
  PFET #(.unidirectional("true")) pfet_56 (.G(pfet_36_d), .S(pfet_55_s), .D(pfet_55_d));
  NFET #(.unidirectional("true")) nfet_55 (.G(o[1]), .D(pfet_55_d), .S(nfet_55_s));
  NFET #(.unidirectional("true")) nfet_56 (.G(pfet_36_d), .D(nfet_55_s), .S(1'b0));
  PFET #(.unidirectional("true")) pfet_57 (.G(pfet_37_d), .S(pfet_57_s), .D(o[2]));
  PFET #(.unidirectional("true")) pfet_58 (.G(pfet_59_d), .S(pfet_57_s), .D(o[2]));
  NFET #(.unidirectional("true")) nfet_57 (.G(pfet_37_d), .D(o[2]), .S(nfet_57_s));
  NFET #(.unidirectional("true")) nfet_58 (.G(pfet_59_d), .D(nfet_57_s), .S(1'b0));
  PFET #(.unidirectional("true")) pfet_59 (.G(o[2]), .S(pfet_59_s), .D(pfet_59_d));
  PFET #(.unidirectional("true")) pfet_60 (.G(pfet_38_d), .S(pfet_59_s), .D(pfet_59_d));
  NFET #(.unidirectional("true")) nfet_59 (.G(o[2]), .D(pfet_59_d), .S(nfet_59_s));
  NFET #(.unidirectional("true")) nfet_60 (.G(pfet_38_d), .D(nfet_59_s), .S(1'b0));
  PFET #(.unidirectional("true")) pfet_61 (.G(pfet_39_d), .S(pfet_61_s), .D(o[3]));
  PFET #(.unidirectional("true")) pfet_62 (.G(pfet_63_d), .S(pfet_61_s), .D(o[3]));
  NFET #(.unidirectional("true")) nfet_61 (.G(pfet_39_d), .D(o[3]), .S(nfet_61_s));
  NFET #(.unidirectional("true")) nfet_62 (.G(pfet_63_d), .D(nfet_61_s), .S(1'b0));
  PFET #(.unidirectional("true")) pfet_63 (.G(o[3]), .S(pfet_63_s), .D(pfet_63_d));
  PFET #(.unidirectional("true")) pfet_64 (.G(pfet_40_d), .S(pfet_63_s), .D(pfet_63_d));
  NFET #(.unidirectional("true")) nfet_63 (.G(o[3]), .D(pfet_63_d), .S(nfet_63_s));
  NFET #(.unidirectional("true")) nfet_64 (.G(pfet_40_d), .D(nfet_63_s), .S(1'b0));
  PullUp pullup_25 (.out(pfet_49_s));
  PullDown pulldown_5 (.out(o[0]));
  PullUp pullup_26 (.out(pfet_51_s));
  PullUp pullup_27 (.out(pfet_53_s));
  PullDown pulldown_6 (.out(o[1]));
  PullUp pullup_28 (.out(pfet_55_s));
  PullUp pullup_29 (.out(pfet_57_s));
  PullDown pulldown_7 (.out(o[2]));
  PullUp pullup_30 (.out(pfet_59_s));
  PullUp pullup_31 (.out(pfet_61_s));
  PullDown pulldown_8 (.out(o[3]));
  PullUp pullup_32 (.out(pfet_63_s));
  LED led_1 (.in(in_1));
  Seven_Seg_Hex seven_seg_hex_1 (.d(o[7:4]), .dp(1'b0));
  Seven_Seg_Hex seven_seg_hex_2 (.d(o[3:0]), .dp(1'b0));

  // Notes on the sheet:
  //   Register enabled
  //   Input
  //   1b mem
  //   Set
  //   NAND
  //   Data
  //   Output
endmodule
