// Digital circuit ALU.dig as structural Verilog
module ALU (
  input  [7:0] a,
  input  [2:0] op,
  input  c_i,
  input  [7:0] b,
  output [7:0] o,
  output c_o
);

  wire decoder_3x8_1__000, decoder_3x8_1__001, decoder_3x8_1__010, decoder_3x8_1__011, decoder_3x8_1__100,
       decoder_3x8_1__101, decoder_3x8_1__110, decoder_3x8_1__111;

  shifter_left Left (.i(a), .o(o), .si(c_i), .so(c_o), .e(decoder_3x8_1__000));
  shifter_right Right (.i(a), .o(o), .si(c_i), .so(c_o), .e(decoder_3x8_1__001));
  NOTer noter_1 (.i(a), .o(o), .e(decoder_3x8_1__010));
  ANDer ander_1 (.i(a), .i2(b), .o(o), .e(decoder_3x8_1__011));
  ORer orer_1 (.i(a), .i2(b), .o(o), .e(decoder_3x8_1__100));
  XORer xorer_1 (.i(a), .i2(b), .o(o), .e(decoder_3x8_1__101));
  LED led_1 (.in(decoder_3x8_1__111));
  LED led_2 (.in(decoder_3x8_1__110));
  decoder_3x8 decoder_3x8_1 (
    .sel(op), ._000(decoder_3x8_1__000), ._001(decoder_3x8_1__001), ._010(decoder_3x8_1__010),
    ._011(decoder_3x8_1__011), ._100(decoder_3x8_1__100), ._101(decoder_3x8_1__101),
    ._110(decoder_3x8_1__110), ._111(decoder_3x8_1__111));

  // Notes on the sheet:
  //   c_i: carry in
  //   c_o: carry out
endmodule
