// Digital circuit ANDer.dig as structural Verilog
module ANDer (
  input  [7:0] i,
  input  e,
  input  [7:0] i2,
  output [7:0] o
);

  wire [7:0] and_nand_3_o, enabler_and_1_o, enabler_and_2_o;

  enabler_and enabler_and_1 (.o(enabler_and_1_o), .i(i), .e(e));
  enabler_and enabler_and_2 (.o(enabler_and_2_o), .i(i2), .e(e));
  and_nand and_nand_1 (.i1(enabler_and_2_o[0]), .i2(enabler_and_1_o[0]), .o(and_nand_3_o[0]));
  and_nand and_nand_2 (.i1(enabler_and_2_o[1]), .i2(enabler_and_1_o[1]), .o(and_nand_3_o[1]));
  and_nand and_nand_3 (.i1(enabler_and_2_o[2]), .i2(enabler_and_1_o[2]), .o(and_nand_3_o[2]));
  and_nand and_nand_4 (.i1(enabler_and_2_o[3]), .i2(enabler_and_1_o[3]), .o(and_nand_3_o[3]));
  and_nand and_nand_5 (.i1(enabler_and_2_o[4]), .i2(enabler_and_1_o[4]), .o(and_nand_3_o[4]));
  and_nand and_nand_6 (.i1(enabler_and_2_o[5]), .i2(enabler_and_1_o[5]), .o(and_nand_3_o[5]));
  and_nand and_nand_7 (.i1(enabler_and_2_o[6]), .i2(enabler_and_1_o[6]), .o(and_nand_3_o[6]));
  and_nand and_nand_8 (.i1(enabler_and_2_o[7]), .i2(enabler_and_1_o[7]), .o(and_nand_3_o[7]));
  enabler_high_impedance enabler_high_impedance_1 (.o(o), .i(and_nand_3_o), .e(e));
endmodule
