// Digital circuit NOTer.dig as structural Verilog
module NOTer (
  input  [7:0] i,
  input  e,
  output [7:0] o
);

  wire [7:0] enabler_and_1_o, not_1_out;

  enabler_and enabler_and_1 (.o(enabler_and_1_o), .i(i), .e(e));
  not not_1 (not_1_out[0], enabler_and_1_o[0]);
  not not_2 (not_1_out[1], enabler_and_1_o[1]);
  not not_3 (not_1_out[2], enabler_and_1_o[2]);
  not not_4 (not_1_out[3], enabler_and_1_o[3]);
  not not_5 (not_1_out[4], enabler_and_1_o[4]);
  not not_6 (not_1_out[5], enabler_and_1_o[5]);
  not not_7 (not_1_out[6], enabler_and_1_o[6]);
  not not_8 (not_1_out[7], enabler_and_1_o[7]);
  enabler_high_impedance enabler_high_impedance_1 (.o(o), .i(not_1_out), .e(e));
endmodule
