// Digital circuit RAM.dig as structural Verilog
module RAM (
  input  [7:0] a,
  input  e,
  input  s,
  input  [7:0] i,
  output [7:0] o
);

  wire decoder_4x16_1__0000, decoder_4x16_1__0001, decoder_4x16_1__0010, decoder_4x16_1__0011,
       decoder_4x16_1__0100, decoder_4x16_1__0101, decoder_4x16_1__0111, decoder_4x16_1__1000,
       decoder_4x16_1__1001, decoder_4x16_1__1010, decoder_4x16_1__1011, decoder_4x16_1__1100,
       decoder_4x16_1__1101, decoder_4x16_1__1110, decoder_4x16_1__1111, decoder_4x16_2__0000,
       decoder_4x16_2__0001, decoder_4x16_2__0010, decoder_4x16_2__0011, decoder_4x16_2__0100,
       decoder_4x16_2__0101, decoder_4x16_2__0110, decoder_4x16_2__0111, decoder_4x16_2__1000,
       decoder_4x16_2__1001, decoder_4x16_2__1010, decoder_4x16_2__1011, decoder_4x16_2__1100,
       decoder_4x16_2__1101, decoder_4x16_2__1110, decoder_4x16_2__1111;

  buffer_high_impedance buffer_high_impedance_1 (.i(i[0]), .e(s), .o(o[0]));
  buffer_high_impedance buffer_high_impedance_2 (.i(i[1]), .e(s), .o(o[1]));
  buffer_high_impedance buffer_high_impedance_3 (.i(i[2]), .e(s), .o(o[2]));
  buffer_high_impedance buffer_high_impedance_4 (.i(i[3]), .e(s), .o(o[3]));
  buffer_high_impedance buffer_high_impedance_5 (.i(i[4]), .e(s), .o(o[4]));
  buffer_high_impedance buffer_high_impedance_6 (.i(i[5]), .e(s), .o(o[5]));
  buffer_high_impedance buffer_high_impedance_7 (.i(i[6]), .e(s), .o(o[6]));
  buffer_high_impedance buffer_high_impedance_8 (.i(i[7]), .e(s), .o(o[7]));
  decoder_4x16 decoder_4x16_1 (
    .sel(a[3:0]), ._0000(decoder_4x16_1__0000), ._0001(decoder_4x16_1__0001), ._0010(decoder_4x16_1__0010),
    ._0011(decoder_4x16_1__0011), ._0100(decoder_4x16_1__0100), ._0101(decoder_4x16_1__0101),
    ._0110(decoder_4x16_1__0101), ._0111(decoder_4x16_1__0111), ._1000(decoder_4x16_1__1000),
    ._1001(decoder_4x16_1__1001), ._1010(decoder_4x16_1__1010), ._1011(decoder_4x16_1__1011),
    ._1100(decoder_4x16_1__1100), ._1101(decoder_4x16_1__1101), ._1110(decoder_4x16_1__1110),
    ._1111(decoder_4x16_1__1111));
  registro_x_y registro_x_y_1 (.i(o), .s(s), .e(e), .y(decoder_4x16_2__0000), .o(o), .x(decoder_4x16_1__0000));
  registro_x_y registro_x_y_2 (.i(o), .s(s), .e(e), .y(decoder_4x16_2__0000), .o(o), .x(decoder_4x16_1__0001));
  registro_x_y registro_x_y_3 (.i(o), .s(s), .e(e), .y(decoder_4x16_2__0000), .o(o), .x(decoder_4x16_1__0010));
  registro_x_y registro_x_y_4 (.i(o), .s(s), .e(e), .y(decoder_4x16_2__0000), .o(o), .x(decoder_4x16_1__0011));
  registro_x_y registro_x_y_5 (.i(o), .s(s), .e(e), .y(decoder_4x16_2__0000), .o(o), .x(decoder_4x16_1__0100));
  registro_x_y registro_x_y_6 (.i(o), .s(s), .e(e), .y(decoder_4x16_2__0000), .o(o), .x(decoder_4x16_1__0101));
  registro_x_y registro_x_y_7 (.i(o), .s(s), .e(e), .y(decoder_4x16_2__0000), .o(o), .x(decoder_4x16_1__0101));
  registro_x_y registro_x_y_8 (.i(o), .s(s), .e(e), .y(decoder_4x16_2__0000), .o(o), .x(decoder_4x16_1__0111));
  registro_x_y registro_x_y_9 (.i(o), .s(s), .e(e), .y(decoder_4x16_2__0000), .o(o), .x(decoder_4x16_1__1000));
  registro_x_y registro_x_y_10 (.i(o), .s(s), .e(e), .y(decoder_4x16_2__0000), .o(o), .x(decoder_4x16_1__1001));
  registro_x_y registro_x_y_11 (.i(o), .s(s), .e(e), .y(decoder_4x16_2__0000), .o(o), .x(decoder_4x16_1__1010));
  registro_x_y registro_x_y_12 (.i(o), .s(s), .e(e), .y(decoder_4x16_2__0000), .o(o), .x(decoder_4x16_1__1011));
  registro_x_y registro_x_y_13 (.i(o), .s(s), .e(e), .y(decoder_4x16_2__0000), .o(o), .x(decoder_4x16_1__1100));
  registro_x_y registro_x_y_14 (.i(o), .s(s), .e(e), .y(decoder_4x16_2__0000), .o(o), .x(decoder_4x16_1__1101));
  registro_x_y registro_x_y_15 (.i(o), .s(s), .e(e), .y(decoder_4x16_2__0000), .o(o), .x(decoder_4x16_1__1110));
  registro_x_y registro_x_y_16 (.i(o), .s(s), .e(e), .y(decoder_4x16_2__0000), .o(o), .x(decoder_4x16_1__1111));
  Seven_Seg_Hex seven_seg_hex_1 (.d(o[7:4]), .dp(1'b0));
  Seven_Seg_Hex seven_seg_hex_2 (.d(o[3:0]), .dp(1'b0));
  registro_x_y registro_x_y_17 (.i(o), .s(s), .e(e), .y(decoder_4x16_2__0001), .o(o), .x(decoder_4x16_1__0000));
  registro_x_y registro_x_y_18 (.i(o), .s(s), .e(e), .y(decoder_4x16_2__0001), .o(o), .x(decoder_4x16_1__0001));
  registro_x_y registro_x_y_19 (.i(o), .s(s), .e(e), .y(decoder_4x16_2__0001), .o(o), .x(decoder_4x16_1__0010));
  registro_x_y registro_x_y_20 (.i(o), .s(s), .e(e), .y(decoder_4x16_2__0001), .o(o), .x(decoder_4x16_1__0011));
  registro_x_y registro_x_y_21 (.i(o), .s(s), .e(e), .y(decoder_4x16_2__0001), .o(o), .x(decoder_4x16_1__0100));
  registro_x_y registro_x_y_22 (.i(o), .s(s), .e(e), .y(decoder_4x16_2__0001), .o(o), .x(decoder_4x16_1__0101));
  registro_x_y registro_x_y_23 (.i(o), .s(s), .e(e), .y(decoder_4x16_2__0001), .o(o), .x(decoder_4x16_1__0101));
  registro_x_y registro_x_y_24 (.i(o), .s(s), .e(e), .y(decoder_4x16_2__0001), .o(o), .x(decoder_4x16_1__0111));
  registro_x_y registro_x_y_25 (.i(o), .s(s), .e(e), .y(decoder_4x16_2__0001), .o(o), .x(decoder_4x16_1__1000));
  registro_x_y registro_x_y_26 (.i(o), .s(s), .e(e), .y(decoder_4x16_2__0001), .o(o), .x(decoder_4x16_1__1001));
  registro_x_y registro_x_y_27 (.i(o), .s(s), .e(e), .y(decoder_4x16_2__0001), .o(o), .x(decoder_4x16_1__1010));
  registro_x_y registro_x_y_28 (.i(o), .s(s), .e(e), .y(decoder_4x16_2__0001), .o(o), .x(decoder_4x16_1__1011));
  registro_x_y registro_x_y_29 (.i(o), .s(s), .e(e), .y(decoder_4x16_2__0001), .o(o), .x(decoder_4x16_1__1100));
  registro_x_y registro_x_y_30 (.i(o), .s(s), .e(e), .y(decoder_4x16_2__0001), .o(o), .x(decoder_4x16_1__1101));
  registro_x_y registro_x_y_31 (.i(o), .s(s), .e(e), .y(decoder_4x16_2__0001), .o(o), .x(decoder_4x16_1__1110));
  registro_x_y registro_x_y_32 (.i(o), .s(s), .e(e), .y(decoder_4x16_2__0001), .o(o), .x(decoder_4x16_1__1111));
  registro_x_y registro_x_y_33 (.i(o), .s(s), .e(e), .y(decoder_4x16_2__0010), .o(o), .x(decoder_4x16_1__0000));
  registro_x_y registro_x_y_34 (.i(o), .s(s), .e(e), .y(decoder_4x16_2__0010), .o(o), .x(decoder_4x16_1__0001));
  registro_x_y registro_x_y_35 (.i(o), .s(s), .e(e), .y(decoder_4x16_2__0010), .o(o), .x(decoder_4x16_1__0010));
  registro_x_y registro_x_y_36 (.i(o), .s(s), .e(e), .y(decoder_4x16_2__0010), .o(o), .x(decoder_4x16_1__0011));
  registro_x_y registro_x_y_37 (.i(o), .s(s), .e(e), .y(decoder_4x16_2__0010), .o(o), .x(decoder_4x16_1__0100));
  registro_x_y registro_x_y_38 (.i(o), .s(s), .e(e), .y(decoder_4x16_2__0010), .o(o), .x(decoder_4x16_1__0101));
  registro_x_y registro_x_y_39 (.i(o), .s(s), .e(e), .y(decoder_4x16_2__0010), .o(o), .x(decoder_4x16_1__0101));
  registro_x_y registro_x_y_40 (.i(o), .s(s), .e(e), .y(decoder_4x16_2__0010), .o(o), .x(decoder_4x16_1__0111));
  registro_x_y registro_x_y_41 (.i(o), .s(s), .e(e), .y(decoder_4x16_2__0010), .o(o), .x(decoder_4x16_1__1000));
  registro_x_y registro_x_y_42 (.i(o), .s(s), .e(e), .y(decoder_4x16_2__0010), .o(o), .x(decoder_4x16_1__1001));
  registro_x_y registro_x_y_43 (.i(o), .s(s), .e(e), .y(decoder_4x16_2__0010), .o(o), .x(decoder_4x16_1__1010));
  registro_x_y registro_x_y_44 (.i(o), .s(s), .e(e), .y(decoder_4x16_2__0010), .o(o), .x(decoder_4x16_1__1011));
  registro_x_y registro_x_y_45 (.i(o), .s(s), .e(e), .y(decoder_4x16_2__0010), .o(o), .x(decoder_4x16_1__1100));
  registro_x_y registro_x_y_46 (.i(o), .s(s), .e(e), .y(decoder_4x16_2__0010), .o(o), .x(decoder_4x16_1__1101));
  registro_x_y registro_x_y_47 (.i(o), .s(s), .e(e), .y(decoder_4x16_2__0010), .o(o), .x(decoder_4x16_1__1110));
  registro_x_y registro_x_y_48 (.i(o), .s(s), .e(e), .y(decoder_4x16_2__0010), .o(o), .x(decoder_4x16_1__1111));
  registro_x_y registro_x_y_49 (.i(o), .s(s), .e(e), .y(decoder_4x16_2__0011), .o(o), .x(decoder_4x16_1__0000));
  registro_x_y registro_x_y_50 (.i(o), .s(s), .e(e), .y(decoder_4x16_2__0011), .o(o), .x(decoder_4x16_1__0001));
  registro_x_y registro_x_y_51 (.i(o), .s(s), .e(e), .y(decoder_4x16_2__0011), .o(o), .x(decoder_4x16_1__0010));
  registro_x_y registro_x_y_52 (.i(o), .s(s), .e(e), .y(decoder_4x16_2__0011), .o(o), .x(decoder_4x16_1__0011));
  registro_x_y registro_x_y_53 (.i(o), .s(s), .e(e), .y(decoder_4x16_2__0011), .o(o), .x(decoder_4x16_1__0100));
  registro_x_y registro_x_y_54 (.i(o), .s(s), .e(e), .y(decoder_4x16_2__0011), .o(o), .x(decoder_4x16_1__0101));
  registro_x_y registro_x_y_55 (.i(o), .s(s), .e(e), .y(decoder_4x16_2__0011), .o(o), .x(decoder_4x16_1__0101));
  registro_x_y registro_x_y_56 (.i(o), .s(s), .e(e), .y(decoder_4x16_2__0011), .o(o), .x(decoder_4x16_1__0111));
  registro_x_y registro_x_y_57 (.i(o), .s(s), .e(e), .y(decoder_4x16_2__0011), .o(o), .x(decoder_4x16_1__1000));
  registro_x_y registro_x_y_58 (.i(o), .s(s), .e(e), .y(decoder_4x16_2__0011), .o(o), .x(decoder_4x16_1__1001));
  registro_x_y registro_x_y_59 (.i(o), .s(s), .e(e), .y(decoder_4x16_2__0011), .o(o), .x(decoder_4x16_1__1010));
  registro_x_y registro_x_y_60 (.i(o), .s(s), .e(e), .y(decoder_4x16_2__0011), .o(o), .x(decoder_4x16_1__1011));
  registro_x_y registro_x_y_61 (.i(o), .s(s), .e(e), .y(decoder_4x16_2__0011), .o(o), .x(decoder_4x16_1__1100));
  registro_x_y registro_x_y_62 (.i(o), .s(s), .e(e), .y(decoder_4x16_2__0011), .o(o), .x(decoder_4x16_1__1101));
  registro_x_y registro_x_y_63 (.i(o), .s(s), .e(e), .y(decoder_4x16_2__0011), .o(o), .x(decoder_4x16_1__1110));
  registro_x_y registro_x_y_64 (.i(o), .s(s), .e(e), .y(decoder_4x16_2__0011), .o(o), .x(decoder_4x16_1__1111));
  registro_x_y registro_x_y_65 (.i(o), .s(s), .e(e), .y(decoder_4x16_2__0100), .o(o), .x(decoder_4x16_1__0000));
  registro_x_y registro_x_y_66 (.i(o), .s(s), .e(e), .y(decoder_4x16_2__0100), .o(o), .x(decoder_4x16_1__0001));
  registro_x_y registro_x_y_67 (.i(o), .s(s), .e(e), .y(decoder_4x16_2__0100), .o(o), .x(decoder_4x16_1__0010));
  registro_x_y registro_x_y_68 (.i(o), .s(s), .e(e), .y(decoder_4x16_2__0100), .o(o), .x(decoder_4x16_1__0011));
  registro_x_y registro_x_y_69 (.i(o), .s(s), .e(e), .y(decoder_4x16_2__0100), .o(o), .x(decoder_4x16_1__0100));
  registro_x_y registro_x_y_70 (.i(o), .s(s), .e(e), .y(decoder_4x16_2__0100), .o(o), .x(decoder_4x16_1__0101));
  registro_x_y registro_x_y_71 (.i(o), .s(s), .e(e), .y(decoder_4x16_2__0100), .o(o), .x(decoder_4x16_1__0101));
  registro_x_y registro_x_y_72 (.i(o), .s(s), .e(e), .y(decoder_4x16_2__0100), .o(o), .x(decoder_4x16_1__0111));
  registro_x_y registro_x_y_73 (.i(o), .s(s), .e(e), .y(decoder_4x16_2__0100), .o(o), .x(decoder_4x16_1__1000));
  registro_x_y registro_x_y_74 (.i(o), .s(s), .e(e), .y(decoder_4x16_2__0100), .o(o), .x(decoder_4x16_1__1001));
  registro_x_y registro_x_y_75 (.i(o), .s(s), .e(e), .y(decoder_4x16_2__0100), .o(o), .x(decoder_4x16_1__1010));
  registro_x_y registro_x_y_76 (.i(o), .s(s), .e(e), .y(decoder_4x16_2__0100), .o(o), .x(decoder_4x16_1__1011));
  registro_x_y registro_x_y_77 (.i(o), .s(s), .e(e), .y(decoder_4x16_2__0100), .o(o), .x(decoder_4x16_1__1100));
  registro_x_y registro_x_y_78 (.i(o), .s(s), .e(e), .y(decoder_4x16_2__0100), .o(o), .x(decoder_4x16_1__1101));
  registro_x_y registro_x_y_79 (.i(o), .s(s), .e(e), .y(decoder_4x16_2__0100), .o(o), .x(decoder_4x16_1__1110));
  registro_x_y registro_x_y_80 (.i(o), .s(s), .e(e), .y(decoder_4x16_2__0100), .o(o), .x(decoder_4x16_1__1111));
  registro_x_y registro_x_y_81 (.i(o), .s(s), .e(e), .y(decoder_4x16_2__0101), .o(o), .x(decoder_4x16_1__0000));
  registro_x_y registro_x_y_82 (.i(o), .s(s), .e(e), .y(decoder_4x16_2__0101), .o(o), .x(decoder_4x16_1__0001));
  registro_x_y registro_x_y_83 (.i(o), .s(s), .e(e), .y(decoder_4x16_2__0101), .o(o), .x(decoder_4x16_1__0010));
  registro_x_y registro_x_y_84 (.i(o), .s(s), .e(e), .y(decoder_4x16_2__0101), .o(o), .x(decoder_4x16_1__0011));
  registro_x_y registro_x_y_85 (.i(o), .s(s), .e(e), .y(decoder_4x16_2__0101), .o(o), .x(decoder_4x16_1__0100));
  registro_x_y registro_x_y_86 (.i(o), .s(s), .e(e), .y(decoder_4x16_2__0101), .o(o), .x(decoder_4x16_1__0101));
  registro_x_y registro_x_y_87 (.i(o), .s(s), .e(e), .y(decoder_4x16_2__0101), .o(o), .x(decoder_4x16_1__0101));
  registro_x_y registro_x_y_88 (.i(o), .s(s), .e(e), .y(decoder_4x16_2__0101), .o(o), .x(decoder_4x16_1__0111));
  registro_x_y registro_x_y_89 (.i(o), .s(s), .e(e), .y(decoder_4x16_2__0101), .o(o), .x(decoder_4x16_1__1000));
  registro_x_y registro_x_y_90 (.i(o), .s(s), .e(e), .y(decoder_4x16_2__0101), .o(o), .x(decoder_4x16_1__1001));
  registro_x_y registro_x_y_91 (.i(o), .s(s), .e(e), .y(decoder_4x16_2__0101), .o(o), .x(decoder_4x16_1__1010));
  registro_x_y registro_x_y_92 (.i(o), .s(s), .e(e), .y(decoder_4x16_2__0101), .o(o), .x(decoder_4x16_1__1011));
  registro_x_y registro_x_y_93 (.i(o), .s(s), .e(e), .y(decoder_4x16_2__0101), .o(o), .x(decoder_4x16_1__1100));
  registro_x_y registro_x_y_94 (.i(o), .s(s), .e(e), .y(decoder_4x16_2__0101), .o(o), .x(decoder_4x16_1__1101));
  registro_x_y registro_x_y_95 (.i(o), .s(s), .e(e), .y(decoder_4x16_2__0101), .o(o), .x(decoder_4x16_1__1110));
  registro_x_y registro_x_y_96 (.i(o), .s(s), .e(e), .y(decoder_4x16_2__0101), .o(o), .x(decoder_4x16_1__1111));
  registro_x_y registro_x_y_97 (.i(o), .s(s), .e(e), .y(decoder_4x16_2__0110), .o(o), .x(decoder_4x16_1__0000));
  registro_x_y registro_x_y_98 (.i(o), .s(s), .e(e), .y(decoder_4x16_2__0110), .o(o), .x(decoder_4x16_1__0001));
  registro_x_y registro_x_y_99 (.i(o), .s(s), .e(e), .y(decoder_4x16_2__0110), .o(o), .x(decoder_4x16_1__0010));
  registro_x_y registro_x_y_100 (.i(o), .s(s), .e(e), .y(decoder_4x16_2__0110), .o(o), .x(decoder_4x16_1__0011));
  registro_x_y registro_x_y_101 (.i(o), .s(s), .e(e), .y(decoder_4x16_2__0110), .o(o), .x(decoder_4x16_1__0100));
  registro_x_y registro_x_y_102 (.i(o), .s(s), .e(e), .y(decoder_4x16_2__0110), .o(o), .x(decoder_4x16_1__0101));
  registro_x_y registro_x_y_103 (.i(o), .s(s), .e(e), .y(decoder_4x16_2__0110), .o(o), .x(decoder_4x16_1__0101));
  registro_x_y registro_x_y_104 (.i(o), .s(s), .e(e), .y(decoder_4x16_2__0110), .o(o), .x(decoder_4x16_1__0111));
  registro_x_y registro_x_y_105 (.i(o), .s(s), .e(e), .y(decoder_4x16_2__0110), .o(o), .x(decoder_4x16_1__1000));
  registro_x_y registro_x_y_106 (.i(o), .s(s), .e(e), .y(decoder_4x16_2__0110), .o(o), .x(decoder_4x16_1__1001));
  registro_x_y registro_x_y_107 (.i(o), .s(s), .e(e), .y(decoder_4x16_2__0110), .o(o), .x(decoder_4x16_1__1010));
  registro_x_y registro_x_y_108 (.i(o), .s(s), .e(e), .y(decoder_4x16_2__0110), .o(o), .x(decoder_4x16_1__1011));
  registro_x_y registro_x_y_109 (.i(o), .s(s), .e(e), .y(decoder_4x16_2__0110), .o(o), .x(decoder_4x16_1__1100));
  registro_x_y registro_x_y_110 (.i(o), .s(s), .e(e), .y(decoder_4x16_2__0110), .o(o), .x(decoder_4x16_1__1101));
  registro_x_y registro_x_y_111 (.i(o), .s(s), .e(e), .y(decoder_4x16_2__0110), .o(o), .x(decoder_4x16_1__1110));
  registro_x_y registro_x_y_112 (.i(o), .s(s), .e(e), .y(decoder_4x16_2__0110), .o(o), .x(decoder_4x16_1__1111));
  decoder_4x16 decoder_4x16_2 (
    .sel(a[7:4]), ._0000(decoder_4x16_2__0000), ._0001(decoder_4x16_2__0001), ._0010(decoder_4x16_2__0010),
    ._0011(decoder_4x16_2__0011), ._0100(decoder_4x16_2__0100), ._0101(decoder_4x16_2__0101),
    ._0110(decoder_4x16_2__0110), ._0111(decoder_4x16_2__0111), ._1000(decoder_4x16_2__1000),
    ._1001(decoder_4x16_2__1001), ._1010(decoder_4x16_2__1010), ._1011(decoder_4x16_2__1011),
    ._1100(decoder_4x16_2__1100), ._1101(decoder_4x16_2__1101), ._1110(decoder_4x16_2__1110),
    ._1111(decoder_4x16_2__1111));
  registro_x_y registro_x_y_113 (.i(o), .s(s), .e(e), .y(decoder_4x16_2__0111), .o(o), .x(decoder_4x16_1__0000));
  registro_x_y registro_x_y_114 (.i(o), .s(s), .e(e), .y(decoder_4x16_2__0111), .o(o), .x(decoder_4x16_1__0001));
  registro_x_y registro_x_y_115 (.i(o), .s(s), .e(e), .y(decoder_4x16_2__0111), .o(o), .x(decoder_4x16_1__0010));
  registro_x_y registro_x_y_116 (.i(o), .s(s), .e(e), .y(decoder_4x16_2__0111), .o(o), .x(decoder_4x16_1__0011));
  registro_x_y registro_x_y_117 (.i(o), .s(s), .e(e), .y(decoder_4x16_2__0111), .o(o), .x(decoder_4x16_1__0100));
  registro_x_y registro_x_y_118 (.i(o), .s(s), .e(e), .y(decoder_4x16_2__0111), .o(o), .x(decoder_4x16_1__0101));
  registro_x_y registro_x_y_119 (.i(o), .s(s), .e(e), .y(decoder_4x16_2__0111), .o(o), .x(decoder_4x16_1__0101));
  registro_x_y registro_x_y_120 (.i(o), .s(s), .e(e), .y(decoder_4x16_2__0111), .o(o), .x(decoder_4x16_1__0111));
  registro_x_y registro_x_y_121 (.i(o), .s(s), .e(e), .y(decoder_4x16_2__0111), .o(o), .x(decoder_4x16_1__1000));
  registro_x_y registro_x_y_122 (.i(o), .s(s), .e(e), .y(decoder_4x16_2__0111), .o(o), .x(decoder_4x16_1__1001));
  registro_x_y registro_x_y_123 (.i(o), .s(s), .e(e), .y(decoder_4x16_2__0111), .o(o), .x(decoder_4x16_1__1010));
  registro_x_y registro_x_y_124 (.i(o), .s(s), .e(e), .y(decoder_4x16_2__0111), .o(o), .x(decoder_4x16_1__1011));
  registro_x_y registro_x_y_125 (.i(o), .s(s), .e(e), .y(decoder_4x16_2__0111), .o(o), .x(decoder_4x16_1__1100));
  registro_x_y registro_x_y_126 (.i(o), .s(s), .e(e), .y(decoder_4x16_2__0111), .o(o), .x(decoder_4x16_1__1101));
  registro_x_y registro_x_y_127 (.i(o), .s(s), .e(e), .y(decoder_4x16_2__0111), .o(o), .x(decoder_4x16_1__1110));
  registro_x_y registro_x_y_128 (.i(o), .s(s), .e(e), .y(decoder_4x16_2__0111), .o(o), .x(decoder_4x16_1__1111));
  registro_x_y registro_x_y_129 (.i(o), .s(s), .e(e), .y(decoder_4x16_2__1000), .o(o), .x(decoder_4x16_1__0000));
  registro_x_y registro_x_y_130 (.i(o), .s(s), .e(e), .y(decoder_4x16_2__1000), .o(o), .x(decoder_4x16_1__0001));
  registro_x_y registro_x_y_131 (.i(o), .s(s), .e(e), .y(decoder_4x16_2__1000), .o(o), .x(decoder_4x16_1__0010));
  registro_x_y registro_x_y_132 (.i(o), .s(s), .e(e), .y(decoder_4x16_2__1000), .o(o), .x(decoder_4x16_1__0011));
  registro_x_y registro_x_y_133 (.i(o), .s(s), .e(e), .y(decoder_4x16_2__1000), .o(o), .x(decoder_4x16_1__0100));
  registro_x_y registro_x_y_134 (.i(o), .s(s), .e(e), .y(decoder_4x16_2__1000), .o(o), .x(decoder_4x16_1__0101));
  registro_x_y registro_x_y_135 (.i(o), .s(s), .e(e), .y(decoder_4x16_2__1000), .o(o), .x(decoder_4x16_1__0101));
  registro_x_y registro_x_y_136 (.i(o), .s(s), .e(e), .y(decoder_4x16_2__1000), .o(o), .x(decoder_4x16_1__0111));
  registro_x_y registro_x_y_137 (.i(o), .s(s), .e(e), .y(decoder_4x16_2__1000), .o(o), .x(decoder_4x16_1__1000));
  registro_x_y registro_x_y_138 (.i(o), .s(s), .e(e), .y(decoder_4x16_2__1000), .o(o), .x(decoder_4x16_1__1001));
  registro_x_y registro_x_y_139 (.i(o), .s(s), .e(e), .y(decoder_4x16_2__1000), .o(o), .x(decoder_4x16_1__1010));
  registro_x_y registro_x_y_140 (.i(o), .s(s), .e(e), .y(decoder_4x16_2__1000), .o(o), .x(decoder_4x16_1__1011));
  registro_x_y registro_x_y_141 (.i(o), .s(s), .e(e), .y(decoder_4x16_2__1000), .o(o), .x(decoder_4x16_1__1100));
  registro_x_y registro_x_y_142 (.i(o), .s(s), .e(e), .y(decoder_4x16_2__1000), .o(o), .x(decoder_4x16_1__1101));
  registro_x_y registro_x_y_143 (.i(o), .s(s), .e(e), .y(decoder_4x16_2__1000), .o(o), .x(decoder_4x16_1__1110));
  registro_x_y registro_x_y_144 (.i(o), .s(s), .e(e), .y(decoder_4x16_2__1000), .o(o), .x(decoder_4x16_1__1111));
  registro_x_y registro_x_y_145 (.i(o), .s(s), .e(e), .y(decoder_4x16_2__1001), .o(o), .x(decoder_4x16_1__0000));
  registro_x_y registro_x_y_146 (.i(o), .s(s), .e(e), .y(decoder_4x16_2__1001), .o(o), .x(decoder_4x16_1__0001));
  registro_x_y registro_x_y_147 (.i(o), .s(s), .e(e), .y(decoder_4x16_2__1001), .o(o), .x(decoder_4x16_1__0010));
  registro_x_y registro_x_y_148 (.i(o), .s(s), .e(e), .y(decoder_4x16_2__1001), .o(o), .x(decoder_4x16_1__0011));
  registro_x_y registro_x_y_149 (.i(o), .s(s), .e(e), .y(decoder_4x16_2__1001), .o(o), .x(decoder_4x16_1__0100));
  registro_x_y registro_x_y_150 (.i(o), .s(s), .e(e), .y(decoder_4x16_2__1001), .o(o), .x(decoder_4x16_1__0101));
  registro_x_y registro_x_y_151 (.i(o), .s(s), .e(e), .y(decoder_4x16_2__1001), .o(o), .x(decoder_4x16_1__0101));
  registro_x_y registro_x_y_152 (.i(o), .s(s), .e(e), .y(decoder_4x16_2__1001), .o(o), .x(decoder_4x16_1__0111));
  registro_x_y registro_x_y_153 (.i(o), .s(s), .e(e), .y(decoder_4x16_2__1001), .o(o), .x(decoder_4x16_1__1000));
  registro_x_y registro_x_y_154 (.i(o), .s(s), .e(e), .y(decoder_4x16_2__1001), .o(o), .x(decoder_4x16_1__1001));
  registro_x_y registro_x_y_155 (.i(o), .s(s), .e(e), .y(decoder_4x16_2__1001), .o(o), .x(decoder_4x16_1__1010));
  registro_x_y registro_x_y_156 (.i(o), .s(s), .e(e), .y(decoder_4x16_2__1001), .o(o), .x(decoder_4x16_1__1011));
  registro_x_y registro_x_y_157 (.i(o), .s(s), .e(e), .y(decoder_4x16_2__1001), .o(o), .x(decoder_4x16_1__1100));
  registro_x_y registro_x_y_158 (.i(o), .s(s), .e(e), .y(decoder_4x16_2__1001), .o(o), .x(decoder_4x16_1__1101));
  registro_x_y registro_x_y_159 (.i(o), .s(s), .e(e), .y(decoder_4x16_2__1001), .o(o), .x(decoder_4x16_1__1110));
  registro_x_y registro_x_y_160 (.i(o), .s(s), .e(e), .y(decoder_4x16_2__1001), .o(o), .x(decoder_4x16_1__1111));
  registro_x_y registro_x_y_161 (.i(o), .s(s), .e(e), .y(decoder_4x16_2__1010), .o(o), .x(decoder_4x16_1__0000));
  registro_x_y registro_x_y_162 (.i(o), .s(s), .e(e), .y(decoder_4x16_2__1010), .o(o), .x(decoder_4x16_1__0001));
  registro_x_y registro_x_y_163 (.i(o), .s(s), .e(e), .y(decoder_4x16_2__1010), .o(o), .x(decoder_4x16_1__0010));
  registro_x_y registro_x_y_164 (.i(o), .s(s), .e(e), .y(decoder_4x16_2__1010), .o(o), .x(decoder_4x16_1__0011));
  registro_x_y registro_x_y_165 (.i(o), .s(s), .e(e), .y(decoder_4x16_2__1010), .o(o), .x(decoder_4x16_1__0100));
  registro_x_y registro_x_y_166 (.i(o), .s(s), .e(e), .y(decoder_4x16_2__1010), .o(o), .x(decoder_4x16_1__0101));
  registro_x_y registro_x_y_167 (.i(o), .s(s), .e(e), .y(decoder_4x16_2__1010), .o(o), .x(decoder_4x16_1__0101));
  registro_x_y registro_x_y_168 (.i(o), .s(s), .e(e), .y(decoder_4x16_2__1010), .o(o), .x(decoder_4x16_1__0111));
  registro_x_y registro_x_y_169 (.i(o), .s(s), .e(e), .y(decoder_4x16_2__1010), .o(o), .x(decoder_4x16_1__1000));
  registro_x_y registro_x_y_170 (.i(o), .s(s), .e(e), .y(decoder_4x16_2__1010), .o(o), .x(decoder_4x16_1__1001));
  registro_x_y registro_x_y_171 (.i(o), .s(s), .e(e), .y(decoder_4x16_2__1010), .o(o), .x(decoder_4x16_1__1010));
  registro_x_y registro_x_y_172 (.i(o), .s(s), .e(e), .y(decoder_4x16_2__1010), .o(o), .x(decoder_4x16_1__1011));
  registro_x_y registro_x_y_173 (.i(o), .s(s), .e(e), .y(decoder_4x16_2__1010), .o(o), .x(decoder_4x16_1__1100));
  registro_x_y registro_x_y_174 (.i(o), .s(s), .e(e), .y(decoder_4x16_2__1010), .o(o), .x(decoder_4x16_1__1101));
  registro_x_y registro_x_y_175 (.i(o), .s(s), .e(e), .y(decoder_4x16_2__1010), .o(o), .x(decoder_4x16_1__1110));
  registro_x_y registro_x_y_176 (.i(o), .s(s), .e(e), .y(decoder_4x16_2__1010), .o(o), .x(decoder_4x16_1__1111));
  registro_x_y registro_x_y_177 (.i(o), .s(s), .e(e), .y(decoder_4x16_2__1011), .o(o), .x(decoder_4x16_1__0000));
  registro_x_y registro_x_y_178 (.i(o), .s(s), .e(e), .y(decoder_4x16_2__1011), .o(o), .x(decoder_4x16_1__0001));
  registro_x_y registro_x_y_179 (.i(o), .s(s), .e(e), .y(decoder_4x16_2__1011), .o(o), .x(decoder_4x16_1__0010));
  registro_x_y registro_x_y_180 (.i(o), .s(s), .e(e), .y(decoder_4x16_2__1011), .o(o), .x(decoder_4x16_1__0011));
  registro_x_y registro_x_y_181 (.i(o), .s(s), .e(e), .y(decoder_4x16_2__1011), .o(o), .x(decoder_4x16_1__0100));
  registro_x_y registro_x_y_182 (.i(o), .s(s), .e(e), .y(decoder_4x16_2__1011), .o(o), .x(decoder_4x16_1__0101));
  registro_x_y registro_x_y_183 (.i(o), .s(s), .e(e), .y(decoder_4x16_2__1011), .o(o), .x(decoder_4x16_1__0101));
  registro_x_y registro_x_y_184 (.i(o), .s(s), .e(e), .y(decoder_4x16_2__1011), .o(o), .x(decoder_4x16_1__0111));
  registro_x_y registro_x_y_185 (.i(o), .s(s), .e(e), .y(decoder_4x16_2__1011), .o(o), .x(decoder_4x16_1__1000));
  registro_x_y registro_x_y_186 (.i(o), .s(s), .e(e), .y(decoder_4x16_2__1011), .o(o), .x(decoder_4x16_1__1001));
  registro_x_y registro_x_y_187 (.i(o), .s(s), .e(e), .y(decoder_4x16_2__1011), .o(o), .x(decoder_4x16_1__1010));
  registro_x_y registro_x_y_188 (.i(o), .s(s), .e(e), .y(decoder_4x16_2__1011), .o(o), .x(decoder_4x16_1__1011));
  registro_x_y registro_x_y_189 (.i(o), .s(s), .e(e), .y(decoder_4x16_2__1011), .o(o), .x(decoder_4x16_1__1100));
  registro_x_y registro_x_y_190 (.i(o), .s(s), .e(e), .y(decoder_4x16_2__1011), .o(o), .x(decoder_4x16_1__1101));
  registro_x_y registro_x_y_191 (.i(o), .s(s), .e(e), .y(decoder_4x16_2__1011), .o(o), .x(decoder_4x16_1__1110));
  registro_x_y registro_x_y_192 (.i(o), .s(s), .e(e), .y(decoder_4x16_2__1011), .o(o), .x(decoder_4x16_1__1111));
  registro_x_y registro_x_y_193 (.i(o), .s(s), .e(e), .y(decoder_4x16_2__1100), .o(o), .x(decoder_4x16_1__0000));
  registro_x_y registro_x_y_194 (.i(o), .s(s), .e(e), .y(decoder_4x16_2__1100), .o(o), .x(decoder_4x16_1__0001));
  registro_x_y registro_x_y_195 (.i(o), .s(s), .e(e), .y(decoder_4x16_2__1100), .o(o), .x(decoder_4x16_1__0010));
  registro_x_y registro_x_y_196 (.i(o), .s(s), .e(e), .y(decoder_4x16_2__1100), .o(o), .x(decoder_4x16_1__0011));
  registro_x_y registro_x_y_197 (.i(o), .s(s), .e(e), .y(decoder_4x16_2__1100), .o(o), .x(decoder_4x16_1__0100));
  registro_x_y registro_x_y_198 (.i(o), .s(s), .e(e), .y(decoder_4x16_2__1100), .o(o), .x(decoder_4x16_1__0101));
  registro_x_y registro_x_y_199 (.i(o), .s(s), .e(e), .y(decoder_4x16_2__1100), .o(o), .x(decoder_4x16_1__0101));
  registro_x_y registro_x_y_200 (.i(o), .s(s), .e(e), .y(decoder_4x16_2__1100), .o(o), .x(decoder_4x16_1__0111));
  registro_x_y registro_x_y_201 (.i(o), .s(s), .e(e), .y(decoder_4x16_2__1100), .o(o), .x(decoder_4x16_1__1000));
  registro_x_y registro_x_y_202 (.i(o), .s(s), .e(e), .y(decoder_4x16_2__1100), .o(o), .x(decoder_4x16_1__1001));
  registro_x_y registro_x_y_203 (.i(o), .s(s), .e(e), .y(decoder_4x16_2__1100), .o(o), .x(decoder_4x16_1__1010));
  registro_x_y registro_x_y_204 (.i(o), .s(s), .e(e), .y(decoder_4x16_2__1100), .o(o), .x(decoder_4x16_1__1011));
  registro_x_y registro_x_y_205 (.i(o), .s(s), .e(e), .y(decoder_4x16_2__1100), .o(o), .x(decoder_4x16_1__1100));
  registro_x_y registro_x_y_206 (.i(o), .s(s), .e(e), .y(decoder_4x16_2__1100), .o(o), .x(decoder_4x16_1__1101));
  registro_x_y registro_x_y_207 (.i(o), .s(s), .e(e), .y(decoder_4x16_2__1100), .o(o), .x(decoder_4x16_1__1110));
  registro_x_y registro_x_y_208 (.i(o), .s(s), .e(e), .y(decoder_4x16_2__1100), .o(o), .x(decoder_4x16_1__1111));
  registro_x_y registro_x_y_209 (.i(o), .s(s), .e(e), .y(decoder_4x16_2__1101), .o(o), .x(decoder_4x16_1__0000));
  registro_x_y registro_x_y_210 (.i(o), .s(s), .e(e), .y(decoder_4x16_2__1101), .o(o), .x(decoder_4x16_1__0001));
  registro_x_y registro_x_y_211 (.i(o), .s(s), .e(e), .y(decoder_4x16_2__1101), .o(o), .x(decoder_4x16_1__0010));
  registro_x_y registro_x_y_212 (.i(o), .s(s), .e(e), .y(decoder_4x16_2__1101), .o(o), .x(decoder_4x16_1__0011));
  registro_x_y registro_x_y_213 (.i(o), .s(s), .e(e), .y(decoder_4x16_2__1101), .o(o), .x(decoder_4x16_1__0100));
  registro_x_y registro_x_y_214 (.i(o), .s(s), .e(e), .y(decoder_4x16_2__1101), .o(o), .x(decoder_4x16_1__0101));
  registro_x_y registro_x_y_215 (.i(o), .s(s), .e(e), .y(decoder_4x16_2__1101), .o(o), .x(decoder_4x16_1__0101));
  registro_x_y registro_x_y_216 (.i(o), .s(s), .e(e), .y(decoder_4x16_2__1101), .o(o), .x(decoder_4x16_1__0111));
  registro_x_y registro_x_y_217 (.i(o), .s(s), .e(e), .y(decoder_4x16_2__1101), .o(o), .x(decoder_4x16_1__1000));
  registro_x_y registro_x_y_218 (.i(o), .s(s), .e(e), .y(decoder_4x16_2__1101), .o(o), .x(decoder_4x16_1__1001));
  registro_x_y registro_x_y_219 (.i(o), .s(s), .e(e), .y(decoder_4x16_2__1101), .o(o), .x(decoder_4x16_1__1010));
  registro_x_y registro_x_y_220 (.i(o), .s(s), .e(e), .y(decoder_4x16_2__1101), .o(o), .x(decoder_4x16_1__1011));
  registro_x_y registro_x_y_221 (.i(o), .s(s), .e(e), .y(decoder_4x16_2__1101), .o(o), .x(decoder_4x16_1__1100));
  registro_x_y registro_x_y_222 (.i(o), .s(s), .e(e), .y(decoder_4x16_2__1101), .o(o), .x(decoder_4x16_1__1101));
  registro_x_y registro_x_y_223 (.i(o), .s(s), .e(e), .y(decoder_4x16_2__1101), .o(o), .x(decoder_4x16_1__1110));
  registro_x_y registro_x_y_224 (.i(o), .s(s), .e(e), .y(decoder_4x16_2__1101), .o(o), .x(decoder_4x16_1__1111));
  registro_x_y registro_x_y_225 (.i(o), .s(s), .e(e), .y(decoder_4x16_2__1110), .o(o), .x(decoder_4x16_1__0000));
  registro_x_y registro_x_y_226 (.i(o), .s(s), .e(e), .y(decoder_4x16_2__1110), .o(o), .x(decoder_4x16_1__0001));
  registro_x_y registro_x_y_227 (.i(o), .s(s), .e(e), .y(decoder_4x16_2__1110), .o(o), .x(decoder_4x16_1__0010));
  registro_x_y registro_x_y_228 (.i(o), .s(s), .e(e), .y(decoder_4x16_2__1110), .o(o), .x(decoder_4x16_1__0011));
  registro_x_y registro_x_y_229 (.i(o), .s(s), .e(e), .y(decoder_4x16_2__1110), .o(o), .x(decoder_4x16_1__0100));
  registro_x_y registro_x_y_230 (.i(o), .s(s), .e(e), .y(decoder_4x16_2__1110), .o(o), .x(decoder_4x16_1__0101));
  registro_x_y registro_x_y_231 (.i(o), .s(s), .e(e), .y(decoder_4x16_2__1110), .o(o), .x(decoder_4x16_1__0101));
  registro_x_y registro_x_y_232 (.i(o), .s(s), .e(e), .y(decoder_4x16_2__1110), .o(o), .x(decoder_4x16_1__0111));
  registro_x_y registro_x_y_233 (.i(o), .s(s), .e(e), .y(decoder_4x16_2__1110), .o(o), .x(decoder_4x16_1__1000));
  registro_x_y registro_x_y_234 (.i(o), .s(s), .e(e), .y(decoder_4x16_2__1110), .o(o), .x(decoder_4x16_1__1001));
  registro_x_y registro_x_y_235 (.i(o), .s(s), .e(e), .y(decoder_4x16_2__1110), .o(o), .x(decoder_4x16_1__1010));
  registro_x_y registro_x_y_236 (.i(o), .s(s), .e(e), .y(decoder_4x16_2__1110), .o(o), .x(decoder_4x16_1__1011));
  registro_x_y registro_x_y_237 (.i(o), .s(s), .e(e), .y(decoder_4x16_2__1110), .o(o), .x(decoder_4x16_1__1100));
  registro_x_y registro_x_y_238 (.i(o), .s(s), .e(e), .y(decoder_4x16_2__1110), .o(o), .x(decoder_4x16_1__1101));
  registro_x_y registro_x_y_239 (.i(o), .s(s), .e(e), .y(decoder_4x16_2__1110), .o(o), .x(decoder_4x16_1__1110));
  registro_x_y registro_x_y_240 (.i(o), .s(s), .e(e), .y(decoder_4x16_2__1110), .o(o), .x(decoder_4x16_1__1111));
  registro_x_y registro_x_y_241 (.i(o), .s(s), .e(e), .y(decoder_4x16_2__1111), .o(o), .x(decoder_4x16_1__0000));
  registro_x_y registro_x_y_242 (.i(o), .s(s), .e(e), .y(decoder_4x16_2__1111), .o(o), .x(decoder_4x16_1__0001));
  registro_x_y registro_x_y_243 (.i(o), .s(s), .e(e), .y(decoder_4x16_2__1111), .o(o), .x(decoder_4x16_1__0010));
  registro_x_y registro_x_y_244 (.i(o), .s(s), .e(e), .y(decoder_4x16_2__1111), .o(o), .x(decoder_4x16_1__0011));
  registro_x_y registro_x_y_245 (.i(o), .s(s), .e(e), .y(decoder_4x16_2__1111), .o(o), .x(decoder_4x16_1__0100));
  registro_x_y registro_x_y_246 (.i(o), .s(s), .e(e), .y(decoder_4x16_2__1111), .o(o), .x(decoder_4x16_1__0101));
  registro_x_y registro_x_y_247 (.i(o), .s(s), .e(e), .y(decoder_4x16_2__1111), .o(o), .x(decoder_4x16_1__0101));
  registro_x_y registro_x_y_248 (.i(o), .s(s), .e(e), .y(decoder_4x16_2__1111), .o(o), .x(decoder_4x16_1__0111));
  registro_x_y registro_x_y_249 (.i(o), .s(s), .e(e), .y(decoder_4x16_2__1111), .o(o), .x(decoder_4x16_1__1000));
  registro_x_y registro_x_y_250 (.i(o), .s(s), .e(e), .y(decoder_4x16_2__1111), .o(o), .x(decoder_4x16_1__1001));
  registro_x_y registro_x_y_251 (.i(o), .s(s), .e(e), .y(decoder_4x16_2__1111), .o(o), .x(decoder_4x16_1__1010));
  registro_x_y registro_x_y_252 (.i(o), .s(s), .e(e), .y(decoder_4x16_2__1111), .o(o), .x(decoder_4x16_1__1011));
  registro_x_y registro_x_y_253 (.i(o), .s(s), .e(e), .y(decoder_4x16_2__1111), .o(o), .x(decoder_4x16_1__1100));
  registro_x_y registro_x_y_254 (.i(o), .s(s), .e(e), .y(decoder_4x16_2__1111), .o(o), .x(decoder_4x16_1__1101));
  registro_x_y registro_x_y_255 (.i(o), .s(s), .e(e), .y(decoder_4x16_2__1111), .o(o), .x(decoder_4x16_1__1110));
  registro_x_y registro_x_y_256 (.i(o), .s(s), .e(e), .y(decoder_4x16_2__1111), .o(o), .x(decoder_4x16_1__1111));

  // Notes on the sheet:
  //   a: address
endmodule
