// Digital circuit Temporary_register.dig as structural Verilog
module Temporary_register (
  input  [7:0] i,
  input  s,
  output [7:0] o
);

  mem_1bit mem_1bit_1 (.i(i[0]), .s(s), .o(o[0]));
  mem_1bit mem_1bit_2 (.i(i[1]), .s(s), .o(o[1]));
  mem_1bit mem_1bit_3 (.i(i[2]), .s(s), .o(o[2]));
  mem_1bit mem_1bit_4 (.i(i[3]), .s(s), .o(o[3]));
  mem_1bit mem_1bit_5 (.i(i[4]), .s(s), .o(o[4]));
  mem_1bit mem_1bit_6 (.i(i[5]), .s(s), .o(o[5]));
  mem_1bit mem_1bit_7 (.i(i[6]), .s(s), .o(o[6]));
  mem_1bit mem_1bit_8 (.i(i[7]), .s(s), .o(o[7]));
endmodule
