// Digital circuit XORer.dig as structural Verilog
module XORer (
  input  [7:0] i,
  input  e,
  input  [7:0] i2,
  output [7:0] o
);

  wire [7:0] enabler_and_1_o, enabler_and_2_o, xor_2_out;

  enabler_and enabler_and_1 (.o(enabler_and_1_o), .i(i), .e(e));
  enabler_and enabler_and_2 (.o(enabler_and_2_o), .i(i2), .e(e));
  xor xor_1 (xor_2_out[0], enabler_and_2_o[0], enabler_and_1_o[0]);
  xor xor_2 (xor_2_out[1], enabler_and_2_o[1], enabler_and_1_o[1]);
  xor xor_3 (xor_2_out[2], enabler_and_2_o[2], enabler_and_1_o[2]);
  xor xor_4 (xor_2_out[3], enabler_and_2_o[3], enabler_and_1_o[3]);
  xor xor_5 (xor_2_out[4], enabler_and_2_o[4], enabler_and_1_o[4]);
  xor xor_6 (xor_2_out[5], enabler_and_2_o[5], enabler_and_1_o[5]);
  xor xor_7 (xor_2_out[6], enabler_and_2_o[6], enabler_and_1_o[6]);
  xor xor_8 (xor_2_out[7], enabler_and_2_o[7], enabler_and_1_o[7]);
  enabler_high_impedance enabler_high_impedance_1 (.o(o), .i(xor_2_out), .e(e));
endmodule
