// Digital circuit and_nand.dig as structural Verilog
module and_nand (
  input  i1,
  input  i2,
  output o
);

  wire nand_tr_1_o;

  nand_tr nand_tr_1 (.i1(i1), .i2(i2), .o(nand_tr_1_o));
  not_nand not_nand_1 (.i(nand_tr_1_o), .o(o));
endmodule
