// Digital circuit buffer_high_impedance.dig as structural Verilog
module buffer_high_impedance (
  input  i,
  input  e,
  output o
);

  wire nand_tr_1_o, not_nand_1_o, or_nand_1_o;

  PullDown pulldown_1 (.out(i));
  PullDown pulldown_2 (.out(e));
  nand_tr nand_tr_1 (.i1(i), .i2(e), .o(nand_tr_1_o));
  not_nand not_nand_1 (.i(e), .o(not_nand_1_o));
  PFET pfet_1 (.G(nand_tr_1_o), .S(1'b1), .D(o));
  or_nand or_nand_1 (.i1(not_nand_1_o), .i2(i), .o(or_nand_1_o));
  PFET pfet_2 (.G(or_nand_1_o), .S(o), .D(1'b0));
endmodule
