// Digital circuit decoder_3x8.dig as structural Verilog
module decoder_3x8 (
  input  [2:0] sel,
  output _000,
  output _001,
  output _010,
  output _011,
  output _100,
  output _101,
  output _110,
  output _111
);

  wire and_nand_1_o, and_nand_2_o, and_nand_3_o, and_nand_4_o, and_nand_5_o, and_nand_6_o, and_nand_7_o,
       and_nand_8_o, not_nand_1_o, not_nand_2_o, not_nand_3_o;

  not_nand not_nand_1 (.i(sel[2]), .o(not_nand_1_o));
  not_nand not_nand_2 (.i(sel[1]), .o(not_nand_2_o));
  not_nand not_nand_3 (.i(sel[0]), .o(not_nand_3_o));
  and_nand and_nand_1 (.i1(sel[0]), .i2(sel[1]), .o(and_nand_1_o));
  and_nand and_nand_2 (.i1(not_nand_3_o), .i2(sel[1]), .o(and_nand_2_o));
  and_nand and_nand_3 (.i1(sel[0]), .i2(not_nand_2_o), .o(and_nand_3_o));
  and_nand and_nand_4 (.i1(not_nand_3_o), .i2(not_nand_2_o), .o(and_nand_4_o));
  and_nand and_nand_5 (.i1(sel[0]), .i2(sel[1]), .o(and_nand_5_o));
  and_nand and_nand_6 (.i1(not_nand_3_o), .i2(sel[1]), .o(and_nand_6_o));
  and_nand and_nand_7 (.i1(sel[0]), .i2(not_nand_2_o), .o(and_nand_7_o));
  and_nand and_nand_8 (.i1(not_nand_3_o), .i2(not_nand_2_o), .o(and_nand_8_o));
  and_nand and_nand_9 (.i1(and_nand_1_o), .i2(sel[2]), .o(_111));
  and_nand and_nand_10 (.i1(and_nand_2_o), .i2(sel[2]), .o(_110));
  and_nand and_nand_11 (.i1(and_nand_3_o), .i2(sel[2]), .o(_101));
  and_nand and_nand_12 (.i1(and_nand_4_o), .i2(sel[2]), .o(_100));
  and_nand and_nand_13 (.i1(and_nand_5_o), .i2(not_nand_1_o), .o(_011));
  and_nand and_nand_14 (.i1(and_nand_6_o), .i2(not_nand_1_o), .o(_010));
  and_nand and_nand_15 (.i1(and_nand_7_o), .i2(not_nand_1_o), .o(_001));
  and_nand and_nand_16 (.i1(and_nand_8_o), .i2(not_nand_1_o), .o(_000));
endmodule
