// Digital circuit decoder_4x16.dig as structural Verilog
module decoder_4x16 (
  input  [3:0] sel,
  output _0000,
  output _0001,
  output _0010,
  output _0011,
  output _0100,
  output _0101,
  output _0110,
  output _0111,
  output _1000,
  output _1001,
  output _1010,
  output _1011,
  output _1100,
  output _1101,
  output _1110,
  output _1111
);

  wire not_1_out, not_2_out, not_3_out, not_4_out;

  not not_1 (not_1_out, sel[3]);
  not not_2 (not_2_out, sel[1]);
  not not_3 (not_3_out, sel[2]);
  not not_4 (not_4_out, sel[0]);
  and and_1 (_1111, sel[0], sel[1], sel[2], sel[3]);
  and and_2 (_1110, not_4_out, sel[1], sel[2], sel[3]);
  and and_3 (_1101, sel[0], not_2_out, sel[2], sel[3]);
  and and_4 (_1100, not_4_out, not_2_out, sel[2], sel[3]);
  and and_5 (_1011, sel[0], sel[1], not_3_out, sel[3]);
  and and_6 (_1010, not_4_out, sel[1], not_3_out, sel[3]);
  and and_7 (_1001, sel[0], not_2_out, not_3_out, sel[3]);
  and and_8 (_1000, not_4_out, not_2_out, not_3_out, sel[3]);
  and and_9 (_0111, sel[0], sel[1], sel[2], not_1_out);
  and and_10 (_0110, not_4_out, sel[1], sel[2], not_1_out);
  and and_11 (_0101, sel[0], not_2_out, sel[2], not_1_out);
  and and_12 (_0100, not_4_out, not_2_out, sel[2], not_1_out);
  and and_13 (_0011, sel[0], sel[1], not_3_out, not_1_out);
  and and_14 (_0010, not_4_out, sel[1], not_3_out, not_1_out);
  and and_15 (_0001, sel[0], not_2_out, not_3_out, not_1_out);
  and and_16 (_0000, not_4_out, not_2_out, not_3_out, not_1_out);
endmodule
