// Digital circuit enabler_and.dig as structural Verilog
module enabler_and (
  input  [7:0] i,
  input  e,
  output [7:0] o
);

  and and_1 (o[0], i[0], e);
  and and_2 (o[1], i[1], e);
  and and_3 (o[2], i[2], e);
  and and_4 (o[3], i[3], e);
  and and_5 (o[4], i[4], e);
  and and_6 (o[5], i[5], e);
  and and_7 (o[6], i[6], e);
  and and_8 (o[7], i[7], e);
endmodule
