// Digital circuit enabler_high_impedance.dig as structural Verilog
module enabler_high_impedance (
  input  [7:0] i,
  input  e,
  output [7:0] o
);

  buffer_high_impedance buffer_high_impedance_1 (.i(i[0]), .e(e), .o(o[0]));
  buffer_high_impedance buffer_high_impedance_2 (.i(i[1]), .e(e), .o(o[1]));
  buffer_high_impedance buffer_high_impedance_3 (.i(i[2]), .e(e), .o(o[2]));
  buffer_high_impedance buffer_high_impedance_4 (.i(i[3]), .e(e), .o(o[3]));
  buffer_high_impedance buffer_high_impedance_5 (.i(i[4]), .e(e), .o(o[4]));
  buffer_high_impedance buffer_high_impedance_6 (.i(i[5]), .e(e), .o(o[5]));
  buffer_high_impedance buffer_high_impedance_7 (.i(i[6]), .e(e), .o(o[6]));
  buffer_high_impedance buffer_high_impedance_8 (.i(i[7]), .e(e), .o(o[7]));
endmodule
