// Digital circuit main.dig as structural Verilog
module main (
  input  in_1,
  input  in_2,
  input  in_3,
  input  in_4,
  input  in_5,
  input  in_6,
  input  in_7,
  input  in_8,
  input  in_9,
  input  in_10,
  input  in_11
);

  wire [3:0] R0_p1, R0_p1_2;
  wire [7:0] MAR_out;

  Seven_Seg_Hex seven_seg_hex_1 (.d(R0_p1_2), .dp(1'b0));
  Seven_Seg_Hex seven_seg_hex_2 (.d(R0_p1), .dp(1'b0));
  // registro R0: pin names not known; wires that end beside it: {R0_p1_2, R0_p1}, in_1, {R0_p1_2, R0_p1}, in_2
  // registro R1: pin names not known; wires that end beside it: {R0_p1_2, R0_p1}, in_3, {R0_p1_2, R0_p1}, in_4
  // registro R2: pin names not known; wires that end beside it: {R0_p1_2, R0_p1}, in_5, {R0_p1_2, R0_p1}, in_6
  // registro R3: pin names not known; wires that end beside it: {R0_p1_2, R0_p1}, in_7, {R0_p1_2, R0_p1}, in_8
  MAR MAR (.out(MAR_out), .in({R0_p1_2, R0_p1}), .s(in_9));
  RAM RAM (.a(MAR_out), .s(in_10), .e(in_11), .o({R0_p1_2, R0_p1}), .i({R0_p1_2, R0_p1}));
  Seven_Seg_Hex seven_seg_hex_3 (.d(MAR_out[7:4]), .dp(1'b0));
  Seven_Seg_Hex seven_seg_hex_4 (.d(MAR_out[3:0]), .dp(1'b0));

  // Notes on the sheet:
  //   Datos del bus
  //   Address
endmodule
