// Digital circuit main_PC_clark.dig as structural Verilog
module main_PC_clark (
  input  [7:0] address,
  input  [7:0] input_bus,
  input  clk,
  input  in_4,
  input  in_5,
  input  in_6
);

  wire and_1_out, delay_1_out, or_1_out;
  wire [3:0] registro_1_out, registro_1_out_2;
  wire [7:0] mar_1_out, ram_1_o;

  Seven_Seg_Hex seven_seg_hex_1 (.d(input_bus[7:4]), .dp(1'b0));
  Seven_Seg_Hex seven_seg_hex_2 (.d(input_bus[3:0]), .dp(1'b0));
  Button button_1 ();  // open: out
  Delay #(.delayTime(5)) delay_1 (.in(in_4), .out(delay_1_out));
  or or_1 (or_1_out, in_4, delay_1_out);
  and and_1 (and_1_out, in_4, delay_1_out);
  MAR mar_1 (.in(address), .s(in_6), .out(mar_1_out));
  RAM ram_1 (.a(mar_1_out), .e(or_1_out), .s(in_5), .i(input_bus), .o(ram_1_o));
  Seven_Seg_Hex seven_seg_hex_3 (.d(ram_1_o[7:4]), .dp(1'b0));
  Seven_Seg_Hex seven_seg_hex_4 (.d(ram_1_o[3:0]), .dp(1'b0));
  registro registro_1 (.in(ram_1_o), .s(and_1_out), .e(1'b1), .out({registro_1_out_2, registro_1_out}));
  Seven_Seg_Hex seven_seg_hex_5 (.d(registro_1_out_2), .dp(1'b0));
  Seven_Seg_Hex seven_seg_hex_6 (.d(registro_1_out), .dp(1'b0));
endmodule
