// Digital circuit nand_tr.dig as structural Verilog
module nand_tr (
  input  i1,
  input  i2,
  output o
);

  wire nfet_1_s, pullup_1_out;

  PullUp pullup_1 (.out(pullup_1_out));
  PFET #(.unidirectional("true")) pfet_1 (.G(i1), .S(pullup_1_out), .D(o));
  NFET #(.unidirectional("true")) nfet_1 (.G(i1), .D(o), .S(nfet_1_s));
  NFET #(.unidirectional("true")) nfet_2 (.G(i2), .D(nfet_1_s), .S(1'b0));
  PFET #(.unidirectional("true")) pfet_2 (.G(i2), .S(pullup_1_out), .D(o));
endmodule
