// Digital circuit nand_tr_back.dig as structural Verilog
module nand_tr_back (
  input  i1,
  input  i2,
  output o
);

  wire nfet_1_s;

  NFET #(.unidirectional("true")) nfet_1 (.G(i1), .D(o), .S(nfet_1_s));
  NFET #(.unidirectional("true")) nfet_2 (.G(i2), .D(nfet_1_s), .S(1'b0));
  PullUp pullup_1 (.out(o));
endmodule
