// Digital circuit registro.dig as structural Verilog
module registro (
  input  [7:0] in,
  input  s,
  input  e,
  output [7:0] out
);

  wire mem_1bit_1_o, mem_1bit_2_o, mem_1bit_3_o, mem_1bit_4_o, mem_1bit_5_o, mem_1bit_6_o, mem_1bit_7_o,
       mem_1bit_8_o;

  mem_1bit mem_1bit_1 (.i(in[0]), .s(s), .o(mem_1bit_1_o));
  mem_1bit mem_1bit_2 (.i(in[1]), .s(s), .o(mem_1bit_2_o));
  mem_1bit mem_1bit_3 (.i(in[2]), .s(s), .o(mem_1bit_3_o));
  mem_1bit mem_1bit_4 (.i(in[3]), .s(s), .o(mem_1bit_4_o));
  mem_1bit mem_1bit_5 (.i(in[4]), .s(s), .o(mem_1bit_5_o));
  mem_1bit mem_1bit_6 (.i(in[5]), .s(s), .o(mem_1bit_6_o));
  mem_1bit mem_1bit_7 (.i(in[6]), .s(s), .o(mem_1bit_7_o));
  mem_1bit mem_1bit_8 (.i(in[7]), .s(s), .o(mem_1bit_8_o));
  buffer_high_impedance buffer_high_impedance_1 (.i(mem_1bit_1_o), .e(e), .o(out[0]));
  buffer_high_impedance buffer_high_impedance_2 (.i(mem_1bit_2_o), .e(e), .o(out[1]));
  buffer_high_impedance buffer_high_impedance_3 (.i(mem_1bit_3_o), .e(e), .o(out[2]));
  buffer_high_impedance buffer_high_impedance_4 (.i(mem_1bit_4_o), .e(e), .o(out[3]));
  buffer_high_impedance buffer_high_impedance_5 (.i(mem_1bit_5_o), .e(e), .o(out[4]));
  buffer_high_impedance buffer_high_impedance_6 (.i(mem_1bit_6_o), .e(e), .o(out[5]));
  buffer_high_impedance buffer_high_impedance_7 (.i(mem_1bit_7_o), .e(e), .o(out[6]));
  buffer_high_impedance buffer_high_impedance_8 (.i(mem_1bit_8_o), .e(e), .o(out[7]));
endmodule
