// Digital circuit registro_always_e.dig as structural Verilog
module registro_always_e (
  input  [7:0] in,
  input  s,
  output [7:0] out
);

  mem_1bit mem_1bit_1 (.i(in[0]), .s(s), .o(out[0]));
  mem_1bit mem_1bit_2 (.i(in[1]), .s(s), .o(out[1]));
  mem_1bit mem_1bit_3 (.i(in[2]), .s(s), .o(out[2]));
  mem_1bit mem_1bit_4 (.i(in[3]), .s(s), .o(out[3]));
  mem_1bit mem_1bit_5 (.i(in[4]), .s(s), .o(out[4]));
  mem_1bit mem_1bit_6 (.i(in[5]), .s(s), .o(out[5]));
  mem_1bit mem_1bit_7 (.i(in[6]), .s(s), .o(out[6]));
  mem_1bit mem_1bit_8 (.i(in[7]), .s(s), .o(out[7]));
endmodule
