// Digital circuit registro_x_y.dig as structural Verilog
module registro_x_y (
  input  [7:0] i,
  input  s,
  input  e,
  input  y,
  input  x,
  output [7:0] o
);

  wire and_1_out, and_2_out, and_3_out;

  and and_1 (and_1_out, y, x);
  and and_2 (and_2_out, s, and_1_out);
  and and_3 (and_3_out, e, and_1_out);
  registro registro_1 (.in(i), .s(and_2_out), .e(and_3_out), .out(o));
endmodule
