// Digital circuit shifter_left.dig as structural Verilog
module shifter_left (
  input  [7:0] i,
  input  e,
  input  si,
  output [7:0] o,
  output so
);

  enabler_high_impedance enabler_high_impedance_1 (.o({so, o[7:1]}), .i(i), .e(e));
  buffer_high_impedance buffer_high_impedance_1 (.i(si), .e(e), .o(o[0]));

  // Notes on the sheet:
  //   si: shift in
  //   so: shift out
endmodule
