// Digital circuit shifter_right.dig as structural Verilog
module shifter_right (
  input  [7:0] i,
  input  e,
  input  si,
  output [7:0] o,
  output so
);

  enabler_and enabler_and_1 (.o({so, o[7:1]}), .i(i), .e(e));

  assign o[0] = si;

  // Notes on the sheet:
  //   si: shift in
  //   so: shift out
endmodule
