// Digital circuit xor_nand.dig as structural Verilog
module xor_nand (
  input  i1,
  input  i2,
  output o
);

  wire nand_tr_1_o, nand_tr_2_o, not_nand_1_o, not_nand_2_o;

  not_nand not_nand_1 (.i(i1), .o(not_nand_1_o));
  not_nand not_nand_2 (.i(i2), .o(not_nand_2_o));
  nand_tr nand_tr_1 (.i1(not_nand_1_o), .i2(i2), .o(nand_tr_1_o));
  nand_tr nand_tr_2 (.i1(i1), .i2(not_nand_2_o), .o(nand_tr_2_o));
  nand_tr nand_tr_3 (.i1(nand_tr_1_o), .i2(nand_tr_2_o), .o(o));
endmodule
