// Digital circuit main_PC_clark.dig as structural Verilog
module main_PC_clark (
  input  [7:0] address,
  input  enabler,
  input  set,
  input  [7:0] input_bus
);

  wire [3:0] ram_1_o, ram_1_o_2;

  Seven_Seg_Hex seven_seg_hex_1 (.d(input_bus[7:4]), .dp(1'b0));
  Seven_Seg_Hex seven_seg_hex_2 (.d(input_bus[3:0]), .dp(1'b0));
  RAM ram_1 (.a(address), .e(enabler), .s(set), .i(input_bus), .o({ram_1_o_2, ram_1_o}));
  Seven_Seg_Hex seven_seg_hex_3 (.d(ram_1_o_2), .dp(1'b0));
  Seven_Seg_Hex seven_seg_hex_4 (.d(ram_1_o), .dp(1'b0));
endmodule
