// Digital circuit mem_1byte.dig as structural Verilog
module mem_1byte (
  input  i,
  input  i_2,
  input  i_3,
  input  i_4,
  input  i_5,
  input  i_6,
  input  i_7,
  input  i_8,
  input  s,
  input  e,
  output o,
  output o_2,
  output o_3,
  output o_4,
  output o_5,
  output o_6,
  output o_7,
  output o_8
);

  wire mem_1bit_1_o, mem_1bit_2_o, mem_1bit_3_o, mem_1bit_4_o, mem_1bit_5_o, mem_1bit_6_o, mem_1bit_7_o,
       mem_1bit_8_o;

  mem_1bit mem_1bit_1 (.i(i), .s(s), .o(mem_1bit_1_o));
  mem_1bit mem_1bit_2 (.i(i_2), .s(s), .o(mem_1bit_2_o));
  mem_1bit mem_1bit_3 (.i(i_3), .s(s), .o(mem_1bit_3_o));
  mem_1bit mem_1bit_4 (.i(i_4), .s(s), .o(mem_1bit_4_o));
  mem_1bit mem_1bit_5 (.i(i_5), .s(s), .o(mem_1bit_5_o));
  mem_1bit mem_1bit_6 (.i(i_6), .s(s), .o(mem_1bit_6_o));
  mem_1bit mem_1bit_7 (.i(i_7), .s(s), .o(mem_1bit_7_o));
  mem_1bit mem_1bit_8 (.i(i_8), .s(s), .o(mem_1bit_8_o));
  and_nand and_nand_1 (.i(mem_1bit_1_o), .i_2(e), .o(o));
  and_nand and_nand_2 (.i(mem_1bit_2_o), .i_2(e), .o(o_2));
  and_nand and_nand_3 (.i(mem_1bit_3_o), .i_2(e), .o(o_3));
  and_nand and_nand_4 (.i(mem_1bit_4_o), .i_2(e), .o(o_4));
  and_nand and_nand_5 (.i(mem_1bit_5_o), .i_2(e), .o(o_5));
  and_nand and_nand_6 (.i(mem_1bit_6_o), .i_2(e), .o(o_6));
  and_nand and_nand_7 (.i(mem_1bit_7_o), .i_2(e), .o(o_7));
  and_nand and_nand_8 (.i(mem_1bit_8_o), .i_2(e), .o(o_8));
endmodule
