// Digital circuit registro_x_y.dig as structural Verilog
module registro_x_y (
  input  [7:0] i,
  input  s,
  input  e,
  input  y,
  input  x,
  output [7:0] o
);

  wire and_nand_1_o, and_nand_2_o, and_nand_3_o;

  and_nand and_nand_1 (.i_2(x), .o(and_nand_1_o));  // open: i
  and_nand and_nand_2 (.i(s), .i_2(and_nand_1_o), .o(and_nand_2_o));
  and_nand and_nand_3 (.i(e), .i_2(and_nand_1_o), .o(and_nand_3_o));
  registro registro_1 (.in(i), .s(and_nand_2_o), .e(and_nand_3_o), .out(o));
endmodule
