// Logisim project computer_clark.circ as structural Verilog
module pruebas_dispositivos (
  input  in_1,
  input  in_2,
  input  in_3,
  input  [7:0] in_4,
  input  in_5,
  input  in_6
);

  wire dipswitch_1_p1, dipswitch_1_p2, dipswitch_1_p3, dipswitch_1_p4, dipswitch_1_p5, dipswitch_1_p6,
       dipswitch_1_p7, dipswitch_1_p8, mem_bit_1_out_3, mem_byte_1_out_10, mem_byte_1_out_11,
       mem_byte_1_out_12, mem_byte_1_out_13, mem_byte_1_out_14, mem_byte_1_out_15, mem_byte_1_out_16,
       mem_byte_1_out_17;

  LED led_1 (.in(mem_bit_1_out_3));
  mem_bit mem_bit_1 (.set(in_2), .data(in_1), .out_3(mem_bit_1_out_3));
  // DipSwitch dipswitch_1: pin names not known; wires that end beside it: dipswitch_1_p1, dipswitch_1_p2, dipswitch_1_p3, dipswitch_1_p4, dipswitch_1_p5, dipswitch_1_p6, dipswitch_1_p7, dipswitch_1_p8
  mem_byte mem_byte_1 (
    .set(in_3), .in_2(dipswitch_1_p2), .in_3(dipswitch_1_p3), .in_4(dipswitch_1_p4), .in_5(dipswitch_1_p5),
    .in_6(dipswitch_1_p6), .in_7(dipswitch_1_p7), .in_8(dipswitch_1_p8), .in_1(dipswitch_1_p1),
    .out_11(mem_byte_1_out_11), .out_12(mem_byte_1_out_12), .out_13(mem_byte_1_out_13),
    .out_14(mem_byte_1_out_14), .out_15(mem_byte_1_out_15), .out_16(mem_byte_1_out_16),
    .out_17(mem_byte_1_out_17), .out_10(mem_byte_1_out_10));
  LedBar ledbar_1 (
    .led0(mem_byte_1_out_10), .led1(mem_byte_1_out_11), .led2(mem_byte_1_out_12), .led3(mem_byte_1_out_13),
    .led4(mem_byte_1_out_14), .led5(mem_byte_1_out_15), .led6(mem_byte_1_out_16), .led7(mem_byte_1_out_17));
  register_nand_conbus register_nand_conbus_1 (.input_data(in_4), .set(in_5), .enable(in_6));  // open: output_data

  // Notes on the sheet:
  //   Memoria de 1 bit
  //   Memoria de 1 byte
  //   Registro de 1 byte
endmodule

module pruebas_copy_registros (
  input  [7:0] in_1,
  input  in_2,
  input  in_3,
  input  in_4,
  input  in_5,
  input  in_6,
  output [7:0] out_7
);

  wire button_1_out, button_2_out, button_3_out, button_4_out, button_5_out;

  register_visor register_visor_1 (.input_data(in_1), .set(button_1_out), .enable(in_2), .output_data(out_7));
  Button button_1 (.out(button_1_out));
  register_visor register_visor_2 (.input_data(out_7), .set(button_2_out), .enable(in_3), .output_data(out_7));
  Button button_2 (.out(button_2_out));
  register_visor register_visor_3 (.input_data(out_7), .set(button_3_out), .enable(in_4), .output_data(out_7));
  Button button_3 (.out(button_3_out));
  register_visor register_visor_4 (.input_data(out_7), .set(button_4_out), .enable(in_5), .output_data(out_7));
  Button button_4 (.out(button_4_out));
  Button button_5 (.out(button_5_out));
  register_visor register_visor_5 (.input_data(out_7), .set(button_5_out), .enable(in_6), .output_data(out_7));
  Pull_Resistor pull_resistor_1 (.node(out_7));

  // Notes on the sheet:
  //   Prueba de concepto de grabación de bytes de un registro a otro
endmodule

module RAM_clark (
  input  enabler,
  input  set,
  input  [7:0] data,
  input  in_4,
  input  in_5,
  input  in_6,
  input  in_7,
  input  in_8,
  input  in_9,
  input  in_10,
  input  in_11,
  input  in_12,
  input  in_13,
  input  in_14,
  input  in_15,
  input  in_16,
  input  in_17,
  input  in_18,
  input  in_19,
  input  in_20,
  input  in_21,
  input  in_22,
  input  in_23,
  input  in_24,
  input  in_25,
  input  in_26,
  input  in_27,
  input  in_28,
  input  in_29,
  input  in_30,
  input  in_31,
  input  in_32,
  input  in_33,
  input  in_34,
  input  in_35,
  output [7:0] out_36
);

  wire undriven;

  Pull_Resistor pull_resistor_1 (.node(out_36));
  registro_RAM registro_ram_1 (
    .input_bus(out_36), .vertical_wire(in_4), .horizontal_wire(in_20), .enabler(enabler), .set(set),
    .output_bus(out_36));
  registro_RAM registro_ram_2 (
    .input_bus(out_36), .vertical_wire(in_4), .horizontal_wire(in_21), .enabler(enabler), .set(set),
    .output_bus(out_36));
  registro_RAM registro_ram_3 (
    .input_bus(out_36), .vertical_wire(in_4), .horizontal_wire(in_22), .enabler(enabler), .set(set),
    .output_bus(out_36));
  registro_RAM registro_ram_4 (
    .input_bus(out_36), .vertical_wire(in_4), .horizontal_wire(in_23), .enabler(enabler), .set(set),
    .output_bus(out_36));
  registro_RAM registro_ram_5 (
    .input_bus(out_36), .vertical_wire(in_4), .horizontal_wire(in_24), .enabler(enabler), .set(set),
    .output_bus(out_36));
  registro_RAM registro_ram_6 (
    .input_bus(out_36), .vertical_wire(in_4), .horizontal_wire(in_25), .enabler(enabler), .set(set),
    .output_bus(out_36));
  registro_RAM registro_ram_7 (
    .input_bus(out_36), .vertical_wire(in_4), .horizontal_wire(in_26), .enabler(enabler), .set(set),
    .output_bus(out_36));
  registro_RAM registro_ram_8 (
    .input_bus(out_36), .vertical_wire(in_4), .horizontal_wire(in_27), .enabler(enabler), .set(set),
    .output_bus(out_36));
  registro_RAM registro_ram_9 (
    .input_bus(out_36), .vertical_wire(in_4), .horizontal_wire(in_28), .enabler(enabler), .set(set),
    .output_bus(out_36));
  registro_RAM registro_ram_10 (
    .input_bus(out_36), .vertical_wire(in_4), .horizontal_wire(in_29), .enabler(enabler), .set(set),
    .output_bus(out_36));
  registro_RAM registro_ram_11 (
    .input_bus(out_36), .vertical_wire(in_4), .horizontal_wire(in_30), .enabler(enabler), .set(set),
    .output_bus(out_36));
  registro_RAM registro_ram_12 (
    .input_bus(out_36), .vertical_wire(in_4), .horizontal_wire(in_31), .enabler(enabler), .set(set),
    .output_bus(out_36));
  registro_RAM registro_ram_13 (
    .input_bus(out_36), .vertical_wire(in_4), .horizontal_wire(in_32), .enabler(enabler), .set(set),
    .output_bus(out_36));
  registro_RAM registro_ram_14 (
    .input_bus(out_36), .vertical_wire(in_4), .horizontal_wire(in_33), .enabler(enabler), .set(set),
    .output_bus(out_36));
  registro_RAM registro_ram_15 (
    .input_bus(out_36), .vertical_wire(in_4), .horizontal_wire(in_34), .enabler(enabler), .set(set),
    .output_bus(out_36));
  registro_RAM registro_ram_16 (
    .input_bus(out_36), .vertical_wire(in_4), .horizontal_wire(undriven), .enabler(enabler), .set(set),
    .output_bus(out_36));
  registro_RAM registro_ram_17 (
    .input_bus(out_36), .vertical_wire(in_5), .horizontal_wire(in_20), .enabler(enabler), .set(set),
    .output_bus(out_36));
  registro_RAM registro_ram_18 (
    .input_bus(out_36), .vertical_wire(in_5), .horizontal_wire(in_21), .enabler(enabler), .set(set),
    .output_bus(out_36));
  registro_RAM registro_ram_19 (
    .input_bus(out_36), .vertical_wire(in_5), .horizontal_wire(in_22), .enabler(enabler), .set(set),
    .output_bus(out_36));
  registro_RAM registro_ram_20 (
    .input_bus(out_36), .vertical_wire(in_5), .horizontal_wire(in_23), .enabler(enabler), .set(set),
    .output_bus(out_36));
  registro_RAM registro_ram_21 (
    .input_bus(out_36), .vertical_wire(in_5), .horizontal_wire(in_24), .enabler(enabler), .set(set),
    .output_bus(out_36));
  registro_RAM registro_ram_22 (
    .input_bus(out_36), .vertical_wire(in_5), .horizontal_wire(in_25), .enabler(enabler), .set(set),
    .output_bus(out_36));
  registro_RAM registro_ram_23 (
    .input_bus(out_36), .vertical_wire(in_5), .horizontal_wire(in_26), .enabler(enabler), .set(set),
    .output_bus(out_36));
  registro_RAM registro_ram_24 (
    .input_bus(out_36), .vertical_wire(in_5), .horizontal_wire(in_27), .enabler(enabler), .set(set),
    .output_bus(out_36));
  registro_RAM registro_ram_25 (
    .input_bus(out_36), .vertical_wire(in_5), .horizontal_wire(in_28), .enabler(enabler), .set(set),
    .output_bus(out_36));
  registro_RAM registro_ram_26 (
    .input_bus(out_36), .vertical_wire(in_5), .horizontal_wire(in_29), .enabler(enabler), .set(set),
    .output_bus(out_36));
  registro_RAM registro_ram_27 (
    .input_bus(out_36), .vertical_wire(in_5), .horizontal_wire(in_30), .enabler(enabler), .set(set),
    .output_bus(out_36));
  registro_RAM registro_ram_28 (
    .input_bus(out_36), .vertical_wire(in_5), .horizontal_wire(in_31), .enabler(enabler), .set(set),
    .output_bus(out_36));
  registro_RAM registro_ram_29 (
    .input_bus(out_36), .vertical_wire(in_5), .horizontal_wire(in_32), .enabler(enabler), .set(set),
    .output_bus(out_36));
  registro_RAM registro_ram_30 (
    .input_bus(out_36), .vertical_wire(in_5), .horizontal_wire(in_33), .enabler(enabler), .set(set),
    .output_bus(out_36));
  registro_RAM registro_ram_31 (
    .input_bus(out_36), .vertical_wire(in_5), .horizontal_wire(in_34), .enabler(enabler), .set(set),
    .output_bus(out_36));
  registro_RAM registro_ram_32 (
    .input_bus(out_36), .vertical_wire(in_5), .horizontal_wire(undriven), .enabler(enabler), .set(set),
    .output_bus(out_36));
  registro_RAM registro_ram_33 (
    .input_bus(out_36), .vertical_wire(in_6), .horizontal_wire(in_20), .enabler(enabler), .set(set),
    .output_bus(out_36));
  registro_RAM registro_ram_34 (
    .input_bus(out_36), .vertical_wire(in_6), .horizontal_wire(in_21), .enabler(enabler), .set(set),
    .output_bus(out_36));
  registro_RAM registro_ram_35 (
    .input_bus(out_36), .vertical_wire(in_6), .horizontal_wire(in_22), .enabler(enabler), .set(set),
    .output_bus(out_36));
  registro_RAM registro_ram_36 (
    .input_bus(out_36), .vertical_wire(in_6), .horizontal_wire(in_23), .enabler(enabler), .set(set),
    .output_bus(out_36));
  registro_RAM registro_ram_37 (
    .input_bus(out_36), .vertical_wire(in_6), .horizontal_wire(in_24), .enabler(enabler), .set(set),
    .output_bus(out_36));
  registro_RAM registro_ram_38 (
    .input_bus(out_36), .vertical_wire(in_6), .horizontal_wire(in_25), .enabler(enabler), .set(set),
    .output_bus(out_36));
  registro_RAM registro_ram_39 (
    .input_bus(out_36), .vertical_wire(in_6), .horizontal_wire(in_26), .enabler(enabler), .set(set),
    .output_bus(out_36));
  registro_RAM registro_ram_40 (
    .input_bus(out_36), .vertical_wire(in_6), .horizontal_wire(in_27), .enabler(enabler), .set(set),
    .output_bus(out_36));
  registro_RAM registro_ram_41 (
    .input_bus(out_36), .vertical_wire(in_6), .horizontal_wire(in_28), .enabler(enabler), .set(set),
    .output_bus(out_36));
  registro_RAM registro_ram_42 (
    .input_bus(out_36), .vertical_wire(in_6), .horizontal_wire(in_29), .enabler(enabler), .set(set),
    .output_bus(out_36));
  registro_RAM registro_ram_43 (
    .input_bus(out_36), .vertical_wire(in_6), .horizontal_wire(in_30), .enabler(enabler), .set(set),
    .output_bus(out_36));
  registro_RAM registro_ram_44 (
    .input_bus(out_36), .vertical_wire(in_6), .horizontal_wire(in_31), .enabler(enabler), .set(set),
    .output_bus(out_36));
  registro_RAM registro_ram_45 (
    .input_bus(out_36), .vertical_wire(in_6), .horizontal_wire(in_32), .enabler(enabler), .set(set),
    .output_bus(out_36));
  registro_RAM registro_ram_46 (
    .input_bus(out_36), .vertical_wire(in_6), .horizontal_wire(in_33), .enabler(enabler), .set(set),
    .output_bus(out_36));
  registro_RAM registro_ram_47 (
    .input_bus(out_36), .vertical_wire(in_6), .horizontal_wire(in_34), .enabler(enabler), .set(set),
    .output_bus(out_36));
  registro_RAM registro_ram_48 (
    .input_bus(out_36), .vertical_wire(in_6), .horizontal_wire(undriven), .enabler(enabler), .set(set),
    .output_bus(out_36));
  registro_RAM registro_ram_49 (
    .input_bus(out_36), .vertical_wire(in_7), .horizontal_wire(in_20), .enabler(enabler), .set(set),
    .output_bus(out_36));
  registro_RAM registro_ram_50 (
    .input_bus(out_36), .vertical_wire(in_7), .horizontal_wire(in_21), .enabler(enabler), .set(set),
    .output_bus(out_36));
  registro_RAM registro_ram_51 (
    .input_bus(out_36), .vertical_wire(in_7), .horizontal_wire(in_22), .enabler(enabler), .set(set),
    .output_bus(out_36));
  registro_RAM registro_ram_52 (
    .input_bus(out_36), .vertical_wire(in_7), .horizontal_wire(in_23), .enabler(enabler), .set(set),
    .output_bus(out_36));
  registro_RAM registro_ram_53 (
    .input_bus(out_36), .vertical_wire(in_7), .horizontal_wire(in_24), .enabler(enabler), .set(set),
    .output_bus(out_36));
  registro_RAM registro_ram_54 (
    .input_bus(out_36), .vertical_wire(in_7), .horizontal_wire(in_25), .enabler(enabler), .set(set),
    .output_bus(out_36));
  registro_RAM registro_ram_55 (
    .input_bus(out_36), .vertical_wire(in_7), .horizontal_wire(in_26), .enabler(enabler), .set(set),
    .output_bus(out_36));
  registro_RAM registro_ram_56 (
    .input_bus(out_36), .vertical_wire(in_7), .horizontal_wire(in_27), .enabler(enabler), .set(set),
    .output_bus(out_36));
  registro_RAM registro_ram_57 (
    .input_bus(out_36), .vertical_wire(in_7), .horizontal_wire(in_28), .enabler(enabler), .set(set),
    .output_bus(out_36));
  registro_RAM registro_ram_58 (
    .input_bus(out_36), .vertical_wire(in_7), .horizontal_wire(in_29), .enabler(enabler), .set(set),
    .output_bus(out_36));
  registro_RAM registro_ram_59 (
    .input_bus(out_36), .vertical_wire(in_7), .horizontal_wire(in_30), .enabler(enabler), .set(set),
    .output_bus(out_36));
  registro_RAM registro_ram_60 (
    .input_bus(out_36), .vertical_wire(in_7), .horizontal_wire(in_31), .enabler(enabler), .set(set),
    .output_bus(out_36));
  registro_RAM registro_ram_61 (
    .input_bus(out_36), .vertical_wire(in_7), .horizontal_wire(in_32), .enabler(enabler), .set(set),
    .output_bus(out_36));
  registro_RAM registro_ram_62 (
    .input_bus(out_36), .vertical_wire(in_7), .horizontal_wire(in_33), .enabler(enabler), .set(set),
    .output_bus(out_36));
  registro_RAM registro_ram_63 (
    .input_bus(out_36), .vertical_wire(in_7), .horizontal_wire(in_34), .enabler(enabler), .set(set),
    .output_bus(out_36));
  registro_RAM registro_ram_64 (
    .input_bus(out_36), .vertical_wire(in_7), .horizontal_wire(undriven), .enabler(enabler), .set(set),
    .output_bus(out_36));
  registro_RAM registro_ram_65 (
    .input_bus(out_36), .vertical_wire(in_8), .horizontal_wire(in_20), .enabler(enabler), .set(set),
    .output_bus(out_36));
  registro_RAM registro_ram_66 (
    .input_bus(out_36), .vertical_wire(in_8), .horizontal_wire(in_21), .enabler(enabler), .set(set),
    .output_bus(out_36));
  registro_RAM registro_ram_67 (
    .input_bus(out_36), .vertical_wire(in_8), .horizontal_wire(in_22), .enabler(enabler), .set(set),
    .output_bus(out_36));
  registro_RAM registro_ram_68 (
    .input_bus(out_36), .vertical_wire(in_8), .horizontal_wire(in_23), .enabler(enabler), .set(set),
    .output_bus(out_36));
  registro_RAM registro_ram_69 (
    .input_bus(out_36), .vertical_wire(in_8), .horizontal_wire(in_24), .enabler(enabler), .set(set),
    .output_bus(out_36));
  registro_RAM registro_ram_70 (
    .input_bus(out_36), .vertical_wire(in_8), .horizontal_wire(in_25), .enabler(enabler), .set(set),
    .output_bus(out_36));
  registro_RAM registro_ram_71 (
    .input_bus(out_36), .vertical_wire(in_8), .horizontal_wire(in_26), .enabler(enabler), .set(set),
    .output_bus(out_36));
  registro_RAM registro_ram_72 (
    .input_bus(out_36), .vertical_wire(in_8), .horizontal_wire(in_27), .enabler(enabler), .set(set),
    .output_bus(out_36));
  registro_RAM registro_ram_73 (
    .input_bus(out_36), .vertical_wire(in_8), .horizontal_wire(in_28), .enabler(enabler), .set(set),
    .output_bus(out_36));
  registro_RAM registro_ram_74 (
    .input_bus(out_36), .vertical_wire(in_8), .horizontal_wire(in_29), .enabler(enabler), .set(set),
    .output_bus(out_36));
  registro_RAM registro_ram_75 (
    .input_bus(out_36), .vertical_wire(in_8), .horizontal_wire(in_30), .enabler(enabler), .set(set),
    .output_bus(out_36));
  registro_RAM registro_ram_76 (
    .input_bus(out_36), .vertical_wire(in_8), .horizontal_wire(in_31), .enabler(enabler), .set(set),
    .output_bus(out_36));
  registro_RAM registro_ram_77 (
    .input_bus(out_36), .vertical_wire(in_8), .horizontal_wire(in_32), .enabler(enabler), .set(set),
    .output_bus(out_36));
  registro_RAM registro_ram_78 (
    .input_bus(out_36), .vertical_wire(in_8), .horizontal_wire(in_33), .enabler(enabler), .set(set),
    .output_bus(out_36));
  registro_RAM registro_ram_79 (
    .input_bus(out_36), .vertical_wire(in_8), .horizontal_wire(in_34), .enabler(enabler), .set(set),
    .output_bus(out_36));
  registro_RAM registro_ram_80 (
    .input_bus(out_36), .vertical_wire(in_8), .horizontal_wire(undriven), .enabler(enabler), .set(set),
    .output_bus(out_36));
  registro_RAM registro_ram_81 (
    .input_bus(out_36), .vertical_wire(in_9), .horizontal_wire(in_20), .enabler(enabler), .set(set),
    .output_bus(out_36));
  registro_RAM registro_ram_82 (
    .input_bus(out_36), .vertical_wire(in_9), .horizontal_wire(in_21), .enabler(enabler), .set(set),
    .output_bus(out_36));
  registro_RAM registro_ram_83 (
    .input_bus(out_36), .vertical_wire(in_9), .horizontal_wire(in_22), .enabler(enabler), .set(set),
    .output_bus(out_36));
  registro_RAM registro_ram_84 (
    .input_bus(out_36), .vertical_wire(in_9), .horizontal_wire(in_23), .enabler(enabler), .set(set),
    .output_bus(out_36));
  registro_RAM registro_ram_85 (
    .input_bus(out_36), .vertical_wire(in_9), .horizontal_wire(in_24), .enabler(enabler), .set(set),
    .output_bus(out_36));
  registro_RAM registro_ram_86 (
    .input_bus(out_36), .vertical_wire(in_9), .horizontal_wire(in_25), .enabler(enabler), .set(set),
    .output_bus(out_36));
  registro_RAM registro_ram_87 (
    .input_bus(out_36), .vertical_wire(in_9), .horizontal_wire(in_26), .enabler(enabler), .set(set),
    .output_bus(out_36));
  registro_RAM registro_ram_88 (
    .input_bus(out_36), .vertical_wire(in_9), .horizontal_wire(in_27), .enabler(enabler), .set(set),
    .output_bus(out_36));
  registro_RAM registro_ram_89 (
    .input_bus(out_36), .vertical_wire(in_9), .horizontal_wire(in_28), .enabler(enabler), .set(set),
    .output_bus(out_36));
  registro_RAM registro_ram_90 (
    .input_bus(out_36), .vertical_wire(in_9), .horizontal_wire(in_29), .enabler(enabler), .set(set),
    .output_bus(out_36));
  registro_RAM registro_ram_91 (
    .input_bus(out_36), .vertical_wire(in_9), .horizontal_wire(in_30), .enabler(enabler), .set(set),
    .output_bus(out_36));
  registro_RAM registro_ram_92 (
    .input_bus(out_36), .vertical_wire(in_9), .horizontal_wire(in_31), .enabler(enabler), .set(set),
    .output_bus(out_36));
  registro_RAM registro_ram_93 (
    .input_bus(out_36), .vertical_wire(in_9), .horizontal_wire(in_32), .enabler(enabler), .set(set),
    .output_bus(out_36));
  registro_RAM registro_ram_94 (
    .input_bus(out_36), .vertical_wire(in_9), .horizontal_wire(in_33), .enabler(enabler), .set(set),
    .output_bus(out_36));
  registro_RAM registro_ram_95 (
    .input_bus(out_36), .vertical_wire(in_9), .horizontal_wire(in_34), .enabler(enabler), .set(set),
    .output_bus(out_36));
  registro_RAM registro_ram_96 (
    .input_bus(out_36), .vertical_wire(in_9), .horizontal_wire(undriven), .enabler(enabler), .set(set),
    .output_bus(out_36));
  registro_RAM registro_ram_97 (
    .input_bus(out_36), .vertical_wire(in_10), .horizontal_wire(in_20), .enabler(enabler), .set(set),
    .output_bus(out_36));
  registro_RAM registro_ram_98 (
    .input_bus(out_36), .vertical_wire(in_10), .horizontal_wire(in_21), .enabler(enabler), .set(set),
    .output_bus(out_36));
  registro_RAM registro_ram_99 (
    .input_bus(out_36), .vertical_wire(in_10), .horizontal_wire(in_22), .enabler(enabler), .set(set),
    .output_bus(out_36));
  registro_RAM registro_ram_100 (
    .input_bus(out_36), .vertical_wire(in_10), .horizontal_wire(in_23), .enabler(enabler), .set(set),
    .output_bus(out_36));
  registro_RAM registro_ram_101 (
    .input_bus(out_36), .vertical_wire(in_10), .horizontal_wire(in_24), .enabler(enabler), .set(set),
    .output_bus(out_36));
  registro_RAM registro_ram_102 (
    .input_bus(out_36), .vertical_wire(in_10), .horizontal_wire(in_25), .enabler(enabler), .set(set),
    .output_bus(out_36));
  registro_RAM registro_ram_103 (
    .input_bus(out_36), .vertical_wire(in_10), .horizontal_wire(in_26), .enabler(enabler), .set(set),
    .output_bus(out_36));
  registro_RAM registro_ram_104 (
    .input_bus(out_36), .vertical_wire(in_10), .horizontal_wire(in_27), .enabler(enabler), .set(set),
    .output_bus(out_36));
  registro_RAM registro_ram_105 (
    .input_bus(out_36), .vertical_wire(in_10), .horizontal_wire(in_28), .enabler(enabler), .set(set),
    .output_bus(out_36));
  registro_RAM registro_ram_106 (
    .input_bus(out_36), .vertical_wire(in_10), .horizontal_wire(in_29), .enabler(enabler), .set(set),
    .output_bus(out_36));
  registro_RAM registro_ram_107 (
    .input_bus(out_36), .vertical_wire(in_10), .horizontal_wire(in_30), .enabler(enabler), .set(set),
    .output_bus(out_36));
  registro_RAM registro_ram_108 (
    .input_bus(out_36), .vertical_wire(in_10), .horizontal_wire(in_31), .enabler(enabler), .set(set),
    .output_bus(out_36));
  registro_RAM registro_ram_109 (
    .input_bus(out_36), .vertical_wire(in_10), .horizontal_wire(in_32), .enabler(enabler), .set(set),
    .output_bus(out_36));
  registro_RAM registro_ram_110 (
    .input_bus(out_36), .vertical_wire(in_10), .horizontal_wire(in_33), .enabler(enabler), .set(set),
    .output_bus(out_36));
  registro_RAM registro_ram_111 (
    .input_bus(out_36), .vertical_wire(in_10), .horizontal_wire(in_34), .enabler(enabler), .set(set),
    .output_bus(out_36));
  registro_RAM registro_ram_112 (
    .input_bus(out_36), .vertical_wire(in_10), .horizontal_wire(undriven), .enabler(enabler), .set(set),
    .output_bus(out_36));
  registro_RAM registro_ram_113 (
    .input_bus(out_36), .vertical_wire(in_11), .horizontal_wire(in_20), .enabler(enabler), .set(set),
    .output_bus(out_36));
  registro_RAM registro_ram_114 (
    .input_bus(out_36), .vertical_wire(in_11), .horizontal_wire(in_21), .enabler(enabler), .set(set),
    .output_bus(out_36));
  registro_RAM registro_ram_115 (
    .input_bus(out_36), .vertical_wire(in_11), .horizontal_wire(in_22), .enabler(enabler), .set(set),
    .output_bus(out_36));
  registro_RAM registro_ram_116 (
    .input_bus(out_36), .vertical_wire(in_11), .horizontal_wire(in_23), .enabler(enabler), .set(set),
    .output_bus(out_36));
  registro_RAM registro_ram_117 (
    .input_bus(out_36), .vertical_wire(in_11), .horizontal_wire(in_24), .enabler(enabler), .set(set),
    .output_bus(out_36));
  registro_RAM registro_ram_118 (
    .input_bus(out_36), .vertical_wire(in_11), .horizontal_wire(in_25), .enabler(enabler), .set(set),
    .output_bus(out_36));
  registro_RAM registro_ram_119 (
    .input_bus(out_36), .vertical_wire(in_11), .horizontal_wire(in_26), .enabler(enabler), .set(set),
    .output_bus(out_36));
  registro_RAM registro_ram_120 (
    .input_bus(out_36), .vertical_wire(in_11), .horizontal_wire(in_27), .enabler(enabler), .set(set),
    .output_bus(out_36));
  registro_RAM registro_ram_121 (
    .input_bus(out_36), .vertical_wire(in_11), .horizontal_wire(in_28), .enabler(enabler), .set(set),
    .output_bus(out_36));
  registro_RAM registro_ram_122 (
    .input_bus(out_36), .vertical_wire(in_11), .horizontal_wire(in_29), .enabler(enabler), .set(set),
    .output_bus(out_36));
  registro_RAM registro_ram_123 (
    .input_bus(out_36), .vertical_wire(in_11), .horizontal_wire(in_30), .enabler(enabler), .set(set),
    .output_bus(out_36));
  registro_RAM registro_ram_124 (
    .input_bus(out_36), .vertical_wire(in_11), .horizontal_wire(in_31), .enabler(enabler), .set(set),
    .output_bus(out_36));
  registro_RAM registro_ram_125 (
    .input_bus(out_36), .vertical_wire(in_11), .horizontal_wire(in_32), .enabler(enabler), .set(set),
    .output_bus(out_36));
  registro_RAM registro_ram_126 (
    .input_bus(out_36), .vertical_wire(in_11), .horizontal_wire(in_33), .enabler(enabler), .set(set),
    .output_bus(out_36));
  registro_RAM registro_ram_127 (
    .input_bus(out_36), .vertical_wire(in_11), .horizontal_wire(in_34), .enabler(enabler), .set(set),
    .output_bus(out_36));
  registro_RAM registro_ram_128 (
    .input_bus(out_36), .vertical_wire(in_11), .horizontal_wire(undriven), .enabler(enabler), .set(set),
    .output_bus(out_36));
  registro_RAM registro_ram_129 (
    .input_bus(out_36), .vertical_wire(in_12), .horizontal_wire(in_20), .enabler(enabler), .set(set),
    .output_bus(out_36));
  registro_RAM registro_ram_130 (
    .input_bus(out_36), .vertical_wire(in_12), .horizontal_wire(in_21), .enabler(enabler), .set(set),
    .output_bus(out_36));
  registro_RAM registro_ram_131 (
    .input_bus(out_36), .vertical_wire(in_12), .horizontal_wire(in_22), .enabler(enabler), .set(set),
    .output_bus(out_36));
  registro_RAM registro_ram_132 (
    .input_bus(out_36), .vertical_wire(in_12), .horizontal_wire(in_23), .enabler(enabler), .set(set),
    .output_bus(out_36));
  registro_RAM registro_ram_133 (
    .input_bus(out_36), .vertical_wire(in_12), .horizontal_wire(in_24), .enabler(enabler), .set(set),
    .output_bus(out_36));
  registro_RAM registro_ram_134 (
    .input_bus(out_36), .vertical_wire(in_12), .horizontal_wire(in_25), .enabler(enabler), .set(set),
    .output_bus(out_36));
  registro_RAM registro_ram_135 (
    .input_bus(out_36), .vertical_wire(in_12), .horizontal_wire(in_26), .enabler(enabler), .set(set),
    .output_bus(out_36));
  registro_RAM registro_ram_136 (
    .input_bus(out_36), .vertical_wire(in_12), .horizontal_wire(in_27), .enabler(enabler), .set(set),
    .output_bus(out_36));
  registro_RAM registro_ram_137 (
    .input_bus(out_36), .vertical_wire(in_12), .horizontal_wire(in_28), .enabler(enabler), .set(set),
    .output_bus(out_36));
  registro_RAM registro_ram_138 (
    .input_bus(out_36), .vertical_wire(in_12), .horizontal_wire(in_29), .enabler(enabler), .set(set),
    .output_bus(out_36));
  registro_RAM registro_ram_139 (
    .input_bus(out_36), .vertical_wire(in_12), .horizontal_wire(in_30), .enabler(enabler), .set(set),
    .output_bus(out_36));
  registro_RAM registro_ram_140 (
    .input_bus(out_36), .vertical_wire(in_12), .horizontal_wire(in_31), .enabler(enabler), .set(set),
    .output_bus(out_36));
  registro_RAM registro_ram_141 (
    .input_bus(out_36), .vertical_wire(in_12), .horizontal_wire(in_32), .enabler(enabler), .set(set),
    .output_bus(out_36));
  registro_RAM registro_ram_142 (
    .input_bus(out_36), .vertical_wire(in_12), .horizontal_wire(in_33), .enabler(enabler), .set(set),
    .output_bus(out_36));
  registro_RAM registro_ram_143 (
    .input_bus(out_36), .vertical_wire(in_12), .horizontal_wire(in_34), .enabler(enabler), .set(set),
    .output_bus(out_36));
  registro_RAM registro_ram_144 (
    .input_bus(out_36), .vertical_wire(in_12), .horizontal_wire(undriven), .enabler(enabler), .set(set),
    .output_bus(out_36));
  registro_RAM registro_ram_145 (
    .input_bus(out_36), .vertical_wire(in_13), .horizontal_wire(in_20), .enabler(enabler), .set(set),
    .output_bus(out_36));
  registro_RAM registro_ram_146 (
    .input_bus(out_36), .vertical_wire(in_13), .horizontal_wire(in_21), .enabler(enabler), .set(set),
    .output_bus(out_36));
  registro_RAM registro_ram_147 (
    .input_bus(out_36), .vertical_wire(in_13), .horizontal_wire(in_22), .enabler(enabler), .set(set),
    .output_bus(out_36));
  registro_RAM registro_ram_148 (
    .input_bus(out_36), .vertical_wire(in_13), .horizontal_wire(in_23), .enabler(enabler), .set(set),
    .output_bus(out_36));
  registro_RAM registro_ram_149 (
    .input_bus(out_36), .vertical_wire(in_13), .horizontal_wire(in_24), .enabler(enabler), .set(set),
    .output_bus(out_36));
  registro_RAM registro_ram_150 (
    .input_bus(out_36), .vertical_wire(in_13), .horizontal_wire(in_25), .enabler(enabler), .set(set),
    .output_bus(out_36));
  registro_RAM registro_ram_151 (
    .input_bus(out_36), .vertical_wire(in_13), .horizontal_wire(in_26), .enabler(enabler), .set(set),
    .output_bus(out_36));
  registro_RAM registro_ram_152 (
    .input_bus(out_36), .vertical_wire(in_13), .horizontal_wire(in_27), .enabler(enabler), .set(set),
    .output_bus(out_36));
  registro_RAM registro_ram_153 (
    .input_bus(out_36), .vertical_wire(in_13), .horizontal_wire(in_28), .enabler(enabler), .set(set),
    .output_bus(out_36));
  registro_RAM registro_ram_154 (
    .input_bus(out_36), .vertical_wire(in_13), .horizontal_wire(in_29), .enabler(enabler), .set(set),
    .output_bus(out_36));
  registro_RAM registro_ram_155 (
    .input_bus(out_36), .vertical_wire(in_13), .horizontal_wire(in_30), .enabler(enabler), .set(set),
    .output_bus(out_36));
  registro_RAM registro_ram_156 (
    .input_bus(out_36), .vertical_wire(in_13), .horizontal_wire(in_31), .enabler(enabler), .set(set),
    .output_bus(out_36));
  registro_RAM registro_ram_157 (
    .input_bus(out_36), .vertical_wire(in_13), .horizontal_wire(in_32), .enabler(enabler), .set(set),
    .output_bus(out_36));
  registro_RAM registro_ram_158 (
    .input_bus(out_36), .vertical_wire(in_13), .horizontal_wire(in_33), .enabler(enabler), .set(set),
    .output_bus(out_36));
  registro_RAM registro_ram_159 (
    .input_bus(out_36), .vertical_wire(in_13), .horizontal_wire(in_34), .enabler(enabler), .set(set),
    .output_bus(out_36));
  registro_RAM registro_ram_160 (
    .input_bus(out_36), .vertical_wire(in_13), .horizontal_wire(undriven), .enabler(enabler), .set(set),
    .output_bus(out_36));
  registro_RAM registro_ram_161 (
    .input_bus(out_36), .vertical_wire(in_14), .horizontal_wire(in_20), .enabler(enabler), .set(set),
    .output_bus(out_36));
  registro_RAM registro_ram_162 (
    .input_bus(out_36), .vertical_wire(in_14), .horizontal_wire(in_21), .enabler(enabler), .set(set),
    .output_bus(out_36));
  registro_RAM registro_ram_163 (
    .input_bus(out_36), .vertical_wire(in_14), .horizontal_wire(in_22), .enabler(enabler), .set(set),
    .output_bus(out_36));
  registro_RAM registro_ram_164 (
    .input_bus(out_36), .vertical_wire(in_14), .horizontal_wire(in_23), .enabler(enabler), .set(set),
    .output_bus(out_36));
  registro_RAM registro_ram_165 (
    .input_bus(out_36), .vertical_wire(in_14), .horizontal_wire(in_24), .enabler(enabler), .set(set),
    .output_bus(out_36));
  registro_RAM registro_ram_166 (
    .input_bus(out_36), .vertical_wire(in_14), .horizontal_wire(in_25), .enabler(enabler), .set(set),
    .output_bus(out_36));
  registro_RAM registro_ram_167 (
    .input_bus(out_36), .vertical_wire(in_14), .horizontal_wire(in_26), .enabler(enabler), .set(set),
    .output_bus(out_36));
  registro_RAM registro_ram_168 (
    .input_bus(out_36), .vertical_wire(in_14), .horizontal_wire(in_27), .enabler(enabler), .set(set),
    .output_bus(out_36));
  registro_RAM registro_ram_169 (
    .input_bus(out_36), .vertical_wire(in_14), .horizontal_wire(in_28), .enabler(enabler), .set(set),
    .output_bus(out_36));
  registro_RAM registro_ram_170 (
    .input_bus(out_36), .vertical_wire(in_14), .horizontal_wire(in_29), .enabler(enabler), .set(set),
    .output_bus(out_36));
  registro_RAM registro_ram_171 (
    .input_bus(out_36), .vertical_wire(in_14), .horizontal_wire(in_30), .enabler(enabler), .set(set),
    .output_bus(out_36));
  registro_RAM registro_ram_172 (
    .input_bus(out_36), .vertical_wire(in_14), .horizontal_wire(in_31), .enabler(enabler), .set(set),
    .output_bus(out_36));
  registro_RAM registro_ram_173 (
    .input_bus(out_36), .vertical_wire(in_14), .horizontal_wire(in_32), .enabler(enabler), .set(set),
    .output_bus(out_36));
  registro_RAM registro_ram_174 (
    .input_bus(out_36), .vertical_wire(in_14), .horizontal_wire(in_33), .enabler(enabler), .set(set),
    .output_bus(out_36));
  registro_RAM registro_ram_175 (
    .input_bus(out_36), .vertical_wire(in_14), .horizontal_wire(in_34), .enabler(enabler), .set(set),
    .output_bus(out_36));
  registro_RAM registro_ram_176 (
    .input_bus(out_36), .vertical_wire(in_14), .horizontal_wire(undriven), .enabler(enabler), .set(set),
    .output_bus(out_36));
  registro_RAM registro_ram_177 (
    .input_bus(out_36), .vertical_wire(in_15), .horizontal_wire(in_20), .enabler(enabler), .set(set),
    .output_bus(out_36));
  registro_RAM registro_ram_178 (
    .input_bus(out_36), .vertical_wire(in_15), .horizontal_wire(in_21), .enabler(enabler), .set(set),
    .output_bus(out_36));
  registro_RAM registro_ram_179 (
    .input_bus(out_36), .vertical_wire(in_15), .horizontal_wire(in_22), .enabler(enabler), .set(set),
    .output_bus(out_36));
  registro_RAM registro_ram_180 (
    .input_bus(out_36), .vertical_wire(in_15), .horizontal_wire(in_23), .enabler(enabler), .set(set),
    .output_bus(out_36));
  registro_RAM registro_ram_181 (
    .input_bus(out_36), .vertical_wire(in_15), .horizontal_wire(in_24), .enabler(enabler), .set(set),
    .output_bus(out_36));
  registro_RAM registro_ram_182 (
    .input_bus(out_36), .vertical_wire(in_15), .horizontal_wire(in_25), .enabler(enabler), .set(set),
    .output_bus(out_36));
  registro_RAM registro_ram_183 (
    .input_bus(out_36), .vertical_wire(in_15), .horizontal_wire(in_26), .enabler(enabler), .set(set),
    .output_bus(out_36));
  registro_RAM registro_ram_184 (
    .input_bus(out_36), .vertical_wire(in_15), .horizontal_wire(in_27), .enabler(enabler), .set(set),
    .output_bus(out_36));
  registro_RAM registro_ram_185 (
    .input_bus(out_36), .vertical_wire(in_15), .horizontal_wire(in_28), .enabler(enabler), .set(set),
    .output_bus(out_36));
  registro_RAM registro_ram_186 (
    .input_bus(out_36), .vertical_wire(in_15), .horizontal_wire(in_29), .enabler(enabler), .set(set),
    .output_bus(out_36));
  registro_RAM registro_ram_187 (
    .input_bus(out_36), .vertical_wire(in_15), .horizontal_wire(in_30), .enabler(enabler), .set(set),
    .output_bus(out_36));
  registro_RAM registro_ram_188 (
    .input_bus(out_36), .vertical_wire(in_15), .horizontal_wire(in_31), .enabler(enabler), .set(set),
    .output_bus(out_36));
  registro_RAM registro_ram_189 (
    .input_bus(out_36), .vertical_wire(in_15), .horizontal_wire(in_32), .enabler(enabler), .set(set),
    .output_bus(out_36));
  registro_RAM registro_ram_190 (
    .input_bus(out_36), .vertical_wire(in_15), .horizontal_wire(in_33), .enabler(enabler), .set(set),
    .output_bus(out_36));
  registro_RAM registro_ram_191 (
    .input_bus(out_36), .vertical_wire(in_15), .horizontal_wire(in_34), .enabler(enabler), .set(set),
    .output_bus(out_36));
  registro_RAM registro_ram_192 (
    .input_bus(out_36), .vertical_wire(in_15), .horizontal_wire(undriven), .enabler(enabler), .set(set),
    .output_bus(out_36));
  registro_RAM registro_ram_193 (
    .input_bus(out_36), .vertical_wire(in_16), .horizontal_wire(in_20), .enabler(enabler), .set(set),
    .output_bus(out_36));
  registro_RAM registro_ram_194 (
    .input_bus(out_36), .vertical_wire(in_16), .horizontal_wire(in_21), .enabler(enabler), .set(set),
    .output_bus(out_36));
  registro_RAM registro_ram_195 (
    .input_bus(out_36), .vertical_wire(in_16), .horizontal_wire(in_22), .enabler(enabler), .set(set),
    .output_bus(out_36));
  registro_RAM registro_ram_196 (
    .input_bus(out_36), .vertical_wire(in_16), .horizontal_wire(in_23), .enabler(enabler), .set(set),
    .output_bus(out_36));
  registro_RAM registro_ram_197 (
    .input_bus(out_36), .vertical_wire(in_16), .horizontal_wire(in_24), .enabler(enabler), .set(set),
    .output_bus(out_36));
  registro_RAM registro_ram_198 (
    .input_bus(out_36), .vertical_wire(in_16), .horizontal_wire(in_25), .enabler(enabler), .set(set),
    .output_bus(out_36));
  registro_RAM registro_ram_199 (
    .input_bus(out_36), .vertical_wire(in_16), .horizontal_wire(in_26), .enabler(enabler), .set(set),
    .output_bus(out_36));
  registro_RAM registro_ram_200 (
    .input_bus(out_36), .vertical_wire(in_16), .horizontal_wire(in_27), .enabler(enabler), .set(set),
    .output_bus(out_36));
  registro_RAM registro_ram_201 (
    .input_bus(out_36), .vertical_wire(in_16), .horizontal_wire(in_28), .enabler(enabler), .set(set),
    .output_bus(out_36));
  registro_RAM registro_ram_202 (
    .input_bus(out_36), .vertical_wire(in_16), .horizontal_wire(in_29), .enabler(enabler), .set(set),
    .output_bus(out_36));
  registro_RAM registro_ram_203 (
    .input_bus(out_36), .vertical_wire(in_16), .horizontal_wire(in_30), .enabler(enabler), .set(set),
    .output_bus(out_36));
  registro_RAM registro_ram_204 (
    .input_bus(out_36), .vertical_wire(in_16), .horizontal_wire(in_31), .enabler(enabler), .set(set),
    .output_bus(out_36));
  registro_RAM registro_ram_205 (
    .input_bus(out_36), .vertical_wire(in_16), .horizontal_wire(in_32), .enabler(enabler), .set(set),
    .output_bus(out_36));
  registro_RAM registro_ram_206 (
    .input_bus(out_36), .vertical_wire(in_16), .horizontal_wire(in_33), .enabler(enabler), .set(set),
    .output_bus(out_36));
  registro_RAM registro_ram_207 (
    .input_bus(out_36), .vertical_wire(in_16), .horizontal_wire(in_34), .enabler(enabler), .set(set),
    .output_bus(out_36));
  registro_RAM registro_ram_208 (
    .input_bus(out_36), .vertical_wire(in_16), .horizontal_wire(undriven), .enabler(enabler), .set(set),
    .output_bus(out_36));
  registro_RAM registro_ram_209 (
    .input_bus(out_36), .vertical_wire(in_17), .horizontal_wire(in_20), .enabler(enabler), .set(set),
    .output_bus(out_36));
  registro_RAM registro_ram_210 (
    .input_bus(out_36), .vertical_wire(in_17), .horizontal_wire(in_21), .enabler(enabler), .set(set),
    .output_bus(out_36));
  registro_RAM registro_ram_211 (
    .input_bus(out_36), .vertical_wire(in_17), .horizontal_wire(in_22), .enabler(enabler), .set(set),
    .output_bus(out_36));
  registro_RAM registro_ram_212 (
    .input_bus(out_36), .vertical_wire(in_17), .horizontal_wire(in_23), .enabler(enabler), .set(set),
    .output_bus(out_36));
  registro_RAM registro_ram_213 (
    .input_bus(out_36), .vertical_wire(in_17), .horizontal_wire(in_24), .enabler(enabler), .set(set),
    .output_bus(out_36));
  registro_RAM registro_ram_214 (
    .input_bus(out_36), .vertical_wire(in_17), .horizontal_wire(in_25), .enabler(enabler), .set(set),
    .output_bus(out_36));
  registro_RAM registro_ram_215 (
    .input_bus(out_36), .vertical_wire(in_17), .horizontal_wire(in_26), .enabler(enabler), .set(set),
    .output_bus(out_36));
  registro_RAM registro_ram_216 (
    .input_bus(out_36), .vertical_wire(in_17), .horizontal_wire(in_27), .enabler(enabler), .set(set),
    .output_bus(out_36));
  registro_RAM registro_ram_217 (
    .input_bus(out_36), .vertical_wire(in_17), .horizontal_wire(in_28), .enabler(enabler), .set(set),
    .output_bus(out_36));
  registro_RAM registro_ram_218 (
    .input_bus(out_36), .vertical_wire(in_17), .horizontal_wire(in_29), .enabler(enabler), .set(set),
    .output_bus(out_36));
  registro_RAM registro_ram_219 (
    .input_bus(out_36), .vertical_wire(in_17), .horizontal_wire(in_30), .enabler(enabler), .set(set),
    .output_bus(out_36));
  registro_RAM registro_ram_220 (
    .input_bus(out_36), .vertical_wire(in_17), .horizontal_wire(in_31), .enabler(enabler), .set(set),
    .output_bus(out_36));
  registro_RAM registro_ram_221 (
    .input_bus(out_36), .vertical_wire(in_17), .horizontal_wire(in_32), .enabler(enabler), .set(set),
    .output_bus(out_36));
  registro_RAM registro_ram_222 (
    .input_bus(out_36), .vertical_wire(in_17), .horizontal_wire(in_33), .enabler(enabler), .set(set),
    .output_bus(out_36));
  registro_RAM registro_ram_223 (
    .input_bus(out_36), .vertical_wire(in_17), .horizontal_wire(in_34), .enabler(enabler), .set(set),
    .output_bus(out_36));
  registro_RAM registro_ram_224 (
    .input_bus(out_36), .vertical_wire(in_17), .horizontal_wire(undriven), .enabler(enabler), .set(set),
    .output_bus(out_36));
  registro_RAM registro_ram_225 (
    .input_bus(out_36), .vertical_wire(in_18), .horizontal_wire(in_20), .enabler(enabler), .set(set),
    .output_bus(out_36));
  registro_RAM registro_ram_226 (
    .input_bus(out_36), .vertical_wire(in_18), .horizontal_wire(in_21), .enabler(enabler), .set(set),
    .output_bus(out_36));
  registro_RAM registro_ram_227 (
    .input_bus(out_36), .vertical_wire(in_18), .horizontal_wire(in_22), .enabler(enabler), .set(set),
    .output_bus(out_36));
  registro_RAM registro_ram_228 (
    .input_bus(out_36), .vertical_wire(in_18), .horizontal_wire(in_23), .enabler(enabler), .set(set),
    .output_bus(out_36));
  registro_RAM registro_ram_229 (
    .input_bus(out_36), .vertical_wire(in_18), .horizontal_wire(in_24), .enabler(enabler), .set(set),
    .output_bus(out_36));
  registro_RAM registro_ram_230 (
    .input_bus(out_36), .vertical_wire(in_18), .horizontal_wire(in_25), .enabler(enabler), .set(set),
    .output_bus(out_36));
  registro_RAM registro_ram_231 (
    .input_bus(out_36), .vertical_wire(in_18), .horizontal_wire(in_26), .enabler(enabler), .set(set),
    .output_bus(out_36));
  registro_RAM registro_ram_232 (
    .input_bus(out_36), .vertical_wire(in_18), .horizontal_wire(in_27), .enabler(enabler), .set(set),
    .output_bus(out_36));
  registro_RAM registro_ram_233 (
    .input_bus(out_36), .vertical_wire(in_18), .horizontal_wire(in_28), .enabler(enabler), .set(set),
    .output_bus(out_36));
  registro_RAM registro_ram_234 (
    .input_bus(out_36), .vertical_wire(in_18), .horizontal_wire(in_29), .enabler(enabler), .set(set),
    .output_bus(out_36));
  registro_RAM registro_ram_235 (
    .input_bus(out_36), .vertical_wire(in_18), .horizontal_wire(in_30), .enabler(enabler), .set(set),
    .output_bus(out_36));
  registro_RAM registro_ram_236 (
    .input_bus(out_36), .vertical_wire(in_18), .horizontal_wire(in_31), .enabler(enabler), .set(set),
    .output_bus(out_36));
  registro_RAM registro_ram_237 (
    .input_bus(out_36), .vertical_wire(in_18), .horizontal_wire(in_32), .enabler(enabler), .set(set),
    .output_bus(out_36));
  registro_RAM registro_ram_238 (
    .input_bus(out_36), .vertical_wire(in_18), .horizontal_wire(in_33), .enabler(enabler), .set(set),
    .output_bus(out_36));
  registro_RAM registro_ram_239 (
    .input_bus(out_36), .vertical_wire(in_18), .horizontal_wire(in_34), .enabler(enabler), .set(set),
    .output_bus(out_36));
  registro_RAM registro_ram_240 (
    .input_bus(out_36), .vertical_wire(in_18), .horizontal_wire(undriven), .enabler(enabler), .set(set),
    .output_bus(out_36));
  registro_RAM registro_ram_241 (
    .input_bus(out_36), .vertical_wire(in_19), .horizontal_wire(in_20), .enabler(enabler), .set(set),
    .output_bus(out_36));
  registro_RAM registro_ram_242 (
    .input_bus(out_36), .vertical_wire(in_19), .horizontal_wire(in_21), .enabler(enabler), .set(set),
    .output_bus(out_36));
  registro_RAM registro_ram_243 (
    .input_bus(out_36), .vertical_wire(in_19), .horizontal_wire(in_22), .enabler(enabler), .set(set),
    .output_bus(out_36));
  registro_RAM registro_ram_244 (
    .input_bus(out_36), .vertical_wire(in_19), .horizontal_wire(in_23), .enabler(enabler), .set(set),
    .output_bus(out_36));
  registro_RAM registro_ram_245 (
    .input_bus(out_36), .vertical_wire(in_19), .horizontal_wire(in_24), .enabler(enabler), .set(set),
    .output_bus(out_36));
  registro_RAM registro_ram_246 (
    .input_bus(out_36), .vertical_wire(in_19), .horizontal_wire(in_25), .enabler(enabler), .set(set),
    .output_bus(out_36));
  registro_RAM registro_ram_247 (
    .input_bus(out_36), .vertical_wire(in_19), .horizontal_wire(in_26), .enabler(enabler), .set(set),
    .output_bus(out_36));
  registro_RAM registro_ram_248 (
    .input_bus(out_36), .vertical_wire(in_19), .horizontal_wire(in_27), .enabler(enabler), .set(set),
    .output_bus(out_36));
  registro_RAM registro_ram_249 (
    .input_bus(out_36), .vertical_wire(in_19), .horizontal_wire(in_28), .enabler(enabler), .set(set),
    .output_bus(out_36));
  registro_RAM registro_ram_250 (
    .input_bus(out_36), .vertical_wire(in_19), .horizontal_wire(in_29), .enabler(enabler), .set(set),
    .output_bus(out_36));
  registro_RAM registro_ram_251 (
    .input_bus(out_36), .vertical_wire(in_19), .horizontal_wire(in_30), .enabler(enabler), .set(set),
    .output_bus(out_36));
  registro_RAM registro_ram_252 (
    .input_bus(out_36), .vertical_wire(in_19), .horizontal_wire(in_31), .enabler(enabler), .set(set),
    .output_bus(out_36));
  registro_RAM registro_ram_253 (
    .input_bus(out_36), .vertical_wire(in_19), .horizontal_wire(in_32), .enabler(enabler), .set(set),
    .output_bus(out_36));
  registro_RAM registro_ram_254 (
    .input_bus(out_36), .vertical_wire(in_19), .horizontal_wire(in_33), .enabler(enabler), .set(set),
    .output_bus(out_36));
  registro_RAM registro_ram_255 (
    .input_bus(out_36), .vertical_wire(in_19), .horizontal_wire(in_34), .enabler(enabler), .set(set),
    .output_bus(out_36));
  registro_RAM registro_ram_256 (
    .input_bus(out_36), .vertical_wire(in_19), .horizontal_wire(undriven), .enabler(enabler), .set(set),
    .output_bus(out_36));
endmodule

module registro_RAM (
  input  [7:0] input_bus,
  input  enabler,
  input  vertical_wire,
  input  set,
  input  horizontal_wire,
  output [7:0] output_bus
);

  wire and_nand_small_1_out_3, and_nand_small_2_out_3, and_nand_small_3_out_3;

  register_nand_conbus register_nand_conbus_1 (
    .input_data(input_bus), .set(and_nand_small_1_out_3), .enable(and_nand_small_2_out_3),
    .output_data(output_bus));
  and_nand_small and_nand_small_1 (.in_1(and_nand_small_3_out_3), .in_2(set), .out_3(and_nand_small_1_out_3));
  and_nand_small and_nand_small_2 (.in_1(and_nand_small_3_out_3), .in_2(enabler), .out_3(and_nand_small_2_out_3));
  and_nand_small and_nand_small_3 (.in_1(vertical_wire), .in_2(horizontal_wire), .out_3(and_nand_small_3_out_3));
endmodule

module register_visor (
  input  [7:0] input_data,
  input  set,
  input  enable,
  output [7:0] output_data
);

  wire [7:0] mem_byte_1_out_10;

  mem_byte mem_byte_1 (
    .set(set), .in_2(input_data[1]), .in_3(input_data[2]), .in_4(input_data[3]), .in_5(input_data[4]),
    .in_6(input_data[5]), .in_7(input_data[6]), .in_8(input_data[7]), .in_1(input_data[0]),
    .out_11(mem_byte_1_out_10[1]), .out_12(mem_byte_1_out_10[2]), .out_13(mem_byte_1_out_10[3]),
    .out_14(mem_byte_1_out_10[4]), .out_15(mem_byte_1_out_10[5]), .out_16(mem_byte_1_out_10[6]),
    .out_17(mem_byte_1_out_10[7]), .out_10(mem_byte_1_out_10[0]));
  enabler_8bits enabler_8bits_1 (
    .in_2(mem_byte_1_out_10[1]), .in_3(mem_byte_1_out_10[2]), .in_4(mem_byte_1_out_10[3]),
    .in_5(mem_byte_1_out_10[4]), .in_6(mem_byte_1_out_10[5]), .in_7(mem_byte_1_out_10[6]),
    .in_8(mem_byte_1_out_10[7]), .in_1(mem_byte_1_out_10[0]), .in_9(enable), .out_11(output_data[1]),
    .out_12(output_data[2]), .out_13(output_data[3]), .out_14(output_data[4]), .out_15(output_data[5]),
    .out_16(output_data[6]), .out_17(output_data[7]), .out_10(output_data[0]));
  Hex_Digit_Display hex_digit_display_1 (.value(mem_byte_1_out_10[3:0]));  // open: dp
  Hex_Digit_Display hex_digit_display_2 (.value(mem_byte_1_out_10[7:4]));  // open: dp
endmodule

module register_nand_conbus (
  input  [7:0] input_data,
  input  set,
  input  enable,
  output [7:0] output_data
);

  wire mem_byte_1_out_10, mem_byte_1_out_11, mem_byte_1_out_12, mem_byte_1_out_13, mem_byte_1_out_14,
       mem_byte_1_out_15, mem_byte_1_out_16, mem_byte_1_out_17;

  mem_byte mem_byte_1 (
    .set(set), .in_2(input_data[1]), .in_3(input_data[2]), .in_4(input_data[3]), .in_5(input_data[4]),
    .in_6(input_data[5]), .in_7(input_data[6]), .in_8(input_data[7]), .in_1(input_data[0]),
    .out_11(mem_byte_1_out_11), .out_12(mem_byte_1_out_12), .out_13(mem_byte_1_out_13),
    .out_14(mem_byte_1_out_14), .out_15(mem_byte_1_out_15), .out_16(mem_byte_1_out_16),
    .out_17(mem_byte_1_out_17), .out_10(mem_byte_1_out_10));
  enabler_8bits enabler_8bits_1 (
    .in_2(mem_byte_1_out_11), .in_3(mem_byte_1_out_12), .in_4(mem_byte_1_out_13), .in_5(mem_byte_1_out_14),
    .in_6(mem_byte_1_out_15), .in_7(mem_byte_1_out_16), .in_8(mem_byte_1_out_17), .in_1(mem_byte_1_out_10),
    .in_9(enable), .out_11(output_data[1]), .out_12(output_data[2]), .out_13(output_data[3]),
    .out_14(output_data[4]), .out_15(output_data[5]), .out_16(output_data[6]), .out_17(output_data[7]),
    .out_10(output_data[0]));
endmodule

module enabler_8bits (
  input  in_1,
  input  in_2,
  input  in_3,
  input  in_4,
  input  in_5,
  input  in_6,
  input  in_7,
  input  in_8,
  input  in_9,
  output out_10,
  output out_11,
  output out_12,
  output out_13,
  output out_14,
  output out_15,
  output out_16,
  output out_17
);

  buffer_alta_impedancia buffer_alta_impedancia_1 ();  // open: enable, data, out_3
  assign out_10 = in_9 ? in_1 : 1'bz;  // Controlled_Buffer controlled_buffer_1
  assign out_11 = in_9 ? in_2 : 1'bz;  // Controlled_Buffer controlled_buffer_2
  assign out_12 = in_9 ? in_3 : 1'bz;  // Controlled_Buffer controlled_buffer_3
  assign out_13 = in_9 ? in_4 : 1'bz;  // Controlled_Buffer controlled_buffer_4
  assign out_14 = in_9 ? in_5 : 1'bz;  // Controlled_Buffer controlled_buffer_5
  assign out_15 = in_9 ? in_6 : 1'bz;  // Controlled_Buffer controlled_buffer_6
  assign out_16 = in_9 ? in_7 : 1'bz;  // Controlled_Buffer controlled_buffer_7
  assign out_17 = in_9 ? in_8 : 1'bz;  // Controlled_Buffer controlled_buffer_8

  // Notes on the sheet:
  //   input
  //   El buffer controlado puede sustituirse por buffer_alta_impedancia
  //   enabler
  //   output
endmodule

module mem_byte (
  input  in_1,
  input  in_2,
  input  in_3,
  input  in_4,
  input  in_5,
  input  in_6,
  input  in_7,
  input  in_8,
  input  set,
  output out_10,
  output out_11,
  output out_12,
  output out_13,
  output out_14,
  output out_15,
  output out_16,
  output out_17
);

  mem_bit mem_bit_1 (.set(set), .data(in_1), .out_3(out_10));
  mem_bit mem_bit_2 (.set(set), .data(in_2), .out_3(out_11));
  mem_bit mem_bit_3 (.set(set), .data(in_3), .out_3(out_12));
  mem_bit mem_bit_4 (.set(set), .data(in_4), .out_3(out_13));
  mem_bit mem_bit_5 (.set(set), .data(in_5), .out_3(out_14));
  mem_bit mem_bit_6 (.set(set), .data(in_6), .out_3(out_15));
  mem_bit mem_bit_7 (.set(set), .data(in_7), .out_3(out_16));
  mem_bit mem_bit_8 (.set(set), .data(in_8), .out_3(out_17));

  // Notes on the sheet:
  //   input
  //   output
endmodule

module mem_bit (
  input  data,
  input  set,
  output out_3
);

  wire nand_1_out, nand_2_out, nand_4_out, or_1_out, por_1_out;

  POR #(.PorHighDuration(1)) por_1 (.out(por_1_out));
  or or_1 (or_1_out, set, por_1_out);
  nand nand_1 (nand_1_out, data, or_1_out);
  nand nand_2 (nand_2_out, nand_1_out, or_1_out);
  nand nand_3 (out_3, nand_1_out, nand_4_out);
  nand nand_4 (nand_4_out, out_3, nand_2_out);

  // Notes on the sheet:
  //   set: pull=up
  //   Los NAND y OR ahora son built-in de logisim por rendimiento. Pero se puede poner nand_transistors con fin educativo
endmodule

module buffer_alta_impedancia (
  input  data,
  input  enable,
  output out_3
);

  wire nand_transistors_1_out_3, nor_nand_1_out_3, not_nand_1_out_2;

  not_nand not_nand_1 (.in_1(enable), .out_2(not_nand_1_out_2));
  nand_transistors nand_transistors_1 (.in_1(data), .in_2(enable), .out_3(nand_transistors_1_out_3));
  Transistor transistor_1 (.in(1'b1), .out(out_3), .gate(nand_transistors_1_out_3));
  nor_nand nor_nand_1 (.in_1(not_nand_1_out_2), .in_2(data), .out_3(nor_nand_1_out_3));
  Transistor #(.\type ("n")) transistor_2 (.in(1'b0), .out(out_3), .gate(nor_nand_1_out_3));
endmodule

module nor_nand (
  input  in_1,
  input  in_2,
  output out_3
);

  wire or_nand_1_out_3;

  or_nand or_nand_1 (.in_1(in_1), .in_2(in_2), .out_3(or_nand_1_out_3));
  not_nand not_nand_1 (.in_1(or_nand_1_out_3), .out_2(out_3));
endmodule

module or_nand (
  input  in_1,
  input  in_2,
  output out_3
);

  wire not_nand_1_out_2, not_nand_2_out_2;

  not_nand not_nand_1 (.in_1(in_1), .out_2(not_nand_1_out_2));
  not_nand not_nand_2 (.in_1(in_2), .out_2(not_nand_2_out_2));
  nand_transistors nand_transistors_1 (.in_1(not_nand_1_out_2), .in_2(not_nand_2_out_2), .out_3(out_3));
endmodule

module and_nand_small (
  input  in_1,
  input  in_2,
  output out_3
);

  and_nand and_nand_1 (.in_1(in_1), .in_2(in_2), .out_3(out_3));
endmodule

module and_nand (
  input  in_1,
  input  in_2,
  output out_3
);

  wire nand_transistors_1_out_3;

  nand_transistors nand_transistors_1 (.in_1(in_1), .in_2(in_2), .out_3(nand_transistors_1_out_3));
  not_nand not_nand_1 (.in_1(nand_transistors_1_out_3), .out_2(out_3));
endmodule

module not_nand (
  input  in_1,
  output out_2
);

  nand_transistors nand_transistors_1 (.in_1(in_1), .in_2(in_1), .out_3(out_2));
endmodule

module nand_transistors (
  input  in_1,
  input  in_2,
  output out_3
);

  wire transistor_1_out;

  Transistor #(.\type ("n")) transistor_1 (.in(1'b0), .out(transistor_1_out), .gate(in_1));
  Transistor #(.\type ("n")) transistor_2 (.in(transistor_1_out), .out(out_3), .gate(in_2));
  Pull_Resistor #(.pull(1)) pull_resistor_1 (.node(out_3));

  // Notes on the sheet:
  //   in_2: initial=0x1
endmodule

module nand_4_transistors (
  input  in_1,
  input  in_2,
  output out_3
);

  wire transistor_4_out;

  Transistor transistor_1 (.in(1'b1), .out(out_3), .gate(in_1));
  Transistor transistor_2 (.in(1'b1), .out(out_3), .gate(in_2));
  Transistor #(.\type ("n")) transistor_3 (.in(transistor_4_out), .out(out_3), .gate(in_1));
  Transistor #(.\type ("n")) transistor_4 (.in(1'b0), .out(transistor_4_out), .gate(in_2));
endmodule
